// Logisim project main.circ as structural Verilog: 30 circuits, main circuit CPU
module DCD (
  input  RESET,
  input  MICRO_RESET,
  input  [5:0] SELECTOR,
  input  CLK,
  input  WE,
  input  IMM_EXT_IN,
  input  EXEC,
  output O0,
  output O1,
  output O2,
  output O3,
  output O4,
  output O5,
  output O6,
  output O7,
  output [5:0] DCD_OUT,
  output [7:0] PC_OUT,
  output O8,
  output IMM_EXT_OUT,
  output O9,
  output O10,
  output O11,
  output O12,
  output O13,
  output O14,
  output O15,
  output O16,
  output O17,
  output O18,
  output O19,
  output O20,
  output O21,
  output O22,
  output O23,
  output O24,
  output O25,
  output O26,
  output O27,
  output O28,
  output O29,
  output O30,
  output O31,
  output O32,
  output O33,
  output O34,
  output O35,
  output O36,
  output O37,
  output O38,
  output O39,
  output O40,
  output O41,
  output O42,
  output O43,
  output O44,
  output O45,
  output O46,
  output O47,
  output O48,
  output O49,
  output O50,
  output O51,
  output O52,
  output O53,
  output O54,
  output O55,
  output O56,
  output O57,
  output O58,
  output O59,
  output O60,
  output O61,
  output O62,
  output O63
);

  wire and_1_out, decoder_1_out0, decoder_1_out1, decoder_1_out2, decoder_1_out3, decoder_2_out0,
       decoder_2_out1, decoder_2_out2, decoder_2_out3, decoder_2_out4, decoder_2_out5, decoder_2_out6,
       decoder_2_out7, decoder_2_out8, decoder_2_out9, decoder_2_out10, decoder_2_out11, decoder_2_out12,
       decoder_2_out13, decoder_2_out14, decoder_2_out15, decoder_3_out0, decoder_3_out1, decoder_3_out2,
       decoder_3_out3, decoder_3_out4, decoder_3_out5, decoder_3_out6, decoder_3_out7, decoder_3_out8,
       decoder_3_out9, decoder_3_out10, decoder_3_out11, decoder_3_out12, decoder_3_out13, decoder_3_out14,
       decoder_3_out15, decoder_4_out0, decoder_4_out1, decoder_4_out2, decoder_4_out3, decoder_4_out4,
       decoder_4_out5, decoder_4_out6, decoder_4_out7, decoder_4_out8, decoder_4_out9, decoder_4_out10,
       decoder_4_out11, decoder_4_out12, decoder_4_out13, decoder_4_out14, decoder_4_out15, decoder_5_out0,
       decoder_5_out1, decoder_5_out2, decoder_5_out3, decoder_5_out4, decoder_5_out5, decoder_5_out6,
       decoder_5_out7, decoder_5_out8, decoder_5_out9, decoder_5_out10, decoder_5_out11, decoder_5_out12,
       decoder_5_out13, decoder_5_out14, decoder_5_out15, not_1_out, or_1_out, register_3_q, register_4_q,
       register_5_q, register_6_q, register_7_q, register_8_q, register_9_q, register_10_q, register_11_q,
       register_12_q, register_13_q, register_14_q, register_15_q, register_16_q, register_17_q,
       register_18_q, register_19_q, register_20_q, register_21_q, register_22_q, register_23_q,
       register_24_q, register_25_q, register_26_q, register_27_q, register_28_q, register_29_q,
       register_30_q, register_31_q, register_32_q, register_33_q, register_34_q, register_35_q,
       register_36_q, register_37_q, register_38_q, register_39_q, register_40_q, register_41_q,
       register_42_q, register_43_q, register_44_q, register_45_q, register_46_q, register_47_q,
       register_48_q, register_49_q, register_50_q, register_51_q, register_52_q, register_53_q,
       register_54_q, register_55_q, register_56_q, register_57_q, register_58_q, register_59_q,
       register_60_q, register_61_q, register_62_q, register_63_q, register_64_q, register_65_q,
       register_66_q;
  wire [7:0] bit_extender_1_out, shifter_1_out, subtractor_1_out;

  D_Flip_Flop d_ff_1 (.D(IMM_EXT_IN), .clk(and_1_out), .Q(IMM_EXT_OUT), .reset(or_1_out));  // open: Qn, preset
  and and_1 (and_1_out, CLK, WE);
  assign bit_extender_1_out = {{2{SELECTOR[5]}}, SELECTOR};  // Bit_Extender bit_extender_1
  Subtractor subtractor_1 (.a(bit_extender_1_out), .b(8'h1), .out(subtractor_1_out));  // open: bin, bout
  Register register_1 (.D(shifter_1_out), .en(WE), .clk(WE), .Q(PC_OUT), .clr(RESET));
  Shifter shifter_1 (.in(subtractor_1_out), .\dist (3'b010), .out(shifter_1_out));
  Decoder #(.select(2)) decoder_1 (
    .out0(decoder_1_out0), .out1(decoder_1_out1), .out2(decoder_1_out2), .out3(decoder_1_out3),
    .sel(SELECTOR[5:4]), .en(WE));
  Register #(.width(6)) register_2 (.D(SELECTOR), .en(WE), .clk(WE), .Q(DCD_OUT), .clr(or_1_out));
  Decoder #(.select(4)) decoder_2 (
    .out0(decoder_2_out0), .out1(decoder_2_out1), .out2(decoder_2_out2), .out3(decoder_2_out3),
    .out4(decoder_2_out4), .out5(decoder_2_out5), .out6(decoder_2_out6), .out7(decoder_2_out7),
    .out8(decoder_2_out8), .out9(decoder_2_out9), .out10(decoder_2_out10), .out11(decoder_2_out11),
    .out12(decoder_2_out12), .out13(decoder_2_out13), .out14(decoder_2_out14), .out15(decoder_2_out15),
    .sel(SELECTOR[3:0]), .en(decoder_1_out0));
  Decoder #(.select(4)) decoder_3 (
    .out0(decoder_3_out0), .out1(decoder_3_out1), .out2(decoder_3_out2), .out3(decoder_3_out3),
    .out4(decoder_3_out4), .out5(decoder_3_out5), .out6(decoder_3_out6), .out7(decoder_3_out7),
    .out8(decoder_3_out8), .out9(decoder_3_out9), .out10(decoder_3_out10), .out11(decoder_3_out11),
    .out12(decoder_3_out12), .out13(decoder_3_out13), .out14(decoder_3_out14), .out15(decoder_3_out15),
    .sel(SELECTOR[3:0]), .en(decoder_1_out1));
  Decoder #(.select(4)) decoder_4 (
    .out0(decoder_4_out0), .out1(decoder_4_out1), .out2(decoder_4_out2), .out3(decoder_4_out3),
    .out4(decoder_4_out4), .out5(decoder_4_out5), .out6(decoder_4_out6), .out7(decoder_4_out7),
    .out8(decoder_4_out8), .out9(decoder_4_out9), .out10(decoder_4_out10), .out11(decoder_4_out11),
    .out12(decoder_4_out12), .out13(decoder_4_out13), .out14(decoder_4_out14), .out15(decoder_4_out15),
    .sel(SELECTOR[3:0]), .en(decoder_1_out2));
  Decoder #(.select(4)) decoder_5 (
    .out0(decoder_5_out0), .out1(decoder_5_out1), .out2(decoder_5_out2), .out3(decoder_5_out3),
    .out4(decoder_5_out4), .out5(decoder_5_out5), .out6(decoder_5_out6), .out7(decoder_5_out7),
    .out8(decoder_5_out8), .out9(decoder_5_out9), .out10(decoder_5_out10), .out11(decoder_5_out11),
    .out12(decoder_5_out12), .out13(decoder_5_out13), .out14(decoder_5_out14), .out15(decoder_5_out15),
    .en(decoder_1_out3));  // open: sel
  Register #(.width(1)) register_3 (.D(not_1_out), .en(not_1_out), .clk(not_1_out), .Q(register_3_q), .clr(or_1_out));
  not not_1 (not_1_out, decoder_2_out0);
  Register #(.width(1)) register_4 (
    .D(decoder_2_out1), .en(decoder_2_out1), .clk(decoder_2_out1), .Q(register_4_q), .clr(or_1_out));
  Register #(.width(1)) register_5 (
    .D(decoder_2_out2), .en(decoder_2_out2), .clk(decoder_2_out2), .Q(register_5_q), .clr(or_1_out));
  Register #(.width(1)) register_6 (
    .D(decoder_2_out3), .en(decoder_2_out3), .clk(decoder_2_out3), .Q(register_6_q), .clr(or_1_out));
  Register #(.width(1)) register_7 (
    .D(decoder_2_out4), .en(decoder_2_out4), .clk(decoder_2_out4), .Q(register_7_q), .clr(or_1_out));
  Register #(.width(1)) register_8 (
    .D(decoder_2_out5), .en(decoder_2_out5), .clk(decoder_2_out5), .Q(register_8_q), .clr(or_1_out));
  Register #(.width(1)) register_9 (
    .D(decoder_2_out6), .en(decoder_2_out6), .clk(decoder_2_out6), .Q(register_9_q), .clr(or_1_out));
  Register #(.width(1)) register_10 (
    .D(decoder_2_out7), .en(decoder_2_out7), .clk(decoder_2_out7), .Q(register_10_q), .clr(or_1_out));
  Register #(.width(1)) register_11 (
    .D(decoder_2_out8), .en(decoder_2_out8), .clk(decoder_2_out8), .Q(register_11_q), .clr(or_1_out));
  Register #(.width(1)) register_12 (
    .D(decoder_2_out9), .en(decoder_2_out9), .clk(decoder_2_out9), .Q(register_12_q), .clr(or_1_out));
  Register #(.width(1)) register_13 (
    .D(decoder_2_out10), .en(decoder_2_out10), .clk(decoder_2_out10), .Q(register_13_q), .clr(or_1_out));
  Register #(.width(1)) register_14 (
    .D(decoder_2_out11), .en(decoder_2_out11), .clk(decoder_2_out11), .Q(register_14_q), .clr(or_1_out));
  Register #(.width(1)) register_15 (
    .D(decoder_2_out12), .en(decoder_2_out12), .clk(decoder_2_out12), .Q(register_15_q), .clr(or_1_out));
  Register #(.width(1)) register_16 (
    .D(decoder_2_out13), .en(decoder_2_out13), .clk(decoder_2_out13), .Q(register_16_q), .clr(or_1_out));
  Register #(.width(1)) register_17 (
    .D(decoder_2_out14), .en(decoder_2_out14), .clk(decoder_2_out14), .Q(register_17_q), .clr(or_1_out));
  Register #(.width(1)) register_18 (
    .D(decoder_2_out15), .en(decoder_2_out15), .clk(decoder_2_out15), .Q(register_18_q), .clr(or_1_out));
  Register #(.width(1)) register_19 (
    .D(decoder_3_out0), .en(decoder_3_out0), .clk(decoder_3_out0), .Q(register_19_q), .clr(or_1_out));
  Register #(.width(1)) register_20 (
    .D(decoder_3_out1), .en(decoder_3_out1), .clk(decoder_3_out1), .Q(register_20_q), .clr(or_1_out));
  Register #(.width(1)) register_21 (
    .D(decoder_3_out2), .en(decoder_3_out2), .clk(decoder_3_out2), .Q(register_21_q), .clr(or_1_out));
  Register #(.width(1)) register_22 (
    .D(decoder_3_out3), .en(decoder_3_out3), .clk(decoder_3_out3), .Q(register_22_q), .clr(or_1_out));
  Register #(.width(1)) register_23 (
    .D(decoder_3_out4), .en(decoder_3_out4), .clk(decoder_3_out4), .Q(register_23_q), .clr(or_1_out));
  Register #(.width(1)) register_24 (
    .D(decoder_3_out5), .en(decoder_3_out5), .clk(decoder_3_out5), .Q(register_24_q), .clr(or_1_out));
  Register #(.width(1)) register_25 (
    .D(decoder_3_out6), .en(decoder_3_out6), .clk(decoder_3_out6), .Q(register_25_q), .clr(or_1_out));
  Register #(.width(1)) register_26 (
    .D(decoder_3_out7), .en(decoder_3_out7), .clk(decoder_3_out7), .Q(register_26_q), .clr(or_1_out));
  Register #(.width(1)) register_27 (
    .D(decoder_3_out8), .en(decoder_3_out8), .clk(decoder_3_out8), .Q(register_27_q), .clr(or_1_out));
  Register #(.width(1)) register_28 (
    .D(decoder_3_out9), .en(decoder_3_out9), .clk(decoder_3_out9), .Q(register_28_q), .clr(or_1_out));
  Register #(.width(1)) register_29 (
    .D(decoder_3_out10), .en(decoder_3_out10), .clk(decoder_3_out10), .Q(register_29_q), .clr(or_1_out));
  Register #(.width(1)) register_30 (
    .D(decoder_3_out11), .en(decoder_3_out11), .clk(decoder_3_out11), .Q(register_30_q), .clr(or_1_out));
  Register #(.width(1)) register_31 (
    .D(decoder_3_out12), .en(decoder_3_out12), .clk(decoder_3_out12), .Q(register_31_q), .clr(or_1_out));
  Register #(.width(1)) register_32 (
    .D(decoder_3_out13), .en(decoder_3_out13), .clk(decoder_3_out13), .Q(register_32_q), .clr(or_1_out));
  Register #(.width(1)) register_33 (
    .D(decoder_3_out14), .en(decoder_3_out14), .clk(decoder_3_out14), .Q(register_33_q), .clr(or_1_out));
  Register #(.width(1)) register_34 (
    .D(decoder_3_out15), .en(decoder_3_out15), .clk(decoder_3_out15), .Q(register_34_q), .clr(or_1_out));
  Register #(.width(1)) register_35 (
    .D(decoder_4_out0), .en(decoder_4_out0), .clk(decoder_4_out0), .Q(register_35_q), .clr(or_1_out));
  Register #(.width(1)) register_36 (
    .D(decoder_4_out1), .en(decoder_4_out1), .clk(decoder_4_out1), .Q(register_36_q), .clr(or_1_out));
  Register #(.width(1)) register_37 (
    .D(decoder_4_out2), .en(decoder_4_out2), .clk(decoder_4_out2), .Q(register_37_q), .clr(or_1_out));
  Register #(.width(1)) register_38 (
    .D(decoder_4_out3), .en(decoder_4_out3), .clk(decoder_4_out3), .Q(register_38_q), .clr(or_1_out));
  Register #(.width(1)) register_39 (
    .D(decoder_4_out4), .en(decoder_4_out4), .clk(decoder_4_out4), .Q(register_39_q), .clr(or_1_out));
  Register #(.width(1)) register_40 (
    .D(decoder_4_out5), .en(decoder_4_out5), .clk(decoder_4_out5), .Q(register_40_q), .clr(or_1_out));
  Register #(.width(1)) register_41 (
    .D(decoder_4_out6), .en(decoder_4_out6), .clk(decoder_4_out6), .Q(register_41_q), .clr(or_1_out));
  Register #(.width(1)) register_42 (
    .D(decoder_4_out7), .en(decoder_4_out7), .clk(decoder_4_out7), .Q(register_42_q), .clr(or_1_out));
  Register #(.width(1)) register_43 (
    .D(decoder_4_out8), .en(decoder_4_out8), .clk(decoder_4_out8), .Q(register_43_q), .clr(or_1_out));
  Register #(.width(1)) register_44 (
    .D(decoder_4_out9), .en(decoder_4_out9), .clk(decoder_4_out9), .Q(register_44_q), .clr(or_1_out));
  Register #(.width(1)) register_45 (
    .D(decoder_4_out10), .en(decoder_4_out10), .clk(decoder_4_out10), .Q(register_45_q), .clr(or_1_out));
  Register #(.width(1)) register_46 (
    .D(decoder_4_out11), .en(decoder_4_out11), .clk(decoder_4_out11), .Q(register_46_q), .clr(or_1_out));
  Register #(.width(1)) register_47 (
    .D(decoder_4_out12), .en(decoder_4_out12), .clk(decoder_4_out12), .Q(register_47_q), .clr(or_1_out));
  Register #(.width(1)) register_48 (
    .D(decoder_4_out13), .en(decoder_4_out13), .clk(decoder_4_out13), .Q(register_48_q), .clr(or_1_out));
  Register #(.width(1)) register_49 (
    .D(decoder_4_out14), .en(decoder_4_out14), .clk(decoder_4_out14), .Q(register_49_q), .clr(or_1_out));
  Register #(.width(1)) register_50 (
    .D(decoder_4_out15), .en(decoder_4_out15), .clk(decoder_4_out15), .Q(register_50_q), .clr(or_1_out));
  Register #(.width(1)) register_51 (
    .D(decoder_5_out0), .en(decoder_5_out0), .clk(decoder_5_out0), .Q(register_51_q), .clr(or_1_out));
  Register #(.width(1)) register_52 (
    .D(decoder_5_out1), .en(decoder_5_out1), .clk(decoder_5_out1), .Q(register_52_q), .clr(or_1_out));
  Register #(.width(1)) register_53 (
    .D(decoder_5_out2), .en(decoder_5_out2), .clk(decoder_5_out2), .Q(register_53_q), .clr(or_1_out));
  Register #(.width(1)) register_54 (
    .D(decoder_5_out3), .en(decoder_5_out3), .clk(decoder_5_out3), .Q(register_54_q), .clr(or_1_out));
  Register #(.width(1)) register_55 (
    .D(decoder_5_out4), .en(decoder_5_out4), .clk(decoder_5_out4), .Q(register_55_q), .clr(or_1_out));
  Register #(.width(1)) register_56 (
    .D(decoder_5_out5), .en(decoder_5_out5), .clk(decoder_5_out5), .Q(register_56_q), .clr(or_1_out));
  Register #(.width(1)) register_57 (
    .D(decoder_5_out6), .en(decoder_5_out6), .clk(decoder_5_out6), .Q(register_57_q), .clr(or_1_out));
  Register #(.width(1)) register_58 (
    .D(decoder_5_out7), .en(decoder_5_out7), .clk(decoder_5_out7), .Q(register_58_q), .clr(or_1_out));
  Register #(.width(1)) register_59 (
    .D(decoder_5_out8), .en(decoder_5_out8), .clk(decoder_5_out8), .Q(register_59_q), .clr(or_1_out));
  Register #(.width(1)) register_60 (
    .D(decoder_5_out9), .en(decoder_5_out9), .clk(decoder_5_out9), .Q(register_60_q), .clr(or_1_out));
  Register #(.width(1)) register_61 (
    .D(decoder_5_out10), .en(decoder_5_out10), .clk(decoder_5_out10), .Q(register_61_q), .clr(or_1_out));
  Register #(.width(1)) register_62 (
    .D(decoder_5_out11), .en(decoder_5_out11), .clk(decoder_5_out11), .Q(register_62_q), .clr(or_1_out));
  Register #(.width(1)) register_63 (
    .D(decoder_5_out12), .en(decoder_5_out12), .clk(decoder_5_out12), .Q(register_63_q), .clr(or_1_out));
  Register #(.width(1)) register_64 (
    .D(decoder_5_out13), .en(decoder_5_out13), .clk(decoder_5_out13), .Q(register_64_q), .clr(or_1_out));
  Register #(.width(1)) register_65 (
    .D(decoder_5_out14), .en(decoder_5_out14), .clk(decoder_5_out14), .Q(register_65_q), .clr(or_1_out));
  Register #(.width(1)) register_66 (
    .D(decoder_5_out15), .en(decoder_5_out15), .clk(decoder_5_out15), .Q(register_66_q), .clr(or_1_out));
  assign O0 = EXEC ? register_3_q : 1'bz;  // Controlled_Buffer controlled_buffer_1
  assign O1 = EXEC ? register_4_q : 1'bz;  // Controlled_Buffer controlled_buffer_2
  assign O2 = EXEC ? register_5_q : 1'bz;  // Controlled_Buffer controlled_buffer_3
  assign O3 = EXEC ? register_6_q : 1'bz;  // Controlled_Buffer controlled_buffer_4
  assign O4 = EXEC ? register_7_q : 1'bz;  // Controlled_Buffer controlled_buffer_5
  assign O5 = EXEC ? register_8_q : 1'bz;  // Controlled_Buffer controlled_buffer_6
  assign O6 = EXEC ? register_9_q : 1'bz;  // Controlled_Buffer controlled_buffer_7
  assign O7 = EXEC ? register_10_q : 1'bz;  // Controlled_Buffer controlled_buffer_8
  assign O8 = EXEC ? register_11_q : 1'bz;  // Controlled_Buffer controlled_buffer_9
  assign O9 = EXEC ? register_12_q : 1'bz;  // Controlled_Buffer controlled_buffer_10
  assign O10 = EXEC ? register_13_q : 1'bz;  // Controlled_Buffer controlled_buffer_11
  assign O11 = EXEC ? register_14_q : 1'bz;  // Controlled_Buffer controlled_buffer_12
  assign O12 = EXEC ? register_15_q : 1'bz;  // Controlled_Buffer controlled_buffer_13
  assign O13 = EXEC ? register_16_q : 1'bz;  // Controlled_Buffer controlled_buffer_14
  assign O14 = EXEC ? register_17_q : 1'bz;  // Controlled_Buffer controlled_buffer_15
  assign O15 = EXEC ? register_18_q : 1'bz;  // Controlled_Buffer controlled_buffer_16
  assign O16 = EXEC ? register_19_q : 1'bz;  // Controlled_Buffer controlled_buffer_17
  assign O17 = EXEC ? register_20_q : 1'bz;  // Controlled_Buffer controlled_buffer_18
  assign O18 = EXEC ? register_21_q : 1'bz;  // Controlled_Buffer controlled_buffer_19
  assign O19 = EXEC ? register_22_q : 1'bz;  // Controlled_Buffer controlled_buffer_20
  assign O20 = EXEC ? register_23_q : 1'bz;  // Controlled_Buffer controlled_buffer_21
  assign O21 = EXEC ? register_24_q : 1'bz;  // Controlled_Buffer controlled_buffer_22
  assign O22 = EXEC ? register_25_q : 1'bz;  // Controlled_Buffer controlled_buffer_23
  assign O23 = EXEC ? register_26_q : 1'bz;  // Controlled_Buffer controlled_buffer_24
  assign O24 = EXEC ? register_27_q : 1'bz;  // Controlled_Buffer controlled_buffer_25
  assign O25 = EXEC ? register_28_q : 1'bz;  // Controlled_Buffer controlled_buffer_26
  assign O26 = EXEC ? register_29_q : 1'bz;  // Controlled_Buffer controlled_buffer_27
  assign O27 = EXEC ? register_30_q : 1'bz;  // Controlled_Buffer controlled_buffer_28
  assign O28 = EXEC ? register_31_q : 1'bz;  // Controlled_Buffer controlled_buffer_29
  assign O29 = EXEC ? register_32_q : 1'bz;  // Controlled_Buffer controlled_buffer_30
  assign O30 = EXEC ? register_33_q : 1'bz;  // Controlled_Buffer controlled_buffer_31
  assign O31 = EXEC ? register_34_q : 1'bz;  // Controlled_Buffer controlled_buffer_32
  assign O32 = EXEC ? register_35_q : 1'bz;  // Controlled_Buffer controlled_buffer_33
  assign O33 = EXEC ? register_36_q : 1'bz;  // Controlled_Buffer controlled_buffer_34
  assign O34 = EXEC ? register_37_q : 1'bz;  // Controlled_Buffer controlled_buffer_35
  assign O35 = EXEC ? register_38_q : 1'bz;  // Controlled_Buffer controlled_buffer_36
  assign O36 = EXEC ? register_39_q : 1'bz;  // Controlled_Buffer controlled_buffer_37
  assign O37 = EXEC ? register_40_q : 1'bz;  // Controlled_Buffer controlled_buffer_38
  assign O38 = EXEC ? register_41_q : 1'bz;  // Controlled_Buffer controlled_buffer_39
  assign O39 = EXEC ? register_42_q : 1'bz;  // Controlled_Buffer controlled_buffer_40
  assign O40 = EXEC ? register_43_q : 1'bz;  // Controlled_Buffer controlled_buffer_41
  assign O41 = EXEC ? register_44_q : 1'bz;  // Controlled_Buffer controlled_buffer_42
  assign O42 = EXEC ? register_45_q : 1'bz;  // Controlled_Buffer controlled_buffer_43
  assign O43 = EXEC ? register_46_q : 1'bz;  // Controlled_Buffer controlled_buffer_44
  assign O44 = EXEC ? register_47_q : 1'bz;  // Controlled_Buffer controlled_buffer_45
  assign O45 = EXEC ? register_48_q : 1'bz;  // Controlled_Buffer controlled_buffer_46
  assign O46 = EXEC ? register_49_q : 1'bz;  // Controlled_Buffer controlled_buffer_47
  assign O47 = EXEC ? register_50_q : 1'bz;  // Controlled_Buffer controlled_buffer_48
  assign O48 = EXEC ? register_51_q : 1'bz;  // Controlled_Buffer controlled_buffer_49
  assign O49 = EXEC ? register_52_q : 1'bz;  // Controlled_Buffer controlled_buffer_50
  assign O50 = EXEC ? register_53_q : 1'bz;  // Controlled_Buffer controlled_buffer_51
  assign O51 = EXEC ? register_54_q : 1'bz;  // Controlled_Buffer controlled_buffer_52
  assign O52 = EXEC ? register_55_q : 1'bz;  // Controlled_Buffer controlled_buffer_53
  assign O53 = EXEC ? register_56_q : 1'bz;  // Controlled_Buffer controlled_buffer_54
  assign O54 = EXEC ? register_57_q : 1'bz;  // Controlled_Buffer controlled_buffer_55
  assign O55 = EXEC ? register_58_q : 1'bz;  // Controlled_Buffer controlled_buffer_56
  assign O56 = EXEC ? register_59_q : 1'bz;  // Controlled_Buffer controlled_buffer_57
  assign O57 = EXEC ? register_60_q : 1'bz;  // Controlled_Buffer controlled_buffer_58
  assign O58 = EXEC ? register_61_q : 1'bz;  // Controlled_Buffer controlled_buffer_59
  assign O59 = EXEC ? register_62_q : 1'bz;  // Controlled_Buffer controlled_buffer_60
  assign O60 = EXEC ? register_63_q : 1'bz;  // Controlled_Buffer controlled_buffer_61
  assign O61 = EXEC ? register_64_q : 1'bz;  // Controlled_Buffer controlled_buffer_62
  assign O62 = EXEC ? register_65_q : 1'bz;  // Controlled_Buffer controlled_buffer_63
  assign O63 = EXEC ? register_66_q : 1'bz;  // Controlled_Buffer controlled_buffer_64
  or or_1 (or_1_out, RESET, MICRO_RESET);
endmodule

module DCD_CTRL (
  input  I5,
  input  I4,
  input  l3,
  input  I2,
  input  I1,
  input  I0,
  output O0
);

  wire and_1_out, and_2_out, and_3_out, and_4_out, and_5_out, and_6_out, or_1_out, or_2_out, or_3_out,
       or_4_out;

  LED led_1 (.in(I5));
  LED led_2 (.in(I4));
  Pull_Resistor pull_resistor_1 (.node(I5));
  Pull_Resistor pull_resistor_2 (.node(I4));
  LED led_3 (.in(l3));
  LED led_4 (.in(I2));
  LED led_5 (.in(I1));
  LED led_6 (.in(I0));
  Pull_Resistor pull_resistor_3 (.node(l3));
  Pull_Resistor pull_resistor_4 (.node(I2));
  Pull_Resistor pull_resistor_5 (.node(I1));
  Pull_Resistor pull_resistor_6 (.node(I0));
  and and_1 (and_1_out, I0, 1'b1);
  and and_2 (and_2_out, I1, 1'b1);
  and and_3 (and_3_out, I2, 1'b1);
  and and_4 (and_4_out, l3, 1'b1);
  and and_5 (and_5_out, I4, 1'b1);
  and and_6 (and_6_out, I5, 1'b1);
  or or_1 (or_1_out, and_1_out, and_2_out);
  or or_2 (or_2_out, and_3_out, and_4_out);
  or or_3 (or_3_out, and_5_out, and_6_out);
  or or_4 (or_4_out, or_1_out, or_2_out);
  or or_5 (O0, or_4_out, or_3_out);
endmodule

module DCD_JMP (
  input  JZ,
  input  ZERO,
  input  JUMP,
  output J_OUT
);

  wire and_1_out;

  or or_1 (J_OUT, and_1_out, JUMP);
  and and_1 (and_1_out, JZ, ZERO);
endmodule

module UOP_DCD (
  input  CLK,
  input  MR,
  input  RESET,
  input  MODE_IN,
  input  EOI,
  input  [3:0] SEL,
  output MODE_OUT,
  output [3:0] UOP_ADDR,
  output [4:0] UOP_OUT
);

  wire and_1_out, controlled_buffer_1_out, decoder_1_out5, not_1_out, not_2_out, not_3_out, or_1_out,
       or_2_out, or_3_out, undriven;
  wire [3:0] sc_1_binary_out;

  or or_1 (or_1_out, MR, RESET);
  MHR mhr_1 (.MODE_IN(MODE_IN), .EOI(EOI), .CLK(CLK), .RESET(or_1_out), .MODE_OUT(MODE_OUT));
  not not_1 (not_1_out, CLK);
  and and_1 (and_1_out, or_1_out, not_1_out);
  or or_2 (or_2_out, undriven, and_1_out);
  not not_2 (not_2_out, CLK);
  assign controlled_buffer_1_out = MODE_OUT ? not_2_out : 1'bz;  // Controlled_Buffer controlled_buffer_1
  not not_3 (not_3_out, controlled_buffer_1_out);
  SC sc_1 (.RESET(or_3_out), .CLOCK(not_3_out), .BINARY_OUT(sc_1_binary_out));
  or or_3 (or_3_out, or_2_out, decoder_1_out5);
  Decoder #(.enable("false"), .select(4)) decoder_1 (
    .out0(UOP_OUT[4]), .out1(UOP_OUT[3]), .out2(UOP_OUT[2]), .out3(UOP_OUT[1]), .out4(UOP_OUT[0]),
    .out5(decoder_1_out5), .sel(sc_1_binary_out));  // open: out6, out7, out8, out9, out10, out11, out12, out13, out14, out15
  Adder #(.width(4)) adder_1 (.a(sc_1_binary_out), .b(SEL), .out(UOP_ADDR));  // open: cin, cout
endmodule

module MHR (
  input  MODE_IN,
  input  EOI,
  input  CLK,
  input  RESET,
  output MODE_OUT
);

  wire and_1_out, nand_1_out, or_1_out, xor_1_out;

  nand nand_1 (nand_1_out, MODE_IN, EOI);
  or or_1 (or_1_out, MODE_IN, EOI);
  and and_1 (and_1_out, or_1_out, xor_1_out);
  xor xor_1 (xor_1_out, EOI, CLK);
  D_Flip_Flop d_ff_1 (.D(nand_1_out), .clk(and_1_out), .Q(MODE_OUT), .reset(RESET));  // open: Qn, preset
endmodule

module MHS (
  input  I0,
  input  I1,
  input  CLK,
  input  RESET,
  input  MR,
  output [3:0] UOP_OUT
);

  wire and_1_out, nor_1_out, not_1_out, or_1_out, or_2_out;
  wire [3:0] controlled_buffer_1_out, multiplexer_1_out;

  not not_1 (not_1_out, I1);
  nor nor_1 (nor_1_out, I0, not_1_out);
  or or_1 (or_1_out, I0, I1);
  assign controlled_buffer_1_out = or_1_out ? multiplexer_1_out : 4'bz;  // Controlled_Buffer controlled_buffer_1
  Multiplexer #(.width(4)) multiplexer_1 (.in0(4'b0000), .in1(4'b0101), .out(multiplexer_1_out), .sel(nor_1_out));
  Register #(.width(4)) register_1 (
    .D(controlled_buffer_1_out), .en(and_1_out), .clk(and_1_out), .Q(UOP_OUT), .clr(or_2_out));
  and and_1 (and_1_out, or_1_out, CLK);
  or or_2 (or_2_out, RESET, MR);
endmodule

module EXEC_LCH (
  input  EXEC_IN,
  input  RESET,
  input  EOI,
  input  CLK,
  output EXEC_OUT
);

  wire and_1_out, or_1_out;

  D_Flip_Flop d_ff_1 (.D(EXEC_IN), .clk(EXEC_IN), .Q(EXEC_OUT), .reset(or_1_out));  // open: Qn, preset
  or or_1 (or_1_out, and_1_out, RESET);
  and and_1 (and_1_out, CLK, EOI);
endmodule

module RESET_LCH (
  input  FAULT_IN,
  input  CLK,
  input  BUTTON_IN,
  output RESET_OUT
);

  wire d_ff_1_q, multiplexer_1_out, not_1_out;

  D_Flip_Flop d_ff_1 (.D(FAULT_IN), .clk(CLK), .Q(d_ff_1_q), .reset(BUTTON_IN));  // open: Qn, preset
  Multiplexer multiplexer_1 (.in0(d_ff_1_q), .in1(1'b0), .out(multiplexer_1_out), .sel(not_1_out));
  not not_1 (not_1_out, CLK);
  or or_1 (RESET_OUT, multiplexer_1_out, BUTTON_IN);
endmodule

module BUS_FLT (
  input  ROM,
  input  CROSS_BUS1,
  input  I0,
  input  CROSS_BUS_2,
  input  I1,
  input  I2,
  input  I3,
  input  I4,
  input  I5,
  input  I6,
  input  I7,
  input  I8,
  input  I9,
  input  I10,
  input  I11,
  input  I12,
  input  I13,
  input  I14,
  input  I15,
  output O0,
  output O1,
  output O2,
  output O3,
  output O4,
  output O5,
  output O6,
  output O7,
  output O8,
  output O9,
  output O10,
  output O11,
  output O12,
  output O13,
  output O14,
  output O15
);

  wire or_1_out, or_2_out;

  or or_1 (or_1_out, ROM, CROSS_BUS_2);
  or or_2 (or_2_out, CROSS_BUS1, CROSS_BUS_2);
  assign O0 = or_1_out ? I0 : 1'bz;  // Controlled_Buffer controlled_buffer_1
  assign O1 = or_1_out ? I1 : 1'bz;  // Controlled_Buffer controlled_buffer_2
  assign O2 = or_1_out ? I2 : 1'bz;  // Controlled_Buffer controlled_buffer_3
  assign O3 = or_1_out ? I3 : 1'bz;  // Controlled_Buffer controlled_buffer_4
  assign O4 = or_1_out ? I4 : 1'bz;  // Controlled_Buffer controlled_buffer_5
  assign O5 = or_1_out ? I5 : 1'bz;  // Controlled_Buffer controlled_buffer_6
  assign O6 = or_2_out ? I6 : 1'bz;  // Controlled_Buffer controlled_buffer_7
  assign O7 = or_2_out ? I7 : 1'bz;  // Controlled_Buffer controlled_buffer_8
  assign O8 = or_2_out ? I8 : 1'bz;  // Controlled_Buffer controlled_buffer_9
  assign O9 = or_2_out ? I9 : 1'bz;  // Controlled_Buffer controlled_buffer_10
  assign O10 = or_2_out ? I10 : 1'bz;  // Controlled_Buffer controlled_buffer_11
  assign O11 = or_2_out ? I11 : 1'bz;  // Controlled_Buffer controlled_buffer_12
  assign O12 = or_2_out ? I12 : 1'bz;  // Controlled_Buffer controlled_buffer_13
  assign O13 = or_2_out ? I13 : 1'bz;  // Controlled_Buffer controlled_buffer_14
  assign O14 = or_2_out ? I14 : 1'bz;  // Controlled_Buffer controlled_buffer_15
  assign O15 = or_2_out ? I15 : 1'bz;  // Controlled_Buffer controlled_buffer_16
endmodule

module PC (
  input  [15:0] ADDR_IN,
  input  MH_COUNTER_ENB,
  input  JUMP,
  input  COUNTER_ENB,
  input  CLOCK,
  input  RESET,
  input  OE,
  output [15:0] ALWAYS_OUT,
  output [15:0] ADDR_OUT
);

  wire and_1_out, and_2_out, d_ff_1_q, multiplexer_1_out, not_1_out, not_2_out, or_1_out, or_2_out, or_3_out;

  Multiplexer multiplexer_1 (.in0(MH_COUNTER_ENB), .in1(1'b0), .out(multiplexer_1_out), .sel(JUMP));
  D_Flip_Flop d_ff_1 (.D(multiplexer_1_out), .clk(or_1_out), .Q(d_ff_1_q), .reset(RESET));  // open: Qn, preset
  not not_1 (not_1_out, multiplexer_1_out);
  or or_1 (or_1_out, not_1_out, CLOCK);
  or or_2 (or_2_out, JUMP, COUNTER_ENB);
  not not_2 (not_2_out, CLOCK);
  Counter #(.max('hffff), .width(16)) counter_1 (
    .clr(RESET), .load(JUMP), .clk(or_3_out), .D(ADDR_IN), .Q(ALWAYS_OUT));  // open: up, count, carry
  and and_1 (and_1_out, or_2_out, CLOCK);
  or or_3 (or_3_out, and_1_out, and_2_out);
  and and_2 (and_2_out, not_2_out, d_ff_1_q);
  assign ADDR_OUT = OE ? ALWAYS_OUT : 16'bz;  // Controlled_Buffer controlled_buffer_1
endmodule

module UPC (
  input  HAS_IMM,
  input  IMM_EXT,
  input  MR,
  input  RESET,
  input  COUNTER_ENB,
  input  CLOCK,
  input  [7:0] ADDR_IN,
  input  OE,
  output [3:0] CURRENT,
  output [7:0] ALWAYS_OUT,
  output [7:0] ADDR_OUT
);

  wire controlled_buffer_1_out, decoder_1_out5, not_1_out, or_1_out, or_2_out;
  wire [3:0] decoder_1_out4, sc_1_binary_out;
  wire [7:0] adder_1_out, counter_1_q, multiplexer_1_out, multiplexer_2_out;

  or or_1 (or_1_out, MR, RESET);
  Counter counter_1 (
    .clr(or_1_out), .up(COUNTER_ENB), .count(COUNTER_ENB), .clk(CLOCK), .Q(counter_1_q));  // open: load, D, carry
  assign controlled_buffer_1_out = COUNTER_ENB ? CLOCK : 1'bz;  // Controlled_Buffer controlled_buffer_1
  or or_2 (or_2_out, or_1_out, decoder_1_out5);
  SC sc_1 (.RESET(or_2_out), .CLOCK(controlled_buffer_1_out), .BINARY_OUT(sc_1_binary_out));
  Decoder #(.enable("false"), .select(4)) decoder_1 (
    .out1(decoder_1_out4[3]), .out2(decoder_1_out4[2]), .out3(decoder_1_out4[1]), .out4(decoder_1_out4[0]),
    .out5(decoder_1_out5), .sel(sc_1_binary_out));  // open: out0, out6, out7, out8, out9, out10, out11, out12, out13, out14, out15
  Multiplexer #(.width(8)) multiplexer_1 (.in0(8'h1), .in1({8{1'b0}}), .out(multiplexer_1_out), .sel(IMM_EXT));
  Adder adder_1 (.a(multiplexer_1_out), .b(counter_1_q), .out(adder_1_out));  // open: cin, cout
  Multiplexer #(.width(8)) multiplexer_2 (.in0(counter_1_q), .in1(adder_1_out), .out(multiplexer_2_out), .sel(HAS_IMM));
  not not_1 (not_1_out, OE);
  Adder adder_2 (.a(ADDR_IN), .b(multiplexer_2_out), .out(ALWAYS_OUT));  // open: cin, cout
  Multiplexer #(.width(4)) multiplexer_3 (.in0(decoder_1_out4), .in1(4'b0000), .out(CURRENT), .sel(not_1_out));
  assign ADDR_OUT = OE ? ALWAYS_OUT : 8'bz;  // Controlled_Buffer controlled_buffer_2
endmodule

module R0 (
  input  [15:0] DATA_IN,
  input  STORE,
  input  OE,
  input  MH_STORE,
  input  CLOCK,
  input  MH_OE,
  input  RESET,
  output [15:0] ALWAYS_OUT,
  output [15:0] DATA_OUT
);

  wire or_1_out, or_2_out;

  or or_1 (or_1_out, STORE, MH_STORE);
  Register #(.width(16)) register_1 (.D(DATA_IN), .en(or_1_out), .clk(CLOCK), .Q(ALWAYS_OUT), .clr(RESET));
  assign DATA_OUT = or_2_out ? ALWAYS_OUT : 16'bz;  // Controlled_Buffer controlled_buffer_1
  or or_2 (or_2_out, OE, MH_OE);
endmodule

module R1 (
  input  [15:0] DATA_IN,
  input  STORE,
  input  OE,
  input  CLOCK,
  input  MH_OE,
  input  RESET,
  output [15:0] ALWAYS_OUT,
  output [15:0] DATA_OUT
);

  wire or_1_out;

  Register #(.width(16)) register_1 (.D(DATA_IN), .en(STORE), .clk(CLOCK), .Q(ALWAYS_OUT), .clr(RESET));
  assign DATA_OUT = or_1_out ? ALWAYS_OUT : 16'bz;  // Controlled_Buffer controlled_buffer_1
  or or_1 (or_1_out, OE, MH_OE);
endmodule

module REG_FILE (
  input  [15:0] REG_IN,
  input  [2:0] A_SEL,
  input  [2:0] B_SEL,
  input  B_ENB,
  input  CONST,
  input  INTERNAL_OP,
  input  WE,
  input  RESET,
  input  CLK,
  input  A_OE,
  input  B_OE,
  input  A_ALU_OE,
  input  B_ALU_OE,
  output [15:0] A_OUT,
  output [15:0] A_ALU_OUT,
  output [15:0] B_OUT,
  output [15:0] B_ALU_OUT
);

  wire and_1_out, and_2_out, and_3_out, and_4_out, and_5_out, and_6_out, and_7_out, and_8_out, and_9_out,
       controlled_buffer_5_out, decoder_1_out0, decoder_1_out1, decoder_1_out2, decoder_1_out3,
       decoder_1_out4, decoder_1_out5, decoder_1_out6, decoder_1_out7, not_1_out;
  wire [2:0] controlled_buffer_1_out, multiplexer_1_out;
  wire [15:0] controlled_buffer_3_out, controlled_buffer_6_out, controlled_buffer_7_out,
       controlled_buffer_8_out, controlled_buffer_9_out, controlled_buffer_10_out, controlled_buffer_11_out,
       controlled_buffer_12_out, controlled_buffer_13_out, multiplexer_2_out, multiplexer_3_out,
       multiplexer_4_out, R0_q, R1_q, R2_q, R3_q, R4_q, R5_q, R6_q, SP_q;

  assign controlled_buffer_1_out = B_ENB ? B_SEL : 3'bz;  // Controlled_Buffer controlled_buffer_1
  LED led_1 (.in(controlled_buffer_1_out[2]));
  LED led_2 (.in(controlled_buffer_1_out[1]));
  LED led_3 (.in(controlled_buffer_1_out[0]));
  LED led_4 (.in(multiplexer_1_out[2]));
  LED led_5 (.in(multiplexer_1_out[1]));
  Multiplexer #(.width(3)) multiplexer_1 (.in0(A_SEL), .in1(3'b111), .out(multiplexer_1_out), .sel(CONST));
  LED led_6 (.in(multiplexer_1_out[0]));
  Decoder #(.select(3)) decoder_1 (
    .out0(decoder_1_out0), .out1(decoder_1_out1), .out2(decoder_1_out2), .out3(decoder_1_out3),
    .out4(decoder_1_out4), .out5(decoder_1_out5), .out6(decoder_1_out6), .out7(decoder_1_out7),
    .sel(multiplexer_1_out), .en(WE));
  and and_1 (and_1_out, B_OE, INTERNAL_OP);
  assign B_OUT = controlled_buffer_5_out ? multiplexer_3_out : 16'bz;  // Controlled_Buffer controlled_buffer_2
  not not_1 (not_1_out, INTERNAL_OP);
  Multiplexer #(.width(16)) multiplexer_2 (
    .in0(REG_IN), .in1(controlled_buffer_3_out), .out(multiplexer_2_out), .sel(INTERNAL_OP));
  assign controlled_buffer_3_out = and_1_out ? multiplexer_3_out : 16'bz;  // Controlled_Buffer controlled_buffer_3
  Multiplexer #(.disabled("Z"), .select(3), .width(16)) multiplexer_3 (
    .in0(R0_q), .in1(R1_q), .in2(R2_q), .in3(R3_q), .in4(R4_q), .in5(R5_q), .in6(R6_q), .in7(SP_q),
    .out(multiplexer_3_out), .sel(controlled_buffer_1_out));
  assign B_ALU_OUT = B_ALU_OE ? multiplexer_3_out : 16'bz;  // Controlled_Buffer controlled_buffer_4
  assign controlled_buffer_5_out = not_1_out ? B_OE : 1'bz;  // Controlled_Buffer controlled_buffer_5
  assign controlled_buffer_6_out = decoder_1_out0 ? multiplexer_2_out : 16'bz;  // Controlled_Buffer controlled_buffer_6
  Register #(.width(16)) R0 (.D(controlled_buffer_6_out), .en(and_2_out), .clk(CLK), .Q(R0_q), .clr(RESET));
  and and_2 (and_2_out, decoder_1_out0, WE);
  assign controlled_buffer_7_out = decoder_1_out1 ? multiplexer_2_out : 16'bz;  // Controlled_Buffer controlled_buffer_7
  Register #(.width(16)) R1 (.D(controlled_buffer_7_out), .en(and_3_out), .clk(CLK), .Q(R1_q), .clr(RESET));
  and and_3 (and_3_out, decoder_1_out1, WE);
  assign controlled_buffer_8_out = decoder_1_out2 ? multiplexer_2_out : 16'bz;  // Controlled_Buffer controlled_buffer_8
  Register #(.width(16)) R2 (.D(controlled_buffer_8_out), .en(and_4_out), .clk(CLK), .Q(R2_q), .clr(RESET));
  and and_4 (and_4_out, decoder_1_out2, WE);
  assign controlled_buffer_9_out = decoder_1_out3 ? multiplexer_2_out : 16'bz;  // Controlled_Buffer controlled_buffer_9
  Register #(.width(16)) R3 (.D(controlled_buffer_9_out), .en(and_5_out), .clk(CLK), .Q(R3_q), .clr(RESET));
  and and_5 (and_5_out, decoder_1_out3, WE);
  assign controlled_buffer_10_out = decoder_1_out4 ? multiplexer_2_out : 16'bz;  // Controlled_Buffer controlled_buffer_10
  Register #(.width(16)) R4 (.D(controlled_buffer_10_out), .en(and_6_out), .clk(CLK), .Q(R4_q), .clr(RESET));
  and and_6 (and_6_out, decoder_1_out4, WE);
  assign controlled_buffer_11_out = decoder_1_out5 ? multiplexer_2_out : 16'bz;  // Controlled_Buffer controlled_buffer_11
  Register #(.width(16)) R5 (.D(controlled_buffer_11_out), .en(and_7_out), .clk(CLK), .Q(R5_q), .clr(RESET));
  and and_7 (and_7_out, decoder_1_out5, WE);
  assign controlled_buffer_12_out = decoder_1_out6 ? multiplexer_2_out : 16'bz;  // Controlled_Buffer controlled_buffer_12
  Register #(.width(16)) R6 (.D(controlled_buffer_12_out), .en(and_8_out), .clk(CLK), .Q(R6_q), .clr(RESET));
  and and_8 (and_8_out, decoder_1_out6, WE);
  assign controlled_buffer_13_out = decoder_1_out7 ? multiplexer_2_out : 16'bz;  // Controlled_Buffer controlled_buffer_13
  Register #(.width(16)) SP (.D(controlled_buffer_13_out), .en(and_9_out), .clk(CLK), .Q(SP_q), .clr(RESET));
  and and_9 (and_9_out, decoder_1_out7, WE);
  assign A_OUT = A_OE ? multiplexer_4_out : 16'bz;  // Controlled_Buffer controlled_buffer_14
  Multiplexer #(.disabled("Z"), .select(3), .width(16)) multiplexer_4 (
    .in0(R0_q), .in1(R1_q), .in2(R2_q), .in3(R3_q), .in4(R4_q), .in5(R5_q), .in6(R6_q), .in7(SP_q),
    .out(multiplexer_4_out), .sel(multiplexer_1_out));
  assign A_ALU_OUT = A_ALU_OE ? multiplexer_4_out : 16'bz;  // Controlled_Buffer controlled_buffer_15
endmodule

module RR (
  input  [15:0] DATA_IN,
  input  STORE,
  input  MH_STORE,
  input  OE,
  input  CLOCK,
  input  MH_OE,
  input  RESET,
  output [15:0] ALWAYS_OUT,
  output [15:0] DATA_OUT
);

  wire or_1_out, or_2_out;

  or or_1 (or_1_out, STORE, MH_STORE);
  Register #(.width(16)) register_1 (.D(DATA_IN), .en(or_1_out), .clk(CLOCK), .Q(ALWAYS_OUT), .clr(RESET));
  or or_2 (or_2_out, OE, MH_OE);
  assign DATA_OUT = or_2_out ? ALWAYS_OUT : 16'bz;  // Controlled_Buffer controlled_buffer_1
endmodule

module IR (
  input  [5:0] DATA_IN,
  input  STORE,
  input  CLOCK,
  input  MICRO_RESET,
  input  RESET,
  input  OE,
  input  IMM_EXT_IN,
  output [5:0] ALWAYS_OUT,
  output [5:0] DATA_OUT,
  output IMM_EXT_OUT,
  output LED_OUT
);

  wire d_ff_1_q, or_1_out;

  Register #(.width(6)) register_1 (.D(DATA_IN), .en(STORE), .clk(CLOCK), .Q(ALWAYS_OUT), .clr(or_1_out));
  or or_1 (or_1_out, MICRO_RESET, RESET);
  D_Flip_Flop d_ff_1 (.D(IMM_EXT_IN), .clk(CLOCK), .Q(d_ff_1_q), .reset(or_1_out));  // open: Qn, preset
  assign DATA_OUT = OE ? ALWAYS_OUT : 6'bz;  // Controlled_Buffer controlled_buffer_1
  assign IMM_EXT_OUT = OE ? d_ff_1_q : 1'bz;  // Controlled_Buffer controlled_buffer_2

  assign LED_OUT = IMM_EXT_OUT;
endmodule

module SC (
  input  RESET,
  input  CLOCK,
  output [3:0] BINARY_OUT
);

  Counter #(.max('hf), .width(4)) counter_1 (
    .clr(RESET), .up(1'b1), .count(1'b1), .clk(CLOCK), .Q(BINARY_OUT));  // open: load, D, carry
endmodule

module OTR (
  input  [12:0] DATA_IN,
  input  STORE,
  input  CLOCK,
  input  RESET,
  output [12:0] DATA_OUT
);

  Register #(.width(13)) register_1 (.D(DATA_IN), .en(STORE), .clk(CLOCK), .Q(DATA_OUT), .clr(RESET));
endmodule

module FLAGS (
  input  CARRY,
  input  ZERO,
  input  STORE,
  input  CLOCK,
  input  RESET,
  output CARRY_OUT,
  output ZERO_OUT
);

  Register #(.width(1)) register_1 (.D(CARRY), .en(STORE), .clk(CLOCK), .Q(CARRY_OUT), .clr(RESET));
  Register #(.width(1)) register_2 (.D(ZERO), .en(STORE), .clk(CLOCK), .Q(ZERO_OUT), .clr(RESET));
endmodule

module ZR (
  input  [15:0] DATA_IN,
  output ZERO
);

  wire or_1_out, or_2_out, or_3_out, or_4_out, or_5_out, or_6_out, or_7_out, or_8_out, or_9_out, or_10_out,
       or_11_out, or_12_out, or_13_out, or_14_out, or_15_out;

  or or_1 (or_1_out, DATA_IN[0], DATA_IN[1]);
  or or_2 (or_2_out, DATA_IN[2], DATA_IN[3]);
  or or_3 (or_3_out, DATA_IN[4], DATA_IN[5]);
  or or_4 (or_4_out, DATA_IN[6], DATA_IN[7]);
  or or_5 (or_5_out, DATA_IN[8], DATA_IN[9]);
  or or_6 (or_6_out, DATA_IN[10], DATA_IN[11]);
  or or_7 (or_7_out, DATA_IN[12], DATA_IN[13]);
  or or_8 (or_8_out, DATA_IN[14], DATA_IN[15]);
  or or_9 (or_9_out, or_1_out, or_2_out);
  or or_10 (or_10_out, or_3_out, or_4_out);
  or or_11 (or_11_out, or_5_out, or_6_out);
  or or_12 (or_12_out, or_7_out, or_8_out);
  or or_13 (or_13_out, or_9_out, or_10_out);
  or or_14 (or_14_out, or_11_out, or_12_out);
  or or_15 (or_15_out, or_13_out, or_14_out);
  not not_1 (ZERO, or_15_out);
endmodule

module MAR (
  input  [15:0] DATA_IN,
  input  STORE,
  input  MH_STORE,
  input  CLOCK,
  input  MICRO_RESET,
  input  RESET,
  input  OE,
  output [15:0] ALWAYS_OUT,
  output [15:0] DATA_OUT
);

  wire or_1_out, or_2_out;

  or or_1 (or_1_out, STORE, MH_STORE);
  or or_2 (or_2_out, MICRO_RESET, RESET);
  Register #(.width(16)) register_1 (.D(DATA_IN), .en(or_1_out), .clk(CLOCK), .Q(ALWAYS_OUT), .clr(or_2_out));
  assign DATA_OUT = OE ? ALWAYS_OUT : 16'bz;  // Controlled_Buffer controlled_buffer_1
endmodule

module OPR (
  input  [2:0] DATA_IN,
  input  STORE,
  input  CLOCK,
  input  RESET,
  input  MICRO_RESET,
  input  OE,
  output [2:0] ALWAYS_OUT,
  output [2:0] DATA_OUT
);

  wire or_1_out;

  or or_1 (or_1_out, RESET, MICRO_RESET);
  Register #(.width(3)) register_1 (.D(DATA_IN), .en(STORE), .clk(CLOCK), .Q(ALWAYS_OUT), .clr(or_1_out));
  assign DATA_OUT = OE ? ALWAYS_OUT : 3'bz;  // Controlled_Buffer controlled_buffer_1
endmodule

module IMR (
  input  [15:0] DATA_IN,
  input  STORE,
  input  MH_STORE,
  input  CLOCK,
  input  OE,
  input  RESET,
  input  MICRO_RESET,
  input  RF_OE,
  output [15:0] ALWAYS_OUT,
  output [15:0] DATA_OUT,
  output [2:0] RF_DATA_OUT
);

  wire not_1_out, or_1_out, or_2_out;
  wire [15:0] multiplexer_1_out;
  wire [15:6] pull_resistor_1_node;

  Pull_Resistor pull_resistor_1 (.node(pull_resistor_1_node[6]));
  Pull_Resistor pull_resistor_2 (.node(pull_resistor_1_node[7]));
  Pull_Resistor pull_resistor_3 (.node(pull_resistor_1_node[8]));
  Pull_Resistor pull_resistor_4 (.node(pull_resistor_1_node[9]));
  Pull_Resistor pull_resistor_5 (.node(pull_resistor_1_node[10]));
  Pull_Resistor pull_resistor_6 (.node(pull_resistor_1_node[11]));
  Pull_Resistor pull_resistor_7 (.node(pull_resistor_1_node[12]));
  Pull_Resistor pull_resistor_8 (.node(pull_resistor_1_node[13]));
  Pull_Resistor pull_resistor_9 (.node(pull_resistor_1_node[14]));
  Pull_Resistor pull_resistor_10 (.node(pull_resistor_1_node[15]));
  or or_1 (or_1_out, STORE, MH_STORE);
  not not_1 (not_1_out, STORE);
  or or_2 (or_2_out, RESET, MICRO_RESET);
  Register #(.width(16)) register_1 (.D(multiplexer_1_out), .en(or_1_out), .clk(CLOCK), .Q(ALWAYS_OUT), .clr(or_2_out));
  Multiplexer #(.width(16)) multiplexer_1 (
    .in0({pull_resistor_1_node, DATA_IN[5:0]}), .in1(DATA_IN), .out(multiplexer_1_out), .sel(not_1_out));
  assign DATA_OUT = OE ? ALWAYS_OUT : 16'bz;  // Controlled_Buffer controlled_buffer_1
  assign RF_DATA_OUT = RF_OE ? ALWAYS_OUT[2:0] : 3'bz;  // Controlled_Buffer controlled_buffer_2
endmodule

module MEM (
  input  [15:0] ADDRESS,
  input  [15:0] DATA_IN,
  input  STORE,
  input  MH_STORE,
  input  CLOCK,
  input  OE,
  output [15:0] ALWAYS_OUT,
  output [15:0] RAM_OUT
);

  wire or_1_out;

  or or_1 (or_1_out, STORE, MH_STORE);
  RAM #(.addrWidth(16), .dataWidth(16), .enables("line")) ram_1 (
    .addr(ADDRESS), .we(or_1_out), .clk(CLOCK), .din(DATA_IN), .dout(ALWAYS_OUT));
  assign RAM_OUT = OE ? ALWAYS_OUT : 16'bz;  // Controlled_Buffer controlled_buffer_1
endmodule

module CLK (
  input  RESET,
  input  CLK_IN,
  input  CLK_ENB,
  input  MANUAL_CLK,
  input  HALT,
  output [15:0] CLK_COUNT,
  output CLK_OUT
);

  wire and_1_out, and_2_out, not_1_out, not_2_out, or_1_out;

  and and_1 (and_1_out, CLK_IN, CLK_ENB);
  not not_1 (not_1_out, CLK_ENB);
  and and_2 (and_2_out, not_1_out, MANUAL_CLK);
  not not_2 (not_2_out, HALT);
  or or_1 (or_1_out, and_1_out, and_2_out);
  and and_3 (CLK_OUT, or_1_out, not_2_out);
  Counter #(.max('hffff), .width(16)) counter_1 (
    .clr(RESET), .up(CLK_OUT), .count(CLK_OUT), .clk(CLK_OUT), .Q(CLK_COUNT));  // open: load, D, carry
endmodule

module BHI (
  input  in_1,
  input  in_2,
  input  in_3,
  input  in_4,
  input  in_5,
  input  in_6,
  input  in_7,
  input  in_8,
  input  in_9,
  input  in_10,
  output FLAG_OUT
);

  or or_1 (FLAG_OUT, in_1, in_2, in_3, in_4, in_5, in_6, in_7, in_8, in_9, in_10);
endmodule

module ALU_OPS (
  input  ADD1,
  input  SUB1,
  input  MUL1,
  input  DIV1,
  input  ADD2,
  input  SUB2,
  input  MUL2,
  input  DIV2,
  output [1:0] OP_OUT
);

  wire or_1_out, or_2_out, or_3_out, or_4_out;
  wire [1:0] pull_resistor_1_node;

  Pull_Resistor pull_resistor_1 (.node(pull_resistor_1_node));
  Priority_Encoder #(.disabled("Z"), .select(2)) priority_encoder_1 (
    .in0(or_1_out), .in1(or_2_out), .in2(or_3_out), .in3(or_4_out), .out(pull_resistor_1_node));
  or or_1 (or_1_out, ADD1, ADD2);
  or or_2 (or_2_out, SUB1, SUB2);
  or or_3 (or_3_out, MUL1, MUL2);
  or or_4 (or_4_out, DIV1, DIV2);
  Multiplexer #(.select(2), .width(2)) multiplexer_1 (
    .in0(2'b00), .in1(2'b01), .in2(2'b10), .in3(2'b11), .out(OP_OUT), .sel(pull_resistor_1_node));
endmodule

module ALU2 (
  input  [15:0] A_IN,
  input  [15:0] B_IN,
  input  ALLOC,
  input  [1:0] OP,
  input  REM_BIT,
  input  OE,
  output [15:0] ALU_OUT,
  output [15:0] ALWAYS_OUT,
  output COUT
);

  wire adder_1_cout, and_1_out, and_2_out, not_1_out, subtractor_1_bout;
  wire [1:0] multiplexer_2_out;
  wire [15:0] adder_1_out, divider_1_out, divider_1_rem, multiplexer_1_out, multiplexer_3_out,
       multiplexer_4_out, multiplier_1_cout, multiplier_1_out, subtractor_1_out;

  Multiplexer #(.width(16)) multiplexer_1 (.in0(B_IN), .in1(16'hf), .out(multiplexer_1_out), .sel(ALLOC));
  Multiplexer #(.width(2)) multiplexer_2 (.in0(OP), .in1(2'b01), .out(multiplexer_2_out), .sel(ALLOC));
  Divider #(.width(16)) divider_1 (
    .a(A_IN), .b(multiplexer_1_out), .out(divider_1_out), .rem(divider_1_rem));  // open: upper
  Subtractor #(.width(16)) subtractor_1 (
    .a(A_IN), .b(multiplexer_1_out), .out(subtractor_1_out), .bout(subtractor_1_bout));  // open: bin
  Multiplier #(.width(16)) multiplier_1 (
    .a(A_IN), .b(multiplexer_1_out), .out(multiplier_1_out), .cout(multiplier_1_cout));  // open: cin
  Adder #(.width(16)) adder_1 (.a(A_IN), .b(multiplexer_1_out), .out(adder_1_out), .cout(adder_1_cout));  // open: cin
  Multiplexer #(.width(16)) multiplexer_3 (
    .in0(multiplier_1_cout), .in1(divider_1_rem), .out(multiplexer_3_out), .sel(and_1_out));
  and and_1 (and_1_out, multiplexer_2_out[0], multiplexer_2_out[1]);
  Multiplexer #(.select(2), .width(16)) multiplexer_4 (
    .in0(adder_1_out), .in1(subtractor_1_out), .in2(multiplier_1_out), .in3(divider_1_out),
    .out(multiplexer_4_out), .sel(multiplexer_2_out));
  not not_1 (not_1_out, multiplexer_2_out[1]);
  and and_2 (and_2_out, multiplexer_2_out[0], not_1_out);
  Multiplexer #(.width(16)) multiplexer_5 (
    .in0(multiplexer_4_out), .in1(multiplexer_3_out), .out(ALWAYS_OUT), .sel(REM_BIT));
  Multiplexer multiplexer_6 (.in0(adder_1_cout), .in1(subtractor_1_bout), .out(COUT), .sel(and_2_out));
  assign ALU_OUT = OE ? ALWAYS_OUT : 16'bz;  // Controlled_Buffer controlled_buffer_1
endmodule

module ALU (
  input  [15:0] R0_IN,
  input  [15:0] R1_IN,
  input  OE,
  input  SUB,
  input  MH_SUB,
  input  [9:0] SP_ADDRESS,
  input  SP_WE,
  input  MH_SP_WE,
  output [15:0] ALWAYS_OUT,
  output [15:0] ALU_OUT,
  output COUT
);

  wire not_1_out, not_2_out, or_1_out, or_2_out;
  wire [9:0] controlled_buffer_2_out, subtractor_1_out;
  wire [15:0] adder_1_out, controlled_buffer_1_out, xor_1_out;
  wire [15:10] pull_resistor_1_node;

  assign controlled_buffer_1_out = or_1_out ? {16{1'b1}} : 16'bz;  // Controlled_Buffer controlled_buffer_1
  or or_1 (or_1_out, SUB, MH_SUB);
  not not_1 (not_1_out, or_1_out);
  assign controlled_buffer_2_out = or_2_out ? SP_ADDRESS : 10'bz;  // Controlled_Buffer controlled_buffer_2
  or or_2 (or_2_out, SP_WE, MH_SP_WE);
  assign controlled_buffer_1_out = not_1_out ? {16{1'b0}} : 16'bz;  // Controlled_Buffer controlled_buffer_3
  not not_2 (not_2_out, OE);
  assign xor_1_out = R1_IN ^ controlled_buffer_1_out;  // XOR_Gate xor_1, 16 bits wide
  Subtractor #(.width(10)) subtractor_1 (
    .a(controlled_buffer_2_out), .b(10'h2), .out(subtractor_1_out));  // open: bin, bout
  Pull_Resistor pull_resistor_1 (.node(pull_resistor_1_node[10]));
  Pull_Resistor pull_resistor_2 (.node(pull_resistor_1_node[11]));
  Pull_Resistor pull_resistor_3 (.node(pull_resistor_1_node[12]));
  Pull_Resistor pull_resistor_4 (.node(pull_resistor_1_node[13]));
  Pull_Resistor pull_resistor_5 (.node(pull_resistor_1_node[14]));
  Pull_Resistor pull_resistor_6 (.node(pull_resistor_1_node[15]));
  Adder #(.width(16)) adder_1 (.a(R0_IN), .b(xor_1_out), .out(adder_1_out), .cin(or_1_out), .cout(COUT));
  Multiplexer #(.width(16)) multiplexer_1 (
    .in0(adder_1_out), .in1({pull_resistor_1_node, subtractor_1_out}), .out(ALWAYS_OUT), .sel(not_2_out));
  assign ALU_OUT = OE ? ALWAYS_OUT : 16'bz;  // Controlled_Buffer controlled_buffer_4
endmodule

module CPU (
  input  CLK_ENB,
  input  MANUAL_TICK,
  output [15:0] CLK_COUNT
);

  wire alu2_1_cout, ALU_OUT, clk_1_clk_out, clock_1_out, controlled_buffer_1_out, controlled_buffer_3_out,
       controlled_buffer_4_out, controlled_buffer_5_out, controlled_buffer_6_out, controlled_buffer_7_out,
       controlled_buffer_8_out, controlled_buffer_9_out, controlled_buffer_10_out, controlled_buffer_11_out,
       controlled_buffer_12_out, controlled_buffer_13_out, controlled_buffer_14_out,
       controlled_buffer_15_out, controlled_buffer_16_out, controlled_buffer_17_out,
       controlled_buffer_18_out, controlled_buffer_20_out, controlled_buffer_21_out,
       controlled_buffer_22_out, controlled_buffer_23_out, controlled_buffer_24_out,
       controlled_buffer_25_out, controlled_buffer_26_out, controlled_buffer_27_out,
       controlled_buffer_28_out, controlled_buffer_29_out, controlled_buffer_30_out,
       controlled_buffer_31_out, controlled_buffer_32_out, controlled_buffer_33_out,
       controlled_buffer_34_out, controlled_buffer_35_out, controlled_buffer_36_out,
       controlled_buffer_37_out, controlled_buffer_38_out, controlled_buffer_39_out,
       controlled_buffer_40_out, controlled_buffer_41_out, controlled_buffer_42_out,
       controlled_buffer_43_out, controlled_buffer_44_out, controlled_buffer_45_out,
       controlled_buffer_46_out, controlled_buffer_47_out, controlled_buffer_48_out,
       controlled_buffer_49_out, controlled_buffer_50_out, controlled_buffer_51_out,
       controlled_buffer_52_out, controlled_buffer_53_out, controlled_buffer_54_out,
       controlled_buffer_55_out, controlled_buffer_56_out, controlled_buffer_57_out,
       controlled_buffer_58_out, controlled_buffer_59_out, controlled_buffer_60_out,
       controlled_buffer_61_out, controlled_buffer_62_out, controlled_buffer_63_out,
       controlled_buffer_64_out, COUNTER_ENB, COUT, CROSS_BUS1, CROSS_BUS2, dcd_1_imm_ext_out, dcd_1_o1,
       dcd_1_o2, dcd_1_o3, dcd_1_o4, dcd_1_o5, dcd_1_o6, dcd_1_o7, dcd_1_o8, dcd_1_o9, dcd_1_o10, dcd_1_o11,
       dcd_1_o12, dcd_1_o13, dcd_1_o14, dcd_1_o15, dcd_1_o16, dcd_1_o17, dcd_1_o18, dcd_1_o19, dcd_1_o20,
       dcd_1_o21, dcd_1_o22, dcd_1_o23, dcd_1_o24, dcd_1_o25, dcd_1_o26, dcd_1_o27, dcd_1_o28, dcd_1_o29,
       dcd_1_o30, dcd_1_o31, dcd_1_o32, dcd_1_o33, dcd_1_o34, dcd_1_o35, dcd_1_o36, dcd_1_o37, dcd_1_o38,
       dcd_1_o39, dcd_1_o40, dcd_1_o41, dcd_1_o42, dcd_1_o43, dcd_1_o44, dcd_1_o45, dcd_1_o46, dcd_1_o47,
       dcd_1_o48, dcd_1_o49, dcd_1_o50, dcd_1_o51, dcd_1_o52, dcd_1_o53, dcd_1_o54, dcd_1_o55, dcd_1_o56,
       dcd_1_o57, dcd_1_o58, dcd_1_o59, dcd_1_o60, dcd_1_o61, dcd_1_o62, DCD_IN, dcd_jmp_1_j_out,
       decoder_1_out3, EOI, EXEC, FLAGS_IN, HALT, HAS_IMM, IMR_IN, IMR_OUT, IMR_RF_OUT, INR_IN, INR_OUT,
       ir_1_led_out, JUMP, JZ, MAR_IN, MAR_OUT, MR, NOP, not_1_out, not_2_out, not_3_out, OP_COUNTER_ENB,
       OP_IMR_IN, OP_MAR_IN, OP_ROM_OUT, OPR_IN, OPR_OUT, or_1_out, or_2_out, OUTPUT_REG_IN,
       pull_resistor_35_node, pull_resistor_81_node, RAM_IN, RAM_OUT, REM_ENB, RESET, RF_A_ALU_OUT, RF_A_OUT,
       RF_B_ALU_OUT, RF_B_ENB, RF_B_OUT, RF_IN, RF_INTERNAL_OP, ROM_OUT, ZERO, zr_1_zero;
  wire [1:0] alu_ops_1_op_out;
  wire [2:0] decoder_1_out2, imr_1_data_out_2, imr_1_rf_data_out, opr_1_always_out, opr_1_data_out;
  wire [3:0] C_OP, sc_1_binary_out;
  wire [3:3] pull_resistor_1_node;
  wire [5:0] dcd_1_dcd_out, imr_1_data_out_3, ir_1_always_out;
  wire [7:0] dcd_1_pc_out, upc_1_always_out;
  wire [9:0] imr_1_data_out;
  wire [12:0] binary_to_bcd_converter_1_p1;
  wire [15:0] alu2_1_always_out, imr_1_always_out, mar_1_always_out, mar_1_data_out, mem_1_always_out,
       PC_ADDR, reg_file_1_a_alu_out, reg_file_1_b_alu_out, rom_1_data;
  wire [15:6] rom_2_data;
  wire [29:0] rom_3_data;
  wire [29:3] controlled_buffer_65_out;

  not not_1 (not_1_out, clk_1_clk_out);
  not not_2 (not_2_out, EXEC);
  assign controlled_buffer_1_out = not_2_out ? not_1_out : 1'bz;  // Controlled_Buffer controlled_buffer_1
  or or_1 (or_1_out, RESET, decoder_1_out3);
  SC sc_1 (.RESET(or_1_out), .CLOCK(controlled_buffer_1_out), .BINARY_OUT(sc_1_binary_out));
  EXEC_LCH exec_lch_1 (.EXEC_IN(rom_2_data[6]), .RESET(RESET), .EOI(EOI), .CLK(clk_1_clk_out), .EXEC_OUT(EXEC));
  LED led_1 (.in(decoder_1_out2[2]));
  Clock clock_1 (.out(clock_1_out));
  LED led_2 (.in(decoder_1_out2[1]));
  LED led_3 (.in(decoder_1_out2[0]));
  Decoder #(.enable("false"), .select(3)) decoder_1 (
    .out0(decoder_1_out2[2]), .out1(decoder_1_out2[1]), .out2(decoder_1_out2[0]), .out3(decoder_1_out3),
    .sel(sc_1_binary_out[2:0]));  // open: out4, out5, out6, out7
  CLK clk_1 (
    .RESET(RESET), .CLK_IN(clock_1_out), .CLK_ENB(CLK_ENB), .MANUAL_CLK(MANUAL_TICK), .HALT(HALT),
    .CLK_OUT(clk_1_clk_out), .CLK_COUNT(CLK_COUNT));
  LED led_4 (.in(mar_1_always_out[15]));
  LED led_5 (.in(mar_1_always_out[14]));
  LED led_6 (.in(mar_1_always_out[13]));
  LED led_7 (.in(imr_1_always_out[15]));
  LED led_8 (.in(imr_1_always_out[14]));
  LED led_9 (.in(imr_1_always_out[13]));
  ROM #(.addrWidth(16), .dataWidth(16)) rom_1 (.addr(PC_ADDR), .data(rom_1_data));
  Pull_Resistor pull_resistor_1 (.node(pull_resistor_1_node[3]));
  ROM #(.addrWidth(4), .dataWidth(16)) rom_2 (
    .addr({pull_resistor_1_node[3], sc_1_binary_out[3], sc_1_binary_out[1:0]}),
    .data({rom_2_data[15:10], OPR_IN, IMR_IN, MR, rom_2_data[6], MAR_IN, INR_OUT, ROM_OUT, COUNTER_ENB, DCD_IN, INR_IN}));
  LED led_10 (.in(rom_2_data[15]));
  LED led_11 (.in(rom_2_data[14]));
  LED led_12 (.in(rom_2_data[13]));
  LED led_13 (.in(mar_1_always_out[10]));
  LED led_14 (.in(mar_1_always_out[9]));
  LED led_15 (.in(mar_1_always_out[12]));
  LED led_16 (.in(mar_1_always_out[11]));
  LED led_17 (.in(imr_1_always_out[10]));
  LED led_18 (.in(imr_1_always_out[9]));
  LED led_19 (.in(imr_1_always_out[12]));
  LED led_20 (.in(imr_1_always_out[11]));
  LED led_21 (.in(ir_1_always_out[4]));
  LED led_22 (.in(ir_1_always_out[3]));
  LED led_23 (.in(ir_1_always_out[5]));
  LED led_24 (.in(opr_1_always_out[2]));
  LED led_25 (.in(rom_2_data[10]));
  LED led_26 (.in(OPR_IN));
  LED led_27 (.in(rom_2_data[12]));
  LED led_28 (.in(rom_2_data[11]));
  MAR mar_1 (
    .STORE(MAR_IN), .MH_STORE(OP_MAR_IN), .DATA_IN(mar_1_data_out), .CLOCK(clk_1_clk_out), .RESET(RESET),
    .OE(MAR_OUT), .ALWAYS_OUT(mar_1_always_out), .DATA_OUT(mar_1_data_out));  // open: MICRO_RESET
  LED led_29 (.in(mar_1_always_out[8]));
  LED led_30 (.in(mar_1_always_out[7]));
  LED led_31 (.in(mar_1_always_out[6]));
  LED led_32 (.in(mar_1_always_out[5]));
  IMR imr_1 (
    .OE(IMR_OUT), .RF_OE(IMR_RF_OUT),
    .DATA_IN({imr_1_data_out_3, imr_1_data_out[9], imr_1_data_out_2, imr_1_data_out[5:0]}), .STORE(IMR_IN),
    .MH_STORE(OP_IMR_IN), .CLOCK(clk_1_clk_out), .RESET(RESET), .ALWAYS_OUT(imr_1_always_out),
    .DATA_OUT({imr_1_data_out_3, imr_1_data_out[9], imr_1_data_out_2, imr_1_data_out[5:0]}),
    .RF_DATA_OUT(imr_1_rf_data_out));  // open: MICRO_RESET
  LED led_33 (.in(imr_1_always_out[8]));
  LED led_34 (.in(imr_1_always_out[7]));
  LED led_35 (.in(imr_1_always_out[6]));
  LED led_36 (.in(imr_1_always_out[5]));
  IR ir_1 (
    .DATA_IN(imr_1_data_out_3), .STORE(INR_IN), .CLOCK(clk_1_clk_out), .RESET(RESET), .OE(INR_OUT),
    .IMM_EXT_IN(imr_1_data_out[9]), .ALWAYS_OUT(ir_1_always_out), .DATA_OUT(imr_1_data_out_3),
    .IMM_EXT_OUT(imr_1_data_out[9]), .LED_OUT(ir_1_led_out));  // open: MICRO_RESET
  LED led_37 (.in(ir_1_always_out[2]));
  LED led_38 (.in(ir_1_always_out[1]));
  LED led_39 (.in(ir_1_always_out[0]));
  LED led_40 (.in(ir_1_led_out));
  OPR opr_1 (
    .DATA_IN(imr_1_data_out_2), .STORE(OPR_IN), .CLOCK(clk_1_clk_out), .RESET(RESET), .OE(OPR_OUT),
    .ALWAYS_OUT(opr_1_always_out), .DATA_OUT(opr_1_data_out));  // open: MICRO_RESET
  LED led_41 (.in(opr_1_always_out[1]));
  LED led_42 (.in(opr_1_always_out[0]));
  LED led_43 (.in(IMR_IN));
  LED led_44 (.in(MR));
  LED led_45 (.in(rom_2_data[6]));
  LED led_46 (.in(MAR_IN));
  LED led_47 (.in(mar_1_always_out[4]));
  LED led_48 (.in(mar_1_always_out[3]));
  LED led_49 (.in(mar_1_always_out[2]));
  LED led_50 (.in(mar_1_always_out[1]));
  LED led_51 (.in(imr_1_always_out[4]));
  LED led_52 (.in(imr_1_always_out[3]));
  LED led_53 (.in(imr_1_always_out[2]));
  LED led_54 (.in(imr_1_always_out[1]));
  or or_2 (or_2_out, OP_ROM_OUT, ROM_OUT);
  LED led_55 (.in(INR_OUT));
  LED led_56 (.in(ROM_OUT));
  LED led_57 (.in(COUNTER_ENB));
  LED led_58 (.in(DCD_IN));
  LED led_59 (.in(mar_1_always_out[0]));
  LED led_60 (.in(imr_1_always_out[0]));
  assign {imr_1_data_out_3, imr_1_data_out[9], imr_1_data_out_2, imr_1_data_out[5:0]} = or_2_out ? rom_1_data : 16'bz;  // Controlled_Buffer controlled_buffer_2
  LED led_61 (.in(INR_IN));
  LED led_62 (.in(imr_1_data_out_3[5]));
  LED led_63 (.in(imr_1_data_out_3[4]));
  LED led_64 (.in(imr_1_data_out_3[3]));
  LED led_65 (.in(imr_1_data_out_3[2]));
  Pull_Resistor pull_resistor_2 (.node(imr_1_data_out_3[5]));
  Pull_Resistor pull_resistor_3 (.node(imr_1_data_out_3[4]));
  Pull_Resistor pull_resistor_4 (.node(imr_1_data_out_3[3]));
  Pull_Resistor pull_resistor_5 (.node(imr_1_data_out_3[2]));
  LED led_66 (.in(imr_1_data_out_3[1]));
  LED led_67 (.in(imr_1_data_out_3[0]));
  LED led_68 (.in(imr_1_data_out[9]));
  LED led_69 (.in(imr_1_data_out_2[2]));
  Pull_Resistor pull_resistor_6 (.node(imr_1_data_out_3[1]));
  Pull_Resistor pull_resistor_7 (.node(imr_1_data_out_3[0]));
  Pull_Resistor pull_resistor_8 (.node(imr_1_data_out[9]));
  Pull_Resistor pull_resistor_9 (.node(imr_1_data_out_2[2]));
  LED led_70 (.in(imr_1_data_out_2[1]));
  LED led_71 (.in(imr_1_data_out_2[0]));
  LED led_72 (.in(imr_1_data_out[5]));
  LED led_73 (.in(imr_1_data_out[4]));
  Pull_Resistor pull_resistor_10 (.node(imr_1_data_out_2[1]));
  Pull_Resistor pull_resistor_11 (.node(imr_1_data_out_2[0]));
  Pull_Resistor pull_resistor_12 (.node(imr_1_data_out[5]));
  Pull_Resistor pull_resistor_13 (.node(imr_1_data_out[4]));
  LED led_74 (.in(imr_1_data_out[3]));
  LED led_75 (.in(imr_1_data_out[2]));
  LED led_76 (.in(imr_1_data_out[1]));
  LED led_77 (.in(imr_1_data_out[0]));
  Pull_Resistor pull_resistor_14 (.node(imr_1_data_out[3]));
  Pull_Resistor pull_resistor_15 (.node(imr_1_data_out[2]));
  Pull_Resistor pull_resistor_16 (.node(imr_1_data_out[1]));
  Pull_Resistor pull_resistor_17 (.node(imr_1_data_out[0]));
  BUS_FLT bus_flt_1 (
    .ROM(or_2_out), .CROSS_BUS1(CROSS_BUS1), .CROSS_BUS_2(CROSS_BUS2), .I12(imr_1_data_out_3[2]),
    .I13(imr_1_data_out_3[3]), .I14(imr_1_data_out_3[4]), .I15(imr_1_data_out_3[5]), .I0(imr_1_data_out[0]),
    .I1(imr_1_data_out[1]), .I2(imr_1_data_out[2]), .I3(imr_1_data_out[3]), .I4(imr_1_data_out[4]),
    .I5(imr_1_data_out[5]), .I6(imr_1_data_out_2[0]), .I7(imr_1_data_out_2[1]), .I8(imr_1_data_out_2[2]),
    .I9(imr_1_data_out[9]), .I10(imr_1_data_out_3[0]), .I11(imr_1_data_out_3[1]), .O12(mar_1_data_out[12]),
    .O13(mar_1_data_out[13]), .O14(mar_1_data_out[14]), .O15(mar_1_data_out[15]), .O0(mar_1_data_out[0]),
    .O1(mar_1_data_out[1]), .O2(mar_1_data_out[2]), .O3(mar_1_data_out[3]), .O4(mar_1_data_out[4]),
    .O5(mar_1_data_out[5]), .O6(mar_1_data_out[6]), .O7(mar_1_data_out[7]), .O8(mar_1_data_out[8]),
    .O9(mar_1_data_out[9]), .O10(mar_1_data_out[10]), .O11(mar_1_data_out[11]));
  LED led_78 (.in(mar_1_data_out[15]));
  LED led_79 (.in(mar_1_data_out[14]));
  LED led_80 (.in(mar_1_data_out[13]));
  Pull_Resistor pull_resistor_18 (.node(mar_1_data_out[15]));
  Pull_Resistor pull_resistor_19 (.node(mar_1_data_out[14]));
  Pull_Resistor pull_resistor_20 (.node(mar_1_data_out[13]));
  LED led_81 (.in(mar_1_data_out[12]));
  LED led_82 (.in(mar_1_data_out[11]));
  LED led_83 (.in(mar_1_data_out[10]));
  LED led_84 (.in(mar_1_data_out[9]));
  Pull_Resistor pull_resistor_21 (.node(mar_1_data_out[12]));
  Pull_Resistor pull_resistor_22 (.node(mar_1_data_out[11]));
  Pull_Resistor pull_resistor_23 (.node(mar_1_data_out[10]));
  Pull_Resistor pull_resistor_24 (.node(mar_1_data_out[9]));
  LED led_85 (.in(mar_1_data_out[8]));
  LED led_86 (.in(mar_1_data_out[7]));
  LED led_87 (.in(mar_1_data_out[6]));
  LED led_88 (.in(mar_1_data_out[5]));
  Pull_Resistor pull_resistor_25 (.node(mar_1_data_out[8]));
  Pull_Resistor pull_resistor_26 (.node(mar_1_data_out[7]));
  Pull_Resistor pull_resistor_27 (.node(mar_1_data_out[6]));
  Pull_Resistor pull_resistor_28 (.node(mar_1_data_out[5]));
  LED led_89 (.in(mar_1_data_out[4]));
  LED led_90 (.in(mar_1_data_out[3]));
  LED led_91 (.in(mar_1_data_out[2]));
  LED led_92 (.in(mar_1_data_out[1]));
  Pull_Resistor pull_resistor_29 (.node(mar_1_data_out[4]));
  Pull_Resistor pull_resistor_30 (.node(mar_1_data_out[3]));
  Pull_Resistor pull_resistor_31 (.node(mar_1_data_out[2]));
  Pull_Resistor pull_resistor_32 (.node(mar_1_data_out[1]));
  LED led_93 (.in(mar_1_data_out[0]));
  Pull_Resistor pull_resistor_33 (.node(mar_1_data_out[0]));
  Pull_Resistor pull_resistor_34 (.node(RESET));
  LED led_94 (.in(dcd_1_dcd_out[5]));
  LED led_95 (.in(dcd_1_dcd_out[4]));
  UPC upc_1 (
    .HAS_IMM(HAS_IMM), .IMM_EXT(dcd_1_imm_ext_out), .MR(MR), .RESET(RESET), .COUNTER_ENB(EXEC),
    .CLOCK(not_3_out), .OE(EXEC), .ADDR_IN(dcd_1_pc_out), .CURRENT(C_OP), .ALWAYS_OUT(upc_1_always_out));  // open: ADDR_OUT
  ROM #(.dataWidth(30)) rom_3 (.addr(upc_1_always_out), .data(rom_3_data));
  LED led_96 (.in(mem_1_always_out[15]));
  LED led_97 (.in(dcd_1_dcd_out[3]));
  LED led_98 (.in(dcd_1_dcd_out[2]));
  LED led_99 (.in(dcd_1_dcd_out[1]));
  LED led_100 (.in(dcd_1_dcd_out[0]));
  Button u_RESET (.out(RESET));
  PC pc_1 (
    .ADDR_IN(mar_1_data_out), .MH_COUNTER_ENB(OP_COUNTER_ENB), .JUMP(dcd_jmp_1_j_out),
    .COUNTER_ENB(COUNTER_ENB), .CLOCK(clk_1_clk_out), .RESET(RESET), .ALWAYS_OUT(PC_ADDR),
    .ADDR_OUT(mar_1_data_out));  // open: OE
  LED led_101 (.in(mem_1_always_out[14]));
  LED led_102 (.in(mem_1_always_out[13]));
  LED led_103 (.in(mem_1_always_out[12]));
  LED led_104 (.in(mem_1_always_out[11]));
  _7_Segment_Display u_7_segment_display_1 ();  // open: g, f, a, b, e, d, c, dp
  // BCD_to_7_Segment_decoder bcd_to_7_segment_decoder_1: pin names not known
  // Binary_to_BCD_converter #(.binvalue(13)) binary_to_bcd_converter_1: pin names not known; wires that end beside it: binary_to_bcd_converter_1_p1
  LED led_105 (.in(C_OP[3]));
  LED led_106 (.in(C_OP[2]));
  LED led_107 (.in(C_OP[1]));
  LED led_108 (.in(C_OP[0]));
  Pull_Resistor pull_resistor_35 (.node(pull_resistor_35_node));
  DCD dcd_1 (
    .IMM_EXT_IN(imr_1_data_out[9]), .SELECTOR(imr_1_data_out_3), .CLK(clk_1_clk_out), .WE(DCD_IN),
    .EXEC(EXEC), .RESET(RESET), .MICRO_RESET(MR), .DCD_OUT(dcd_1_dcd_out), .PC_OUT(dcd_1_pc_out),
    .IMM_EXT_OUT(dcd_1_imm_ext_out), .O7(dcd_1_o7), .O8(dcd_1_o8), .O9(dcd_1_o9), .O10(dcd_1_o10),
    .O11(dcd_1_o11), .O12(dcd_1_o12), .O13(dcd_1_o13), .O14(dcd_1_o14), .O15(dcd_1_o15), .O16(dcd_1_o16),
    .O17(dcd_1_o17), .O18(dcd_1_o18), .O19(dcd_1_o19), .O20(dcd_1_o20), .O21(dcd_1_o21), .O22(dcd_1_o22),
    .O23(dcd_1_o23), .O24(dcd_1_o24), .O25(dcd_1_o25), .O26(dcd_1_o26), .O27(dcd_1_o27), .O28(dcd_1_o28),
    .O29(dcd_1_o29), .O30(dcd_1_o30), .O31(dcd_1_o31), .O0(pull_resistor_35_node), .O32(dcd_1_o32),
    .O33(dcd_1_o33), .O34(dcd_1_o34), .O35(dcd_1_o35), .O36(dcd_1_o36), .O37(dcd_1_o37), .O38(dcd_1_o38),
    .O39(dcd_1_o39), .O40(dcd_1_o40), .O41(dcd_1_o41), .O1(dcd_1_o1), .O42(dcd_1_o42), .O43(dcd_1_o43),
    .O44(dcd_1_o44), .O45(dcd_1_o45), .O46(dcd_1_o46), .O47(dcd_1_o47), .O48(dcd_1_o48), .O49(dcd_1_o49),
    .O50(dcd_1_o50), .O51(dcd_1_o51), .O2(dcd_1_o2), .O52(dcd_1_o52), .O53(dcd_1_o53), .O54(dcd_1_o54),
    .O55(dcd_1_o55), .O56(dcd_1_o56), .O57(dcd_1_o57), .O58(dcd_1_o58), .O59(dcd_1_o59), .O60(dcd_1_o60),
    .O61(dcd_1_o61), .O3(dcd_1_o3), .O62(dcd_1_o62), .O4(dcd_1_o4), .O5(dcd_1_o5), .O6(dcd_1_o6));  // open: O63
  not not_3 (not_3_out, clk_1_clk_out);
  MEM mem_1 (
    .STORE(RAM_IN), .CLOCK(clk_1_clk_out), .OE(RAM_OUT), .ADDRESS(mar_1_data_out),
    .DATA_IN({imr_1_data_out_3, imr_1_data_out[9], imr_1_data_out_2, imr_1_data_out[5:0]}),
    .ALWAYS_OUT(mem_1_always_out),
    .RAM_OUT({imr_1_data_out_3, imr_1_data_out[9], imr_1_data_out_2, imr_1_data_out[5:0]}));  // open: MH_STORE
  LED led_109 (.in(mem_1_always_out[10]));
  LED led_110 (.in(mem_1_always_out[9]));
  LED led_111 (.in(mem_1_always_out[8]));
  LED led_112 (.in(mem_1_always_out[7]));
  ALU2 alu2_1 (
    .OP(alu_ops_1_op_out), .REM_BIT(REM_ENB), .OE(ALU_OUT), .A_IN(reg_file_1_a_alu_out),
    .B_IN(reg_file_1_b_alu_out),
    .ALU_OUT({imr_1_data_out_3, imr_1_data_out[9], imr_1_data_out_2, imr_1_data_out[5:0]}),
    .ALWAYS_OUT(alu2_1_always_out), .COUT(alu2_1_cout));  // open: ALLOC
  REG_FILE reg_file_1 (
    .B_SEL(imr_1_rf_data_out), .B_ENB(RF_B_ENB), .INTERNAL_OP(RF_INTERNAL_OP), .WE(RF_IN), .RESET(RESET),
    .CLK(clk_1_clk_out), .A_OE(RF_A_OUT), .B_OE(RF_B_OUT), .A_ALU_OE(RF_A_ALU_OUT), .B_ALU_OE(RF_B_ALU_OUT),
    .A_SEL(opr_1_data_out),
    .REG_IN({imr_1_data_out_3, imr_1_data_out[9], imr_1_data_out_2, imr_1_data_out[5:0]}),
    .B_OUT({imr_1_data_out_3, imr_1_data_out[9], imr_1_data_out_2, imr_1_data_out[5:0]}),
    .B_ALU_OUT(reg_file_1_b_alu_out),
    .A_OUT({imr_1_data_out_3, imr_1_data_out[9], imr_1_data_out_2, imr_1_data_out[5:0]}),
    .A_ALU_OUT(reg_file_1_a_alu_out));  // open: CONST
  OTR otr_1 (
    .DATA_IN({imr_1_data_out_3[2:0], imr_1_data_out[9], imr_1_data_out_2, imr_1_data_out[5:0]}),
    .STORE(OUTPUT_REG_IN), .CLOCK(clk_1_clk_out), .RESET(RESET), .DATA_OUT(binary_to_bcd_converter_1_p1));
  _7_Segment_Display u_7_segment_display_2 ();  // open: g, f, a, b, e, d, c, dp
  // BCD_to_7_Segment_decoder bcd_to_7_segment_decoder_2: pin names not known
  LED led_113 (.in(controlled_buffer_64_out));
  LED led_114 (.in(controlled_buffer_63_out));
  assign controlled_buffer_3_out = dcd_1_o1 ? dcd_1_o1 : 1'bz;  // Controlled_Buffer controlled_buffer_3
  assign controlled_buffer_4_out = dcd_1_o2 ? dcd_1_o2 : 1'bz;  // Controlled_Buffer controlled_buffer_4
  assign controlled_buffer_5_out = dcd_1_o3 ? dcd_1_o3 : 1'bz;  // Controlled_Buffer controlled_buffer_5
  assign controlled_buffer_6_out = dcd_1_o4 ? dcd_1_o4 : 1'bz;  // Controlled_Buffer controlled_buffer_6
  assign controlled_buffer_7_out = dcd_1_o5 ? dcd_1_o5 : 1'bz;  // Controlled_Buffer controlled_buffer_7
  assign controlled_buffer_8_out = dcd_1_o6 ? dcd_1_o6 : 1'bz;  // Controlled_Buffer controlled_buffer_8
  assign controlled_buffer_9_out = dcd_1_o7 ? dcd_1_o7 : 1'bz;  // Controlled_Buffer controlled_buffer_9
  assign controlled_buffer_10_out = dcd_1_o8 ? dcd_1_o8 : 1'bz;  // Controlled_Buffer controlled_buffer_10
  assign controlled_buffer_11_out = dcd_1_o9 ? dcd_1_o9 : 1'bz;  // Controlled_Buffer controlled_buffer_11
  assign controlled_buffer_12_out = dcd_1_o10 ? dcd_1_o10 : 1'bz;  // Controlled_Buffer controlled_buffer_12
  assign controlled_buffer_13_out = dcd_1_o11 ? dcd_1_o11 : 1'bz;  // Controlled_Buffer controlled_buffer_13
  assign controlled_buffer_14_out = dcd_1_o12 ? dcd_1_o12 : 1'bz;  // Controlled_Buffer controlled_buffer_14
  assign controlled_buffer_15_out = dcd_1_o13 ? dcd_1_o13 : 1'bz;  // Controlled_Buffer controlled_buffer_15
  assign controlled_buffer_16_out = dcd_1_o14 ? dcd_1_o14 : 1'bz;  // Controlled_Buffer controlled_buffer_16
  assign controlled_buffer_17_out = dcd_1_o15 ? dcd_1_o15 : 1'bz;  // Controlled_Buffer controlled_buffer_17
  assign controlled_buffer_18_out = dcd_1_o16 ? dcd_1_o16 : 1'bz;  // Controlled_Buffer controlled_buffer_18
  Controlled_Buffer controlled_buffer_19 (.in(dcd_1_o17), .en(dcd_1_o17));  // open: out
  assign controlled_buffer_20_out = dcd_1_o18 ? dcd_1_o18 : 1'bz;  // Controlled_Buffer controlled_buffer_20
  assign controlled_buffer_21_out = dcd_1_o19 ? dcd_1_o19 : 1'bz;  // Controlled_Buffer controlled_buffer_21
  assign controlled_buffer_22_out = dcd_1_o20 ? dcd_1_o20 : 1'bz;  // Controlled_Buffer controlled_buffer_22
  assign controlled_buffer_23_out = dcd_1_o21 ? dcd_1_o21 : 1'bz;  // Controlled_Buffer controlled_buffer_23
  assign controlled_buffer_24_out = dcd_1_o22 ? dcd_1_o22 : 1'bz;  // Controlled_Buffer controlled_buffer_24
  assign controlled_buffer_25_out = dcd_1_o23 ? dcd_1_o23 : 1'bz;  // Controlled_Buffer controlled_buffer_25
  assign controlled_buffer_26_out = dcd_1_o24 ? dcd_1_o24 : 1'bz;  // Controlled_Buffer controlled_buffer_26
  assign controlled_buffer_27_out = dcd_1_o25 ? dcd_1_o25 : 1'bz;  // Controlled_Buffer controlled_buffer_27
  assign controlled_buffer_28_out = dcd_1_o26 ? dcd_1_o26 : 1'bz;  // Controlled_Buffer controlled_buffer_28
  assign controlled_buffer_29_out = dcd_1_o27 ? dcd_1_o27 : 1'bz;  // Controlled_Buffer controlled_buffer_29
  assign controlled_buffer_30_out = dcd_1_o28 ? dcd_1_o28 : 1'bz;  // Controlled_Buffer controlled_buffer_30
  assign controlled_buffer_31_out = dcd_1_o29 ? dcd_1_o29 : 1'bz;  // Controlled_Buffer controlled_buffer_31
  assign controlled_buffer_32_out = dcd_1_o30 ? dcd_1_o30 : 1'bz;  // Controlled_Buffer controlled_buffer_32
  assign controlled_buffer_33_out = dcd_1_o31 ? dcd_1_o31 : 1'bz;  // Controlled_Buffer controlled_buffer_33
  assign controlled_buffer_34_out = dcd_1_o32 ? dcd_1_o32 : 1'bz;  // Controlled_Buffer controlled_buffer_34
  assign controlled_buffer_35_out = dcd_1_o33 ? dcd_1_o33 : 1'bz;  // Controlled_Buffer controlled_buffer_35
  assign controlled_buffer_36_out = dcd_1_o34 ? dcd_1_o34 : 1'bz;  // Controlled_Buffer controlled_buffer_36
  assign controlled_buffer_37_out = dcd_1_o35 ? dcd_1_o35 : 1'bz;  // Controlled_Buffer controlled_buffer_37
  assign controlled_buffer_38_out = dcd_1_o36 ? dcd_1_o36 : 1'bz;  // Controlled_Buffer controlled_buffer_38
  assign controlled_buffer_39_out = dcd_1_o37 ? dcd_1_o37 : 1'bz;  // Controlled_Buffer controlled_buffer_39
  assign controlled_buffer_40_out = dcd_1_o38 ? dcd_1_o38 : 1'bz;  // Controlled_Buffer controlled_buffer_40
  assign controlled_buffer_41_out = dcd_1_o39 ? dcd_1_o39 : 1'bz;  // Controlled_Buffer controlled_buffer_41
  assign controlled_buffer_42_out = dcd_1_o40 ? dcd_1_o40 : 1'bz;  // Controlled_Buffer controlled_buffer_42
  assign controlled_buffer_43_out = dcd_1_o41 ? dcd_1_o41 : 1'bz;  // Controlled_Buffer controlled_buffer_43
  assign controlled_buffer_44_out = dcd_1_o42 ? dcd_1_o42 : 1'bz;  // Controlled_Buffer controlled_buffer_44
  assign controlled_buffer_45_out = dcd_1_o43 ? dcd_1_o43 : 1'bz;  // Controlled_Buffer controlled_buffer_45
  assign controlled_buffer_46_out = dcd_1_o44 ? dcd_1_o44 : 1'bz;  // Controlled_Buffer controlled_buffer_46
  assign controlled_buffer_47_out = dcd_1_o45 ? dcd_1_o45 : 1'bz;  // Controlled_Buffer controlled_buffer_47
  assign controlled_buffer_48_out = dcd_1_o46 ? dcd_1_o46 : 1'bz;  // Controlled_Buffer controlled_buffer_48
  assign controlled_buffer_49_out = dcd_1_o47 ? dcd_1_o47 : 1'bz;  // Controlled_Buffer controlled_buffer_49
  assign controlled_buffer_50_out = dcd_1_o48 ? dcd_1_o48 : 1'bz;  // Controlled_Buffer controlled_buffer_50
  assign controlled_buffer_51_out = dcd_1_o49 ? dcd_1_o49 : 1'bz;  // Controlled_Buffer controlled_buffer_51
  assign controlled_buffer_52_out = dcd_1_o50 ? dcd_1_o50 : 1'bz;  // Controlled_Buffer controlled_buffer_52
  assign controlled_buffer_53_out = dcd_1_o51 ? dcd_1_o51 : 1'bz;  // Controlled_Buffer controlled_buffer_53
  assign controlled_buffer_54_out = dcd_1_o52 ? dcd_1_o52 : 1'bz;  // Controlled_Buffer controlled_buffer_54
  assign controlled_buffer_55_out = dcd_1_o53 ? dcd_1_o53 : 1'bz;  // Controlled_Buffer controlled_buffer_55
  assign controlled_buffer_56_out = dcd_1_o54 ? dcd_1_o54 : 1'bz;  // Controlled_Buffer controlled_buffer_56
  assign controlled_buffer_57_out = dcd_1_o55 ? dcd_1_o55 : 1'bz;  // Controlled_Buffer controlled_buffer_57
  assign controlled_buffer_58_out = dcd_1_o56 ? dcd_1_o56 : 1'bz;  // Controlled_Buffer controlled_buffer_58
  assign controlled_buffer_59_out = dcd_1_o57 ? dcd_1_o57 : 1'bz;  // Controlled_Buffer controlled_buffer_59
  assign controlled_buffer_60_out = dcd_1_o58 ? dcd_1_o58 : 1'bz;  // Controlled_Buffer controlled_buffer_60
  assign controlled_buffer_61_out = dcd_1_o59 ? dcd_1_o59 : 1'bz;  // Controlled_Buffer controlled_buffer_61
  assign controlled_buffer_62_out = dcd_1_o60 ? dcd_1_o60 : 1'bz;  // Controlled_Buffer controlled_buffer_62
  assign controlled_buffer_63_out = dcd_1_o61 ? dcd_1_o61 : 1'bz;  // Controlled_Buffer controlled_buffer_63
  assign controlled_buffer_64_out = dcd_1_o62 ? dcd_1_o62 : 1'bz;  // Controlled_Buffer controlled_buffer_64
  assign {controlled_buffer_65_out, HALT, NOP, EOI} = EXEC ? rom_3_data : 30'bz;  // Controlled_Buffer controlled_buffer_65
  Pull_Resistor pull_resistor_36 (.node(controlled_buffer_64_out));
  Pull_Resistor pull_resistor_37 (.node(controlled_buffer_63_out));
  DCD_JMP dcd_jmp_1 (.JUMP(JUMP), .JZ(JZ), .ZERO(ZERO), .J_OUT(dcd_jmp_1_j_out));
  LED led_115 (.in(mem_1_always_out[6]));
  LED led_116 (.in(mem_1_always_out[5]));
  LED led_117 (.in(mem_1_always_out[4]));
  LED led_118 (.in(mem_1_always_out[3]));
  _7_Segment_Display u_7_segment_display_3 ();  // open: g, f, a, b, e, d, c, dp
  _7_Segment_Display u_7_segment_display_4 ();  // open: g, f, a, b, e, d, c, dp
  // BCD_to_7_Segment_decoder bcd_to_7_segment_decoder_3: pin names not known
  // BCD_to_7_Segment_decoder bcd_to_7_segment_decoder_4: pin names not known
  LED led_119 (.in(controlled_buffer_62_out));
  LED led_120 (.in(controlled_buffer_61_out));
  LED led_121 (.in(controlled_buffer_60_out));
  LED led_122 (.in(controlled_buffer_59_out));
  Pull_Resistor pull_resistor_38 (.node(controlled_buffer_62_out));
  Pull_Resistor pull_resistor_39 (.node(controlled_buffer_61_out));
  Pull_Resistor pull_resistor_40 (.node(controlled_buffer_60_out));
  Pull_Resistor pull_resistor_41 (.node(controlled_buffer_59_out));
  LED led_123 (.in(mem_1_always_out[2]));
  LED led_124 (.in(mem_1_always_out[1]));
  LED led_125 (.in(mem_1_always_out[0]));
  LED led_126 (.in(controlled_buffer_58_out));
  LED led_127 (.in(controlled_buffer_57_out));
  LED led_128 (.in(controlled_buffer_56_out));
  LED led_129 (.in(controlled_buffer_55_out));
  Pull_Resistor pull_resistor_42 (.node(controlled_buffer_58_out));
  Pull_Resistor pull_resistor_43 (.node(controlled_buffer_57_out));
  Pull_Resistor pull_resistor_44 (.node(controlled_buffer_56_out));
  Pull_Resistor pull_resistor_45 (.node(controlled_buffer_55_out));
  ZR zr_1 (.DATA_IN(alu2_1_always_out), .ZERO(zr_1_zero));
  FLAGS flags_1 (
    .CARRY(alu2_1_cout), .ZERO(zr_1_zero), .STORE(FLAGS_IN), .CLOCK(clk_1_clk_out), .RESET(RESET),
    .CARRY_OUT(COUT), .ZERO_OUT(ZERO));
  LED led_130 (.in(controlled_buffer_54_out));
  LED led_131 (.in(controlled_buffer_53_out));
  LED led_132 (.in(controlled_buffer_52_out));
  LED led_133 (.in(controlled_buffer_51_out));
  Pull_Resistor pull_resistor_46 (.node(controlled_buffer_54_out));
  Pull_Resistor pull_resistor_47 (.node(controlled_buffer_53_out));
  Pull_Resistor pull_resistor_48 (.node(controlled_buffer_52_out));
  Pull_Resistor pull_resistor_49 (.node(controlled_buffer_51_out));
  LED led_134 (.in(COUT));
  LED led_135 (.in(ZERO));
  LED led_136 (.in(controlled_buffer_50_out));
  LED led_137 (.in(controlled_buffer_49_out));
  LED led_138 (.in(controlled_buffer_48_out));
  LED led_139 (.in(controlled_buffer_47_out));
  Pull_Resistor pull_resistor_50 (.node(controlled_buffer_50_out));
  Pull_Resistor pull_resistor_51 (.node(controlled_buffer_49_out));
  Pull_Resistor pull_resistor_52 (.node(controlled_buffer_48_out));
  Pull_Resistor pull_resistor_53 (.node(controlled_buffer_47_out));
  LED led_140 (.in(controlled_buffer_46_out));
  LED led_141 (.in(controlled_buffer_45_out));
  LED led_142 (.in(controlled_buffer_44_out));
  LED led_143 (.in(controlled_buffer_43_out));
  Pull_Resistor pull_resistor_54 (.node(controlled_buffer_46_out));
  Pull_Resistor pull_resistor_55 (.node(controlled_buffer_45_out));
  Pull_Resistor pull_resistor_56 (.node(controlled_buffer_44_out));
  Pull_Resistor pull_resistor_57 (.node(controlled_buffer_43_out));
  LED led_144 (.in(controlled_buffer_42_out));
  LED led_145 (.in(controlled_buffer_41_out));
  LED led_146 (.in(controlled_buffer_40_out));
  LED led_147 (.in(controlled_buffer_39_out));
  Pull_Resistor pull_resistor_58 (.node(controlled_buffer_42_out));
  Pull_Resistor pull_resistor_59 (.node(controlled_buffer_41_out));
  Pull_Resistor pull_resistor_60 (.node(controlled_buffer_40_out));
  Pull_Resistor pull_resistor_61 (.node(controlled_buffer_39_out));
  LED led_148 (.in(controlled_buffer_38_out));
  LED led_149 (.in(controlled_buffer_37_out));
  LED led_150 (.in(controlled_buffer_36_out));
  LED led_151 (.in(controlled_buffer_35_out));
  Pull_Resistor pull_resistor_62 (.node(controlled_buffer_38_out));
  Pull_Resistor pull_resistor_63 (.node(controlled_buffer_37_out));
  Pull_Resistor pull_resistor_64 (.node(controlled_buffer_36_out));
  Pull_Resistor pull_resistor_65 (.node(controlled_buffer_35_out));
  LED led_152 (.in(controlled_buffer_34_out));
  LED led_153 (.in(controlled_buffer_33_out));
  LED led_154 (.in(controlled_buffer_32_out));
  LED led_155 (.in(controlled_buffer_31_out));
  Pull_Resistor pull_resistor_66 (.node(controlled_buffer_34_out));
  Pull_Resistor pull_resistor_67 (.node(controlled_buffer_33_out));
  Pull_Resistor pull_resistor_68 (.node(controlled_buffer_32_out));
  Pull_Resistor pull_resistor_69 (.node(controlled_buffer_31_out));
  LED led_156 (.in(controlled_buffer_30_out));
  LED led_157 (.in(controlled_buffer_29_out));
  LED led_158 (.in(controlled_buffer_28_out));
  LED led_159 (.in(controlled_buffer_27_out));
  Pull_Resistor pull_resistor_70 (.node(controlled_buffer_30_out));
  Pull_Resistor pull_resistor_71 (.node(controlled_buffer_29_out));
  Pull_Resistor pull_resistor_72 (.node(controlled_buffer_28_out));
  Pull_Resistor pull_resistor_73 (.node(controlled_buffer_27_out));
  LED led_160 (.in(controlled_buffer_26_out));
  LED led_161 (.in(controlled_buffer_25_out));
  LED led_162 (.in(controlled_buffer_24_out));
  LED led_163 (.in(controlled_buffer_23_out));
  Pull_Resistor pull_resistor_74 (.node(controlled_buffer_26_out));
  Pull_Resistor pull_resistor_75 (.node(controlled_buffer_25_out));
  Pull_Resistor pull_resistor_76 (.node(controlled_buffer_24_out));
  Pull_Resistor pull_resistor_77 (.node(controlled_buffer_23_out));
  LED led_164 (.in(controlled_buffer_22_out));
  LED led_165 (.in(controlled_buffer_21_out));
  LED led_166 (.in(controlled_buffer_20_out));
  LED led_167 (.in(pull_resistor_81_node));
  Pull_Resistor pull_resistor_78 (.node(controlled_buffer_22_out));
  Pull_Resistor pull_resistor_79 (.node(controlled_buffer_21_out));
  Pull_Resistor pull_resistor_80 (.node(controlled_buffer_20_out));
  Pull_Resistor pull_resistor_81 (.node(pull_resistor_81_node));
  LED led_168 (.in(controlled_buffer_18_out));
  LED led_169 (.in(controlled_buffer_17_out));
  LED led_170 (.in(controlled_buffer_16_out));
  LED led_171 (.in(controlled_buffer_15_out));
  Pull_Resistor pull_resistor_82 (.node(controlled_buffer_18_out));
  Pull_Resistor pull_resistor_83 (.node(controlled_buffer_17_out));
  Pull_Resistor pull_resistor_84 (.node(controlled_buffer_16_out));
  Pull_Resistor pull_resistor_85 (.node(controlled_buffer_15_out));
  LED led_172 (.in(controlled_buffer_14_out));
  LED led_173 (.in(controlled_buffer_13_out));
  LED led_174 (.in(controlled_buffer_12_out));
  LED led_175 (.in(controlled_buffer_11_out));
  Pull_Resistor pull_resistor_86 (.node(controlled_buffer_14_out));
  Pull_Resistor pull_resistor_87 (.node(controlled_buffer_13_out));
  Pull_Resistor pull_resistor_88 (.node(controlled_buffer_12_out));
  Pull_Resistor pull_resistor_89 (.node(controlled_buffer_11_out));
  LED led_176 (.in(controlled_buffer_10_out));
  LED led_177 (.in(controlled_buffer_9_out));
  LED led_178 (.in(controlled_buffer_8_out));
  LED led_179 (.in(controlled_buffer_7_out));
  Pull_Resistor pull_resistor_90 (.node(controlled_buffer_10_out));
  Pull_Resistor pull_resistor_91 (.node(controlled_buffer_9_out));
  Pull_Resistor pull_resistor_92 (.node(controlled_buffer_8_out));
  Pull_Resistor pull_resistor_93 (.node(controlled_buffer_7_out));
  LED led_180 (.in(controlled_buffer_6_out));
  LED led_181 (.in(controlled_buffer_5_out));
  LED led_182 (.in(controlled_buffer_4_out));
  LED led_183 (.in(controlled_buffer_3_out));
  Pull_Resistor pull_resistor_94 (.node(controlled_buffer_6_out));
  Pull_Resistor pull_resistor_95 (.node(controlled_buffer_5_out));
  Pull_Resistor pull_resistor_96 (.node(controlled_buffer_4_out));
  Pull_Resistor pull_resistor_97 (.node(controlled_buffer_3_out));
  ALU_OPS alu_ops_1 (
    .ADD1(controlled_buffer_9_out), .SUB1(controlled_buffer_10_out), .MUL1(controlled_buffer_11_out),
    .DIV1(controlled_buffer_12_out), .SUB2(controlled_buffer_14_out), .DIV2(controlled_buffer_13_out),
    .OP_OUT(alu_ops_1_op_out));  // open: ADD2, MUL2
  BHI bhi_1 (
    .in_1(controlled_buffer_4_out), .in_2(controlled_buffer_5_out), .in_3(controlled_buffer_6_out),
    .in_4(controlled_buffer_7_out), .in_5(controlled_buffer_8_out), .FLAG_OUT(HAS_IMM));  // open: in_6, in_7, in_8, in_9, in_10
  LED led_184 (.in(controlled_buffer_65_out[27]));
  LED led_185 (.in(controlled_buffer_65_out[26]));
  LED led_186 (.in(controlled_buffer_65_out[25]));
  LED led_187 (.in(controlled_buffer_65_out[24]));
  LED led_188 (.in(controlled_buffer_65_out[23]));
  LED led_189 (.in(controlled_buffer_65_out[22]));
  LED led_190 (.in(controlled_buffer_65_out[21]));
  LED led_191 (.in(controlled_buffer_65_out[20]));
  LED led_192 (.in(controlled_buffer_65_out[19]));
  LED led_193 (.in(controlled_buffer_65_out[18]));
  LED led_194 (.in(controlled_buffer_65_out[17]));
  LED led_195 (.in(controlled_buffer_65_out[16]));
  LED led_196 (.in(controlled_buffer_65_out[15]));
  LED led_197 (.in(controlled_buffer_65_out[14]));
  LED led_198 (.in(controlled_buffer_65_out[13]));
  LED led_199 (.in(controlled_buffer_65_out[12]));
  LED led_200 (.in(controlled_buffer_65_out[11]));
  LED led_201 (.in(controlled_buffer_65_out[10]));
  LED led_202 (.in(controlled_buffer_65_out[9]));
  LED led_203 (.in(controlled_buffer_65_out[8]));
  LED led_204 (.in(controlled_buffer_65_out[7]));
  LED led_205 (.in(controlled_buffer_65_out[6]));
  LED led_206 (.in(controlled_buffer_65_out[5]));
  LED led_207 (.in(controlled_buffer_65_out[4]));
  LED led_208 (.in(controlled_buffer_65_out[3]));
  LED led_209 (.in(HALT));
  LED led_210 (.in(NOP));
  LED led_211 (.in(EOI));
  DCD_CTRL dcd_ctrl_1 (.I5(controlled_buffer_65_out[3]), .O0(RAM_OUT));  // open: I4, l3, I2, I1, I0
  DCD_CTRL dcd_ctrl_2 (.I5(controlled_buffer_65_out[4]), .O0(RF_IN));  // open: I4, l3, I2, I1, I0
  DCD_CTRL dcd_ctrl_3 (.I5(controlled_buffer_65_out[5]), .O0(IMR_OUT));  // open: I4, l3, I2, I1, I0
  DCD_CTRL dcd_ctrl_4 (.I5(controlled_buffer_65_out[6]), .O0(OUTPUT_REG_IN));  // open: I4, l3, I2, I1, I0
  DCD_CTRL dcd_ctrl_5 (.I5(controlled_buffer_65_out[7]), .O0(RAM_IN));  // open: I4, l3, I2, I1, I0
  DCD_CTRL dcd_ctrl_6 (.I5(controlled_buffer_65_out[8]), .O0(RF_A_OUT));  // open: I4, l3, I2, I1, I0
  DCD_CTRL dcd_ctrl_7 (.I5(controlled_buffer_65_out[9]), .O0(MAR_OUT));  // open: I4, l3, I2, I1, I0
  DCD_CTRL dcd_ctrl_8 (.I5(controlled_buffer_65_out[10]), .O0(OPR_OUT));  // open: I4, l3, I2, I1, I0
  DCD_CTRL dcd_ctrl_9 (.I5(controlled_buffer_65_out[11]), .O0(JUMP));  // open: I4, l3, I2, I1, I0
  DCD_CTRL dcd_ctrl_10 (.I5(controlled_buffer_65_out[12]), .O0(FLAGS_IN));  // open: I4, l3, I2, I1, I0
  DCD_CTRL dcd_ctrl_11 (.I5(controlled_buffer_65_out[13]), .O0(ALU_OUT));  // open: I4, l3, I2, I1, I0
  DCD_CTRL dcd_ctrl_12 (.I5(controlled_buffer_65_out[14]), .O0(RF_INTERNAL_OP));  // open: I4, l3, I2, I1, I0
  DCD_CTRL dcd_ctrl_13 (.I5(controlled_buffer_65_out[15]), .O0(JZ));  // open: I4, l3, I2, I1, I0
  DCD_CTRL dcd_ctrl_14 (.I5(controlled_buffer_65_out[16]), .O0(IMR_RF_OUT));  // open: I4, l3, I2, I1, I0
  DCD_CTRL dcd_ctrl_15 (.I5(controlled_buffer_65_out[17]), .O0(CROSS_BUS1));  // open: I4, l3, I2, I1, I0
  DCD_CTRL dcd_ctrl_16 (.I5(controlled_buffer_65_out[18]), .O0(RF_B_ENB));  // open: I4, l3, I2, I1, I0
  DCD_CTRL dcd_ctrl_17 (.I5(controlled_buffer_65_out[19]), .O0(RF_B_ALU_OUT));  // open: I4, l3, I2, I1, I0
  DCD_CTRL dcd_ctrl_18 (.I5(controlled_buffer_65_out[20]), .O0(RF_A_ALU_OUT));  // open: I4, l3, I2, I1, I0
  DCD_CTRL dcd_ctrl_19 (.I5(controlled_buffer_65_out[21]), .O0(REM_ENB));  // open: I4, l3, I2, I1, I0
  DCD_CTRL dcd_ctrl_20 (.I5(controlled_buffer_65_out[22]), .O0(OP_MAR_IN));  // open: I4, l3, I2, I1, I0
  DCD_CTRL dcd_ctrl_21 (.I5(controlled_buffer_65_out[23]), .O0(RF_B_OUT));  // open: I4, l3, I2, I1, I0
  DCD_CTRL dcd_ctrl_22 (.I5(controlled_buffer_65_out[24]), .O0(OP_IMR_IN));  // open: I4, l3, I2, I1, I0
  DCD_CTRL dcd_ctrl_23 (.I5(controlled_buffer_65_out[25]), .O0(OP_ROM_OUT));  // open: I4, l3, I2, I1, I0
  DCD_CTRL dcd_ctrl_24 (.I5(controlled_buffer_65_out[26]), .O0(OP_COUNTER_ENB));  // open: I4, l3, I2, I1, I0
  DCD_CTRL dcd_ctrl_25 (.I5(controlled_buffer_65_out[27]), .O0(CROSS_BUS2));  // open: I4, l3, I2, I1, I0

  // Notes on the sheet:
  //   T0
  //   T1
  //   T2
  //   contents of rom_1 (hex, n*v repeats v):
  //   1401 1441 1040 c00 1c40 1802 400
  //   contents of rom_2 (hex, n*v repeats v):
  //   3a9 16 40
  //   PROGRAM CODE
  //   MICROCODE
  //   data bus
  //   adress bus
  //   contents of rom_3 (hex, n*v repeats v):
  //   5 0 0 0 6420000 619 0 0 6420000 249 0 0 6420000 781 0 0 7000000 431 0 0 6420000 a01 0 0 1d2411 0 0 0
  //   1d2411 0 0 0 1d2411 0 0 0 1d2411 0 0 0 3d2411 0 0 0 1d1401 0 0 0 6420000 8201 0 0 8c50000 781 0 0
  //   8c50000 619 0 0 854411 0 0 0 1 0 0 0 1 0 0 0 1 0 0 0 1 0 0 0 1 0 0 0 1 0 0 0 1 0 0 0 1 0 0 0 1 0 0 0
  //   1 0 0 0 1 0 0 0 1 0 0 0 1 0 0 0 1 0 0 0 1 0 0 0 1 0 0 0 1 0 0 0 1 0 0 0 1 0 0 0 1 0 0 0 1 0 0 0 1 0
  //   0 0 1 0 0 0 1 0 0 0 1 0 0 0 1 0 0 0 1 0 0 0 1 0 0 0 1 0 0 0 1 0 0 0 1 0 0 0 1 0 0 0 1 0 0 0 1 0 0 0
  //   1 0 0 0 1 0 0 0 1 0 0 0 1 0 0 0 1 0 0 0 1 0 0 0 1 0 0 0 1 0 0 0 1 0 0 0 1 0 0 0 1 0 0 0 1 0 0 0 1 0
  //   0 0 1
  //   T2-a
  //   T2-b
  //   T2-c
  //   T2-d
  //   counter++
endmodule
