// Logisim project main.circ as structural Verilog: 21 circuits, main circuit CLK
module V1 (
  input  [7:0] in_1,
  input  in_2,
  input  in_3,
  input  input_to_bus,
  input  bus_to_reg,
  input  reg_to_bus,
  input  reset_all__regs,
  input  bus_to_ram,
  input  ram_to_bus,
  input  [1:0] in_10,
  input  [1:0] in_11,
  input  instruction_mode,
  input  reset_pc,
  input  in_14,
  output [7:0] DATA_BUS
);

  wire clk_1_p4, clk_1_p5, clock_1_out, controlled_buffer_3_out, demultiplexer_1_out1, demultiplexer_1_out2,
       demultiplexer_1_out3;
  wire [7:0] A_q, B_q, C_q, controlled_buffer_1_out, controlled_buffer_6_out, D_q, demultiplexer_1_out0,
       demultiplexer_2_out0, demultiplexer_2_out2, multiplexer_1_out, PC_q, ram_1_dout, undriven;

  Clock clock_1 (.out(clock_1_out));
  // CLK clk_1: pin names not known; wires that end beside it: clock_1_out, in_2, in_3, clk_1_p4, clk_1_p5
  Register PC (.D(undriven), .clk(in_14), .Q(PC_q), .clr(reset_pc));  // open: en
  Register A (.D(demultiplexer_2_out0), .en(demultiplexer_1_out0[0]), .clk(clk_1_p5), .Q(A_q), .clr(reset_all__regs));
  Register B (.D(demultiplexer_1_out0), .en(demultiplexer_1_out1), .clk(clk_1_p5), .Q(B_q), .clr(reset_all__regs));
  Register C (.D(demultiplexer_2_out2), .en(demultiplexer_1_out2), .clk(clk_1_p5), .Q(C_q), .clr(reset_all__regs));
  Register D (.D(demultiplexer_1_out0), .en(demultiplexer_1_out3), .clk(clk_1_p5), .Q(D_q), .clr(reset_all__regs));
  Demultiplexer #(.select(2)) demultiplexer_1 (
    .out0(demultiplexer_1_out0[0]), .out1(demultiplexer_1_out1), .out2(demultiplexer_1_out2),
    .out3(demultiplexer_1_out3), .in(bus_to_reg), .sel(in_11));
  assign controlled_buffer_1_out = bus_to_reg ? DATA_BUS : 8'bz;  // Controlled_Buffer controlled_buffer_1
  Demultiplexer #(.select(2), .width(8)) demultiplexer_2 (
    .out0(demultiplexer_2_out0), .out1(demultiplexer_1_out0), .out2(demultiplexer_2_out2),
    .out3(demultiplexer_1_out0), .in(controlled_buffer_1_out), .sel(in_11));
  assign DATA_BUS = reg_to_bus ? multiplexer_1_out : 8'bz;  // Controlled_Buffer controlled_buffer_2
  Multiplexer #(.select(2), .width(8)) multiplexer_1 (
    .in0(A_q), .in1(B_q), .in2(C_q), .in3(D_q), .out(multiplexer_1_out), .sel(in_10));
  RAM ram_1 (
    .addr(PC_q), .we(bus_to_ram), .oe(ram_to_bus), .clk(controlled_buffer_3_out),
    .din(controlled_buffer_6_out), .dout(ram_1_dout));
  assign controlled_buffer_3_out = bus_to_ram ? clk_1_p5 : 1'bz;  // Controlled_Buffer controlled_buffer_3
  assign controlled_buffer_3_out = ram_to_bus ? clk_1_p5 : 1'bz;  // Controlled_Buffer controlled_buffer_4
  assign DATA_BUS = ram_to_bus ? ram_1_dout : 8'bz;  // Controlled_Buffer controlled_buffer_5
  assign controlled_buffer_6_out = bus_to_ram ? DATA_BUS : 8'bz;  // Controlled_Buffer controlled_buffer_6
  assign clk_1_p4 = ram_to_bus ? instruction_mode : 1'bz;  // Controlled_Buffer controlled_buffer_7
  assign DATA_BUS = input_to_bus ? in_1 : 8'bz;  // Controlled_Buffer controlled_buffer_8
  // Pins of 1 and 8 bits meet at demultiplexer_1_out0

  // Notes on the sheet:
  //   GPR REGISTERS
  //   alterna o WE pra input
  //   alterna o reg do input
  //   alterna o reg do output
  //   TODO: STORE mem, R1/R2/R3/R4
  //   instruction mode is on only if ram to bus is on
  //   input
  //   reg output selector
  //   reg input selector
endmodule

module V2 (
  input  [1:0] in_1,
  input  [1:0] in_2,
  input  reset_pc,
  input  halt,
  input  input_to_dbus,
  input  [7:0] in_6,
  input  pc_to_pbus,
  input  in_8,
  input  pbus_to_ram,
  input  dbus_to_ram,
  input  ram_to_ibus,
  input  dbus_to_reg,
  input  reg_to_dbus,
  input  reset_GPR,
  output [2:0] instruction_bus,
  output [7:0] data_bus,
  output [7:0] pc_bus
);

  wire clk_1_clk_out, demultiplexer_1_out0, demultiplexer_1_out1, demultiplexer_1_out2, demultiplexer_1_out3;
  wire [7:0] controlled_buffer_1_out, controlled_buffer_2_out, controlled_buffer_4_out,
       controlled_buffer_7_out, demultiplexer_2_out0, demultiplexer_2_out1, demultiplexer_2_out2,
       demultiplexer_2_out3, multiplexer_1_out, R0_q, R1_q, R3_q, ram_1_dout;
  wire [7:1] pc_1_p6;

  Clock clock_1 ();  // open: out
  CLK clk_1 (.CLK_ENB(reset_GPR), .MANUAL_CLK(reset_GPR), .CLK_IN(reset_GPR), .CLK_OUT(clk_1_clk_out));  // open: HALT
  Demultiplexer #(.select(2)) demultiplexer_1 (
    .out0(demultiplexer_1_out0), .out1(demultiplexer_1_out1), .out2(demultiplexer_1_out2),
    .out3(demultiplexer_1_out3), .in(dbus_to_reg), .sel(in_2));
  Demultiplexer #(.select(2), .width(8)) demultiplexer_2 (
    .out0(demultiplexer_2_out0), .out1(demultiplexer_2_out1), .out2(demultiplexer_2_out2),
    .out3(demultiplexer_2_out3), .in(controlled_buffer_1_out), .sel(in_2));
  // PC pc_1: pin names not known; wires that end beside it: halt, reset_GPR, reset_GPR, clk_1_clk_out, reset_pc, {pc_1_p6, dbus_to_ram}
  Register R0 (.D(demultiplexer_2_out0), .en(demultiplexer_1_out0), .clk(clk_1_clk_out), .Q(R0_q), .clr(reset_GPR));
  Register R1 (.D(demultiplexer_2_out1), .en(demultiplexer_1_out1), .clk(clk_1_clk_out), .Q(R1_q), .clr(reset_GPR));
  Register R2 (
    .D(demultiplexer_2_out2), .en(demultiplexer_1_out2), .clk(clk_1_clk_out), .Q({pc_1_p6, dbus_to_ram}),
    .clr(reset_GPR));
  Register R3 (.D(demultiplexer_2_out3), .en(demultiplexer_1_out3), .clk(clk_1_clk_out), .Q(R3_q), .clr(reset_GPR));
  assign controlled_buffer_1_out = dbus_to_reg ? data_bus : 8'bz;  // Controlled_Buffer controlled_buffer_1
  assign controlled_buffer_2_out = dbus_to_ram ? {pc_1_p6, dbus_to_ram} : 8'bz;  // Controlled_Buffer controlled_buffer_2
  RAM ram_1 (
    .addr(controlled_buffer_2_out), .we(dbus_to_ram), .oe(ram_to_ibus), .clk(clk_1_clk_out),
    .din(controlled_buffer_4_out), .dout(ram_1_dout));
  assign data_bus = reg_to_dbus ? multiplexer_1_out : 8'bz;  // Controlled_Buffer controlled_buffer_3
  assign controlled_buffer_4_out = dbus_to_ram ? data_bus : 8'bz;  // Controlled_Buffer controlled_buffer_4
  assign data_bus = input_to_dbus ? in_6 : 8'bz;  // Controlled_Buffer controlled_buffer_5
  Bit_Extender #(.out_width(3)) bit_extender_1 (.in(controlled_buffer_7_out), .out(instruction_bus));
  assign {pc_1_p6, dbus_to_ram} = pc_bus;  // Buffer buffer_1, 8 bits wide
  Multiplexer #(.select(2), .width(8)) multiplexer_1 (
    .in0(R0_q), .in1(R1_q), .in2(R3_q), .in3({pc_1_p6, dbus_to_ram}), .out(multiplexer_1_out), .sel(in_1));
  assign pc_bus = pc_to_pbus ? {pc_1_p6, dbus_to_ram} : 8'bz;  // Controlled_Buffer controlled_buffer_6
  assign controlled_buffer_7_out = ram_to_ibus ? ram_1_dout : 8'bz;  // Controlled_Buffer controlled_buffer_7
  ALU alu_1 ();  // open: A_IN, B_IN, OUTPUT_ENB, SUB, ALWAYS_OUT, A_OUT, COUT
  DCD dcd_1 ();  // open: DCD_FLUSH, SELECTOR, ENB, EXEC, O8, O9, O10, O11, O12, O13, O14, O15, O0, O1, O2, O3, O4, O5, O6, O7
  // Pins of 1 and 8 bits meet at {pc_1_p6, dbus_to_ram}

  assign pbus_to_ram = dbus_to_ram;

  // Notes on the sheet:
  //   output register selector
  //   input register selector
  //   input
endmodule

module V3 (
  input  in_1,
  input  in_2,
  input  in_3,
  input  [7:0] in_4,
  input  input_to_bus,
  input  [1:0] in_6,
  input  [7:0] in_7,
  input  input_to_bus_2,
  input  bus_to_reg,
  input  bus_to_ram,
  input  ram_to_bus,
  input  reg_to_bus,
  input  pc_to_pbus,
  input  in_14,
  input  reset_all_GPR,
  output [7:0] pc_bus,
  output [7:0] data_bus
);

  wire clock_1_out, dcd_1_p3, demultiplexer_1_out0, demultiplexer_1_out1, demultiplexer_1_out2,
       demultiplexer_1_out3, undriven;
  wire [1:0] buffer_1_out;
  wire [2:0] bit_extender_1_out;
  wire [7:0] buffer_3_out, buffer_5_out, controlled_buffer_4_out, controlled_buffer_6_out,
       controlled_buffer_7_out, demultiplexer_2_out0, demultiplexer_2_out1, demultiplexer_2_out2,
       demultiplexer_2_out3, multiplexer_1_out, pc_1_p1, R0_q, R1_q, R2_q, R3_q, ram_1_dout;

  Clock clock_1 (.out(clock_1_out));
  CLK clk_1 (.HALT(in_3), .CLK_ENB(in_1), .CLK_IN(clock_1_out));  // open: MANUAL_CLK, CLK_OUT
  // PC pc_1: pin names not known; wires that end beside it: pc_1_p1
  assign buffer_1_out = in_6;  // Buffer buffer_1, 2 bits wide
  Demultiplexer #(.select(2)) demultiplexer_1 (
    .out0(demultiplexer_1_out0), .out1(demultiplexer_1_out1), .out2(demultiplexer_1_out2),
    .out3(demultiplexer_1_out3), .in(bus_to_reg), .sel(buffer_1_out));
  Demultiplexer #(.select(2), .width(8)) demultiplexer_2 (
    .out0(demultiplexer_2_out0), .out1(demultiplexer_2_out1), .out2(demultiplexer_2_out2),
    .out3(demultiplexer_2_out3), .in(pc_bus), .sel(buffer_1_out));
  Register R0 (.D(demultiplexer_2_out0), .en(demultiplexer_1_out0), .clk(undriven), .Q(R0_q), .clr(reset_all_GPR));
  Register R1 (.D(demultiplexer_2_out1), .en(demultiplexer_1_out1), .clk(undriven), .Q(R1_q), .clr(reset_all_GPR));
  Register R2 (.D(demultiplexer_2_out2), .en(demultiplexer_1_out2), .clk(undriven), .Q(R2_q), .clr(reset_all_GPR));
  Register R3 (.D(demultiplexer_2_out3), .en(demultiplexer_1_out3), .clk(undriven), .Q(R3_q), .clr(reset_all_GPR));
  assign pc_bus = pc_to_pbus ? pc_1_p1 : 8'bz;  // Controlled_Buffer controlled_buffer_1
  assign pc_bus = controlled_buffer_7_out;  // Buffer buffer_2, 8 bits wide
  assign buffer_3_out = pc_bus;  // Buffer buffer_3, 8 bits wide
  // ALU alu_1: pin names not known; wires that end beside it: pc_bus, pc_bus, buffer_3_out
  assign data_bus = ram_to_bus ? ram_1_dout : 8'bz;  // Controlled_Buffer controlled_buffer_2
  assign data_bus = controlled_buffer_4_out;  // Buffer buffer_4, 8 bits wide
  assign pc_bus = bus_to_reg ? controlled_buffer_4_out : 8'bz;  // Controlled_Buffer controlled_buffer_3
  assign controlled_buffer_4_out = reg_to_bus ? multiplexer_1_out : 8'bz;  // Controlled_Buffer controlled_buffer_4
  Multiplexer #(.select(2), .width(8)) multiplexer_1 (
    .in0(R0_q), .in1(R1_q), .in2(R2_q), .in3(R3_q), .out(multiplexer_1_out), .sel(in_6));
  RAM ram_1 (
    .addr(buffer_3_out), .we(bus_to_ram), .oe(ram_to_bus), .clk(reset_all_GPR),
    .din(controlled_buffer_6_out), .dout(ram_1_dout));
  assign controlled_buffer_4_out = input_to_bus ? in_4 : 8'bz;  // Controlled_Buffer controlled_buffer_5
  assign controlled_buffer_6_out = bus_to_ram ? data_bus : 8'bz;  // Controlled_Buffer controlled_buffer_6
  assign buffer_5_out = data_bus;  // Buffer buffer_5, 8 bits wide
  assign controlled_buffer_7_out = input_to_bus_2 ? in_7 : 8'bz;  // Controlled_Buffer controlled_buffer_7
  Bit_Extender #(.out_width(3)) bit_extender_1 (.in(buffer_5_out), .out(bit_extender_1_out));
  // DCD dcd_1: pin names not known; wires that end beside it: bit_extender_1_out, in_14, dcd_1_p3, ram_1_dout, ram_1_dout, ram_1_dout, ram_1_dout, ram_1_dout

  // Notes on the sheet:
  //   input reg selector
  //   A = reg ; B = value?
  //   address
endmodule

module CLK (
  input  CLK_IN,
  input  CLK_ENB,
  input  MANUAL_CLK,
  input  HALT,
  output CLK_OUT
);

  wire and_1_out, and_2_out, not_1_out, not_2_out, or_1_out;

  not not_1 (not_1_out, HALT);
  not not_2 (not_2_out, CLK_ENB);
  and and_1 (and_1_out, CLK_IN, CLK_ENB);
  and and_2 (and_2_out, not_2_out, MANUAL_CLK);
  or or_1 (or_1_out, and_1_out, and_2_out);
  and and_3 (CLK_OUT, or_1_out, not_1_out);
endmodule

module DCD (
  input  DCD_FLUSH,
  input  [3:0] SELECTOR,
  input  ENB,
  input  EXEC,
  output O0,
  output O1,
  output O2,
  output O3,
  output O4,
  output O5,
  output O6,
  output O7,
  output O8,
  output O9,
  output O10,
  output O11,
  output O12,
  output O13,
  output O14,
  output O15
);

  wire decoder_1_out0, decoder_1_out1, decoder_1_out2, decoder_1_out3, decoder_1_out4, decoder_1_out5,
       decoder_1_out6, decoder_1_out7, decoder_1_out8, decoder_1_out9, decoder_1_out10, decoder_1_out11,
       decoder_1_out12, decoder_1_out13, decoder_1_out14, decoder_1_out15, register_1_q, register_2_q,
       register_3_q, register_4_q, register_5_q, register_6_q, register_7_q, register_8_q, register_9_q,
       register_10_q, register_11_q, register_12_q, register_13_q, register_14_q, register_15_q,
       register_16_q;

  Decoder #(.select(4)) decoder_1 (
    .out0(decoder_1_out0), .out1(decoder_1_out1), .out2(decoder_1_out2), .out3(decoder_1_out3),
    .out4(decoder_1_out4), .out5(decoder_1_out5), .out6(decoder_1_out6), .out7(decoder_1_out7),
    .out8(decoder_1_out8), .out9(decoder_1_out9), .out10(decoder_1_out10), .out11(decoder_1_out11),
    .out12(decoder_1_out12), .out13(decoder_1_out13), .out14(decoder_1_out14), .out15(decoder_1_out15),
    .sel(SELECTOR), .en(ENB));
  Register #(.width(1)) register_1 (
    .D(decoder_1_out0), .en(decoder_1_out0), .clk(decoder_1_out0), .Q(register_1_q), .clr(DCD_FLUSH));
  Register #(.width(1)) register_2 (
    .D(decoder_1_out1), .en(decoder_1_out1), .clk(decoder_1_out1), .Q(register_2_q), .clr(DCD_FLUSH));
  Register #(.width(1)) register_3 (
    .D(decoder_1_out2), .en(decoder_1_out2), .clk(decoder_1_out2), .Q(register_3_q), .clr(DCD_FLUSH));
  Register #(.width(1)) register_4 (
    .D(decoder_1_out3), .en(decoder_1_out3), .clk(decoder_1_out3), .Q(register_4_q), .clr(DCD_FLUSH));
  Register #(.width(1)) register_5 (
    .D(decoder_1_out4), .en(decoder_1_out4), .clk(decoder_1_out4), .Q(register_5_q), .clr(DCD_FLUSH));
  Register #(.width(1)) register_6 (
    .D(decoder_1_out5), .en(decoder_1_out5), .clk(decoder_1_out5), .Q(register_6_q), .clr(DCD_FLUSH));
  Register #(.width(1)) register_7 (
    .D(decoder_1_out6), .en(decoder_1_out6), .clk(decoder_1_out6), .Q(register_7_q), .clr(DCD_FLUSH));
  Register #(.width(1)) register_8 (
    .D(decoder_1_out7), .en(decoder_1_out7), .clk(decoder_1_out7), .Q(register_8_q), .clr(DCD_FLUSH));
  Register #(.width(1)) register_9 (
    .D(decoder_1_out8), .en(decoder_1_out8), .clk(decoder_1_out8), .Q(register_9_q), .clr(DCD_FLUSH));
  Register #(.width(1)) register_10 (
    .D(decoder_1_out9), .en(decoder_1_out9), .clk(decoder_1_out9), .Q(register_10_q), .clr(DCD_FLUSH));
  Register #(.width(1)) register_11 (
    .D(decoder_1_out10), .en(decoder_1_out10), .clk(decoder_1_out10), .Q(register_11_q), .clr(DCD_FLUSH));
  Register #(.width(1)) register_12 (
    .D(decoder_1_out11), .en(decoder_1_out11), .clk(decoder_1_out11), .Q(register_12_q), .clr(DCD_FLUSH));
  Register #(.width(1)) register_13 (
    .D(decoder_1_out12), .en(decoder_1_out12), .clk(decoder_1_out12), .Q(register_13_q), .clr(DCD_FLUSH));
  Register #(.width(1)) register_14 (
    .D(decoder_1_out13), .en(decoder_1_out13), .clk(decoder_1_out13), .Q(register_14_q), .clr(DCD_FLUSH));
  Register #(.width(1)) register_15 (
    .D(decoder_1_out14), .en(decoder_1_out14), .clk(decoder_1_out14), .Q(register_15_q), .clr(DCD_FLUSH));
  Register #(.width(1)) register_16 (
    .D(decoder_1_out15), .en(decoder_1_out15), .clk(decoder_1_out15), .Q(register_16_q), .clr(DCD_FLUSH));
  assign O0 = EXEC ? register_1_q : 1'bz;  // Controlled_Buffer controlled_buffer_1
  assign O1 = EXEC ? register_2_q : 1'bz;  // Controlled_Buffer controlled_buffer_2
  assign O2 = EXEC ? register_3_q : 1'bz;  // Controlled_Buffer controlled_buffer_3
  assign O3 = EXEC ? register_4_q : 1'bz;  // Controlled_Buffer controlled_buffer_4
  assign O4 = EXEC ? register_5_q : 1'bz;  // Controlled_Buffer controlled_buffer_5
  assign O5 = EXEC ? register_6_q : 1'bz;  // Controlled_Buffer controlled_buffer_6
  assign O6 = EXEC ? register_7_q : 1'bz;  // Controlled_Buffer controlled_buffer_7
  assign O7 = EXEC ? register_8_q : 1'bz;  // Controlled_Buffer controlled_buffer_8
  assign O8 = EXEC ? register_9_q : 1'bz;  // Controlled_Buffer controlled_buffer_9
  assign O9 = EXEC ? register_10_q : 1'bz;  // Controlled_Buffer controlled_buffer_10
  assign O10 = EXEC ? register_11_q : 1'bz;  // Controlled_Buffer controlled_buffer_11
  assign O11 = EXEC ? register_12_q : 1'bz;  // Controlled_Buffer controlled_buffer_12
  assign O12 = EXEC ? register_13_q : 1'bz;  // Controlled_Buffer controlled_buffer_13
  assign O13 = EXEC ? register_14_q : 1'bz;  // Controlled_Buffer controlled_buffer_14
  assign O14 = EXEC ? register_15_q : 1'bz;  // Controlled_Buffer controlled_buffer_15
  assign O15 = EXEC ? register_16_q : 1'bz;  // Controlled_Buffer controlled_buffer_16
endmodule

module PC (
  input  RESET,
  input  JUMP,
  input  COUNTER_ENB,
  input  CLOCK,
  input  [3:0] ADDR_IN,
  input  COUNTER_OUT,
  output [3:0] ALWAYS_OUT,
  output [3:0] ADDR_OUT
);

  Counter #(.max('hf), .width(4)) counter_1 (
    .clr(RESET), .load(JUMP), .up(COUNTER_ENB), .count(COUNTER_ENB), .clk(CLOCK), .D(ADDR_IN), .Q(ALWAYS_OUT));  // open: carry
  assign ADDR_OUT = COUNTER_OUT ? ALWAYS_OUT : 4'bz;  // Controlled_Buffer controlled_buffer_1
endmodule

module ALU (
  input  [7:0] A_IN,
  input  [7:0] B_IN,
  input  OUTPUT_ENB,
  input  SUB,
  output [7:0] ALWAYS_OUT,
  output [7:0] A_OUT,
  output COUT
);

  wire not_1_out;
  wire [7:0] controlled_buffer_1_out, xor_1_out;

  assign controlled_buffer_1_out = SUB ? {8{1'b1}} : 8'bz;  // Controlled_Buffer controlled_buffer_1
  not not_1 (not_1_out, SUB);
  assign controlled_buffer_1_out = not_1_out ? {8{1'b0}} : 8'bz;  // Controlled_Buffer controlled_buffer_2
  assign xor_1_out = B_IN ^ controlled_buffer_1_out;  // XOR_Gate xor_1, 8 bits wide
  Adder adder_1 (.a(A_IN), .b(xor_1_out), .out(ALWAYS_OUT), .cin(SUB), .cout(COUT));
  assign A_OUT = OUTPUT_ENB ? ALWAYS_OUT : 8'bz;  // Controlled_Buffer controlled_buffer_3
endmodule

module R0 (
  input  [7:0] DATA_IN,
  input  A_IN,
  input  A_OUT,
  input  CLOCK,
  input  A_RESET,
  output [7:0] ALWAYS_OUT,
  output [7:0] DATA_OUT
);

  Register register_1 (.D(DATA_IN), .en(A_IN), .clk(CLOCK), .Q(ALWAYS_OUT), .clr(A_RESET));
  assign DATA_OUT = A_OUT ? ALWAYS_OUT : 8'bz;  // Controlled_Buffer controlled_buffer_1
endmodule

module R1 (
  input  [7:0] DATA_IN,
  input  B_IN,
  input  B_OUT,
  input  CLOCK,
  input  B_RESET,
  output [7:0] ALWAYS_OUT,
  output [7:0] DATA_OUT
);

  Register register_1 (.D(DATA_IN), .en(B_IN), .clk(CLOCK), .Q(ALWAYS_OUT), .clr(B_RESET));
  assign DATA_OUT = B_OUT ? ALWAYS_OUT : 8'bz;  // Controlled_Buffer controlled_buffer_1
endmodule

module I_REG (
  input  [7:0] DATA_IN,
  input  STORE,
  input  CLOCK,
  input  RESET,
  input  DATA_OUT_ENB,
  output [7:0] ALWAYS_OUT,
  output [7:0] DATA_OUT
);

  wire [3:0] pull_resistor_1_node;

  Register register_1 (.D(DATA_IN), .en(STORE), .clk(CLOCK), .Q(ALWAYS_OUT), .clr(RESET));
  Pull_Resistor pull_resistor_1 (.node(pull_resistor_1_node[0]));
  Pull_Resistor pull_resistor_2 (.node(pull_resistor_1_node[1]));
  Pull_Resistor pull_resistor_3 (.node(pull_resistor_1_node[2]));
  Pull_Resistor pull_resistor_4 (.node(pull_resistor_1_node[3]));
  assign DATA_OUT = DATA_OUT_ENB ? {ALWAYS_OUT[7:4], pull_resistor_1_node} : 8'bz;  // Controlled_Buffer controlled_buffer_1
endmodule

module S_CTN (
  input  RESET,
  input  CLOCK,
  output [3:0] BINARY_OUT
);

  Counter #(.max('hf), .width(4)) counter_1 (
    .clr(RESET), .up(1'b1), .count(1'b1), .clk(CLOCK), .Q(BINARY_OUT));  // open: load, D, carry
endmodule

module O_REG (
  input  [7:0] DATA_IN,
  input  STORE,
  input  CLOCK,
  input  RESET,
  output [7:0] DATA_OUT
);

  Register register_1 (.D(DATA_IN), .en(STORE), .clk(CLOCK), .Q(DATA_OUT), .clr(RESET));
endmodule

module F_REG (
  input  CARRY,
  input  ZERO,
  input  STORE,
  input  CLOCK,
  input  RESET,
  output CARRY_OUT,
  output ZERO_OUT
);

  Register #(.width(1)) register_1 (.D(CARRY), .en(STORE), .clk(CLOCK), .Q(CARRY_OUT), .clr(RESET));
  Register #(.width(1)) register_2 (.D(ZERO), .en(STORE), .clk(CLOCK), .Q(ZERO_OUT), .clr(RESET));
endmodule

module ZF_REG (
  input  [7:0] in_1,
  output ZERO
);

  wire or_1_out, or_2_out, or_3_out, or_4_out, or_5_out, or_6_out, or_7_out;

  or or_1 (or_1_out, in_1[0], in_1[1]);
  or or_2 (or_2_out, in_1[2], in_1[3]);
  or or_3 (or_3_out, in_1[4], in_1[5]);
  or or_4 (or_4_out, in_1[6], in_1[7]);
  or or_5 (or_5_out, or_1_out, or_2_out);
  or or_6 (or_6_out, or_3_out, or_4_out);
  or or_7 (or_7_out, or_5_out, or_6_out);
  not not_1 (ZERO, or_7_out);
endmodule

module MAR_REG (
  input  [3:0] DATA_IN,
  input  MAR_IN,
  input  CLOCK,
  input  MAR_RESET,
  input  MAR_OUT,
  output [3:0] ALWAYS_OUT,
  output [3:0] DATA_OUT
);

  Register #(.width(4)) register_1 (.D(DATA_IN), .en(MAR_IN), .clk(CLOCK), .Q(ALWAYS_OUT), .clr(MAR_RESET));
  assign DATA_OUT = MAR_OUT ? ALWAYS_OUT : 4'bz;  // Controlled_Buffer controlled_buffer_1
endmodule

module MEM (
  input  [3:0] ADDRESS,
  input  [7:0] DATA,
  input  STORE,
  input  CLOCK,
  input  RAM_OUT_ENB,
  output [7:0] ALWAYS_OUT,
  output [7:0] RAM_OUT
);

  RAM #(.addrWidth(4)) ram_1 (.addr(ADDRESS), .we(STORE), .oe(RAM_OUT_ENB), .clk(CLOCK), .din(DATA), .dout(ALWAYS_OUT));
  assign RAM_OUT = RAM_OUT_ENB ? ALWAYS_OUT : 8'bz;  // Controlled_Buffer controlled_buffer_1
endmodule

module DCD_CTRL (
  input  I5,
  input  I4,
  input  l3,
  input  I2,
  input  I1,
  input  I0,
  output O0
);

  wire and_1_out, and_2_out, and_3_out, and_4_out, and_5_out, and_6_out, or_1_out, or_2_out, or_3_out,
       or_4_out;

  LED led_1 (.in(I5));
  LED led_2 (.in(I4));
  Pull_Resistor pull_resistor_1 (.node(I5));
  Pull_Resistor pull_resistor_2 (.node(I4));
  LED led_3 (.in(l3));
  LED led_4 (.in(I2));
  LED led_5 (.in(I1));
  LED led_6 (.in(I0));
  Pull_Resistor pull_resistor_3 (.node(l3));
  Pull_Resistor pull_resistor_4 (.node(I2));
  Pull_Resistor pull_resistor_5 (.node(I1));
  Pull_Resistor pull_resistor_6 (.node(I0));
  and and_1 (and_1_out, I0, 1'b1);
  and and_2 (and_2_out, I1, 1'b1);
  and and_3 (and_3_out, I2, 1'b1);
  and and_4 (and_4_out, l3, 1'b1);
  and and_5 (and_5_out, I4, 1'b1);
  and and_6 (and_6_out, I5, 1'b1);
  or or_1 (or_1_out, and_1_out, and_2_out);
  or or_2 (or_2_out, and_3_out, and_4_out);
  or or_3 (or_3_out, and_5_out, and_6_out);
  or or_4 (or_4_out, or_1_out, or_2_out);
  or or_5 (O0, or_4_out, or_3_out);
endmodule

module OPR_REG (
  input  [3:0] DATA_IN,
  input  STORE,
  input  CLOCK,
  input  RESET,
  input  DATA_OUT_ENB,
  output [3:0] ALWAYS_OUT,
  output [3:0] DATA_OUT
);

  Register #(.width(4)) register_1 (.D(DATA_IN), .en(STORE), .clk(CLOCK), .Q(ALWAYS_OUT), .clr(RESET));
  assign DATA_OUT = DATA_OUT_ENB ? ALWAYS_OUT : 4'bz;  // Controlled_Buffer controlled_buffer_1
endmodule

module RESULT_REG (
  input  [7:0] DATA_IN,
  input  R_IN,
  input  R_OUT,
  input  CLOCK,
  input  R_RESET,
  output [7:0] ALWAYS_OUT,
  output [7:0] DATA_OUT
);

  Register register_1 (.D(DATA_IN), .en(R_IN), .clk(CLOCK), .Q(ALWAYS_OUT), .clr(R_RESET));
  assign DATA_OUT = R_OUT ? ALWAYS_OUT : 8'bz;  // Controlled_Buffer controlled_buffer_1
endmodule

module JMP_DCD (
  input  JZ,
  input  ZERO,
  input  JUMP,
  output J_OUT
);

  wire and_1_out;

  or or_1 (J_OUT, and_1_out, JUMP);
  and and_1 (and_1_out, JZ, ZERO);
endmodule

module CPU (
  input  CLK_ENB,
  input  MANUAL_TICK,
  input  PROGRAM_MODE
);

  wire alu_1_cout, ALU_OUT, button_1_out, clk_1_clk_out, clock_1_out, controlled_buffer_1_out,
       controlled_buffer_4_out, controlled_buffer_5_out, controlled_buffer_6_out, controlled_buffer_7_out,
       controlled_buffer_8_out, controlled_buffer_9_out, controlled_buffer_10_out, controlled_buffer_11_out,
       controlled_buffer_12_out, controlled_buffer_13_out, controlled_buffer_14_out,
       controlled_buffer_15_out, controlled_buffer_16_out, COUNTER_ENB, COUT, dcd_1_o1, dcd_1_o2, dcd_1_o3,
       dcd_1_o4, dcd_1_o5, dcd_1_o6, dcd_1_o7, dcd_1_o8, dcd_1_o9, dcd_1_o10, dcd_1_o11, dcd_1_o12,
       dcd_1_o13, dcd_1_o14, dcd_1_o15, DCD_FLUSH, DCD_IN, decoder_1_out4, EXEC, FLAGS_IN, FLUSH, HALT,
       INR_IN, INR_OUT, jmp_dcd_1_j_out, JUMP, JZ, MAR_IN, MAR_OUT, multiplexer_2_out, not_1_out, not_2_out,
       not_3_out, OPR_IN, OPR_OUT, or_1_out, or_2_out, OUTPUT_REG_IN, pull_resistor_15_node, R0_IN, R0_OUT,
       R1_IN, R1_OUT, RAM_IN, RAM_OUT, ROM_OUT, RR_IN, RR_OUT, SUB, ZERO, zf_reg_1_zero;
  wire [3:0] decoder_1_out3, dipswitch_2_sw4, mar_reg_1_always_out, multiplexer_3_out, opr_reg_1_always_out,
       PC_ADDR, s_ctn_1_binary_out;
  wire [3:3] pull_resistor_1_node;
  wire [7:0] alu_1_always_out, binary_to_bcd_converter_1_p1, dipswitch_1_sw8, i_reg_1_always_out,
       i_reg_1_data_out, mem_1_always_out, multiplexer_1_out, r0_1_always_out, r1_1_always_out,
       result_reg_1_always_out, rom_1_data;
  wire [15:10] rom_2_data;

  not not_1 (not_1_out, PROGRAM_MODE);
  assign controlled_buffer_1_out = not_1_out ? clk_1_clk_out : 1'bz;  // Controlled_Buffer controlled_buffer_1
  not not_2 (not_2_out, controlled_buffer_1_out);
  or or_1 (or_1_out, FLUSH, decoder_1_out4);
  S_CTN s_ctn_1 (.RESET(or_1_out), .CLOCK(not_2_out), .BINARY_OUT(s_ctn_1_binary_out));
  DipSwitch dipswitch_1 (
    .sw1(dipswitch_1_sw8[7]), .sw2(dipswitch_1_sw8[6]), .sw3(dipswitch_1_sw8[5]), .sw4(dipswitch_1_sw8[4]),
    .sw5(dipswitch_1_sw8[3]), .sw6(dipswitch_1_sw8[2]), .sw7(dipswitch_1_sw8[1]), .sw8(dipswitch_1_sw8[0]));
  LED led_1 (.in(decoder_1_out3[3]));
  Clock clock_1 (.out(clock_1_out));
  LED led_2 (.in(decoder_1_out3[2]));
  LED led_3 (.in(decoder_1_out3[1]));
  LED led_4 (.in(decoder_1_out3[0]));
  Decoder #(.enable("false"), .select(3)) decoder_1 (
    .out0(decoder_1_out3[3]), .out1(decoder_1_out3[2]), .out2(decoder_1_out3[1]), .out3(decoder_1_out3[0]),
    .out4(decoder_1_out4), .sel(s_ctn_1_binary_out[2:0]));  // open: out5, out6, out7
  CLK clk_1 (.HALT(HALT), .CLK_ENB(CLK_ENB), .MANUAL_CLK(MANUAL_TICK), .CLK_IN(clock_1_out), .CLK_OUT(clk_1_clk_out));
  not not_3 (not_3_out, PROGRAM_MODE);
  DipSwitch #(.number(4)) dipswitch_2 (
    .sw1(dipswitch_2_sw4[3]), .sw2(dipswitch_2_sw4[2]), .sw3(dipswitch_2_sw4[1]), .sw4(dipswitch_2_sw4[0]));
  Multiplexer #(.width(8)) multiplexer_1 (
    .in0(i_reg_1_data_out), .in1(dipswitch_1_sw8), .out(multiplexer_1_out), .sel(PROGRAM_MODE));
  Multiplexer multiplexer_2 (.in0(RAM_IN), .in1(button_1_out), .out(multiplexer_2_out), .sel(PROGRAM_MODE));
  Button button_1 (.out(button_1_out));
  ROM #(.addrWidth(4)) rom_1 (.addr(PC_ADDR), .data(rom_1_data));
  Pull_Resistor pull_resistor_1 (.node(pull_resistor_1_node[3]));
  ROM #(.addrWidth(4), .dataWidth(16)) rom_2 (
    .addr({pull_resistor_1_node[3], s_ctn_1_binary_out[3], s_ctn_1_binary_out[1:0]}),
    .data({rom_2_data, OPR_IN, DCD_FLUSH, EXEC, MAR_OUT, MAR_IN, INR_OUT, ROM_OUT, COUNTER_ENB, DCD_IN, INR_IN}));
  LED led_5 (.in(rom_2_data[15]));
  LED led_6 (.in(rom_2_data[14]));
  LED led_7 (.in(rom_2_data[13]));
  LED led_8 (.in(not_3_out));
  LED led_9 (.in(PROGRAM_MODE));
  Multiplexer #(.width(4)) multiplexer_3 (
    .in0(mar_reg_1_always_out), .in1(dipswitch_2_sw4), .out(multiplexer_3_out), .sel(PROGRAM_MODE));
  LED led_10 (.in(mem_1_always_out[5]));
  LED led_11 (.in(mem_1_always_out[4]));
  LED led_12 (.in(mem_1_always_out[7]));
  LED led_13 (.in(mem_1_always_out[6]));
  LED led_14 (.in(i_reg_1_always_out[5]));
  LED led_15 (.in(i_reg_1_always_out[4]));
  LED led_16 (.in(i_reg_1_always_out[7]));
  LED led_17 (.in(i_reg_1_always_out[6]));
  LED led_18 (.in(opr_reg_1_always_out[3]));
  LED led_19 (.in(rom_2_data[10]));
  LED led_20 (.in(OPR_IN));
  LED led_21 (.in(rom_2_data[12]));
  LED led_22 (.in(rom_2_data[11]));
  LED led_23 (.in(multiplexer_3_out[3]));
  LED led_24 (.in(multiplexer_3_out[2]));
  LED led_25 (.in(mem_1_always_out[3]));
  LED led_26 (.in(mem_1_always_out[2]));
  LED led_27 (.in(mem_1_always_out[1]));
  LED led_28 (.in(mem_1_always_out[0]));
  I_REG i_reg_1 (
    .DATA_IN(i_reg_1_data_out), .STORE(INR_IN), .CLOCK(clk_1_clk_out), .RESET(FLUSH), .DATA_OUT_ENB(INR_OUT),
    .ALWAYS_OUT(i_reg_1_always_out), .DATA_OUT(i_reg_1_data_out));
  LED led_29 (.in(i_reg_1_always_out[3]));
  LED led_30 (.in(i_reg_1_always_out[2]));
  LED led_31 (.in(i_reg_1_always_out[1]));
  LED led_32 (.in(i_reg_1_always_out[0]));
  OPR_REG opr_reg_1 (
    .DATA_OUT_ENB(OPR_OUT), .DATA_IN(i_reg_1_data_out[3:0]), .STORE(OPR_IN), .CLOCK(clk_1_clk_out),
    .RESET(FLUSH), .ALWAYS_OUT(opr_reg_1_always_out), .DATA_OUT(i_reg_1_data_out[3:0]));
  LED led_33 (.in(opr_reg_1_always_out[2]));
  LED led_34 (.in(opr_reg_1_always_out[1]));
  LED led_35 (.in(opr_reg_1_always_out[0]));
  LED led_36 (.in(DCD_FLUSH));
  LED led_37 (.in(EXEC));
  LED led_38 (.in(MAR_OUT));
  LED led_39 (.in(MAR_IN));
  MAR_REG mar_reg_1 (
    .DATA_IN(i_reg_1_data_out[3:0]), .MAR_IN(MAR_IN), .CLOCK(clk_1_clk_out), .MAR_RESET(FLUSH),
    .MAR_OUT(MAR_OUT), .ALWAYS_OUT(mar_reg_1_always_out), .DATA_OUT(i_reg_1_data_out[3:0]));
  LED led_40 (.in(multiplexer_3_out[1]));
  LED led_41 (.in(multiplexer_3_out[0]));
  MEM mem_1 (
    .STORE(multiplexer_2_out), .CLOCK(clk_1_clk_out), .RAM_OUT_ENB(RAM_OUT), .ADDRESS(multiplexer_3_out),
    .DATA(multiplexer_1_out), .ALWAYS_OUT(mem_1_always_out), .RAM_OUT(i_reg_1_data_out));
  LED led_42 (.in(INR_OUT));
  LED led_43 (.in(ROM_OUT));
  LED led_44 (.in(COUNTER_ENB));
  LED led_45 (.in(DCD_IN));
  assign i_reg_1_data_out = ROM_OUT ? rom_1_data : 8'bz;  // Controlled_Buffer controlled_buffer_2
  LED led_46 (.in(INR_IN));
  LED led_47 (.in(i_reg_1_data_out[7]));
  LED led_48 (.in(i_reg_1_data_out[6]));
  LED led_49 (.in(i_reg_1_data_out[5]));
  LED led_50 (.in(i_reg_1_data_out[4]));
  Pull_Resistor pull_resistor_2 (.node(i_reg_1_data_out[7]));
  Pull_Resistor pull_resistor_3 (.node(i_reg_1_data_out[6]));
  Pull_Resistor pull_resistor_4 (.node(i_reg_1_data_out[5]));
  Pull_Resistor pull_resistor_5 (.node(i_reg_1_data_out[4]));
  LED led_51 (.in(i_reg_1_data_out[3]));
  LED led_52 (.in(i_reg_1_data_out[2]));
  LED led_53 (.in(i_reg_1_data_out[1]));
  LED led_54 (.in(i_reg_1_data_out[0]));
  Pull_Resistor pull_resistor_6 (.node(i_reg_1_data_out[3]));
  Pull_Resistor pull_resistor_7 (.node(i_reg_1_data_out[2]));
  Pull_Resistor pull_resistor_8 (.node(i_reg_1_data_out[1]));
  Pull_Resistor pull_resistor_9 (.node(i_reg_1_data_out[0]));
  LED led_55 (.in(i_reg_1_data_out[3]));
  LED led_56 (.in(i_reg_1_data_out[2]));
  Pull_Resistor pull_resistor_10 (.node(i_reg_1_data_out[3]));
  Pull_Resistor pull_resistor_11 (.node(i_reg_1_data_out[2]));
  LED led_57 (.in(i_reg_1_data_out[1]));
  LED led_58 (.in(i_reg_1_data_out[0]));
  Pull_Resistor pull_resistor_12 (.node(i_reg_1_data_out[1]));
  Pull_Resistor pull_resistor_13 (.node(i_reg_1_data_out[0]));
  LED led_59 (.in(r0_1_always_out[7]));
  LED led_60 (.in(r0_1_always_out[6]));
  LED led_61 (.in(r0_1_always_out[5]));
  LED led_62 (.in(r1_1_always_out[7]));
  LED led_63 (.in(r1_1_always_out[6]));
  LED led_64 (.in(r1_1_always_out[5]));
  LED led_65 (.in(result_reg_1_always_out[7]));
  LED led_66 (.in(result_reg_1_always_out[6]));
  LED led_67 (.in(result_reg_1_always_out[5]));
  or or_2 (or_2_out, FLUSH, DCD_FLUSH);
  Pull_Resistor pull_resistor_14 (.node(FLUSH));
  PC pc_1 (
    .RESET(FLUSH), .JUMP(jmp_dcd_1_j_out), .COUNTER_ENB(COUNTER_ENB), .CLOCK(clk_1_clk_out),
    .ADDR_IN(i_reg_1_data_out[3:0]), .ALWAYS_OUT(PC_ADDR));  // open: COUNTER_OUT, ADDR_OUT
  LED led_68 (.in(r0_1_always_out[4]));
  LED led_69 (.in(r0_1_always_out[3]));
  LED led_70 (.in(r0_1_always_out[2]));
  LED led_71 (.in(r0_1_always_out[1]));
  LED led_72 (.in(r1_1_always_out[4]));
  LED led_73 (.in(r1_1_always_out[3]));
  LED led_74 (.in(r1_1_always_out[2]));
  LED led_75 (.in(r1_1_always_out[1]));
  LED led_76 (.in(result_reg_1_always_out[4]));
  LED led_77 (.in(result_reg_1_always_out[3]));
  LED led_78 (.in(result_reg_1_always_out[2]));
  LED led_79 (.in(result_reg_1_always_out[1]));
  _7_Segment_Display u_7_segment_display_1 ();  // open: g, f, a, b, e, d, c, dp
  _7_Segment_Display u_7_segment_display_2 ();  // open: g, f, a, b, e, d, c, dp
  // BCD_to_7_Segment_decoder bcd_to_7_segment_decoder_1: pin names not known
  // BCD_to_7_Segment_decoder bcd_to_7_segment_decoder_2: pin names not known
  // Binary_to_BCD_converter #(.binvalue(8)) binary_to_bcd_converter_1: pin names not known; wires that end beside it: binary_to_bcd_converter_1_p1
  Pull_Resistor pull_resistor_15 (.node(pull_resistor_15_node));
  DCD dcd_1 (
    .DCD_FLUSH(or_2_out), .SELECTOR(i_reg_1_data_out[7:4]), .ENB(DCD_IN), .EXEC(EXEC), .O8(dcd_1_o8),
    .O9(dcd_1_o9), .O10(dcd_1_o10), .O11(dcd_1_o11), .O12(dcd_1_o12), .O13(dcd_1_o13), .O14(dcd_1_o14),
    .O15(dcd_1_o15), .O0(pull_resistor_15_node), .O1(dcd_1_o1), .O2(dcd_1_o2), .O3(dcd_1_o3), .O4(dcd_1_o4),
    .O5(dcd_1_o5), .O6(dcd_1_o6), .O7(dcd_1_o7));
  Pull_Resistor pull_resistor_16 (.node(dcd_1_o1));
  Button RESET (.out(FLUSH));
  R0 r0_1 (
    .DATA_IN(i_reg_1_data_out), .A_IN(R0_IN), .CLOCK(clk_1_clk_out), .A_RESET(FLUSH), .A_OUT(R0_OUT),
    .ALWAYS_OUT(r0_1_always_out), .DATA_OUT(i_reg_1_data_out));
  LED led_80 (.in(r0_1_always_out[0]));
  ALU alu_1 (
    .A_IN(r0_1_always_out), .B_IN(r1_1_always_out), .OUTPUT_ENB(ALU_OUT), .SUB(SUB),
    .ALWAYS_OUT(alu_1_always_out), .A_OUT(i_reg_1_data_out), .COUT(alu_1_cout));
  LED led_81 (.in(r1_1_always_out[0]));
  R1 r1_1 (
    .DATA_IN(i_reg_1_data_out), .B_IN(R1_IN), .CLOCK(clk_1_clk_out), .B_RESET(FLUSH), .B_OUT(R1_OUT),
    .ALWAYS_OUT(r1_1_always_out), .DATA_OUT(i_reg_1_data_out));
  LED led_82 (.in(result_reg_1_always_out[0]));
  RESULT_REG result_reg_1 (
    .DATA_IN(i_reg_1_data_out), .R_IN(RR_IN), .CLOCK(clk_1_clk_out), .R_RESET(FLUSH), .R_OUT(RR_OUT),
    .ALWAYS_OUT(result_reg_1_always_out), .DATA_OUT(i_reg_1_data_out));
  _7_Segment_Display u_7_segment_display_3 ();  // open: g, f, a, b, e, d, c, dp
  // BCD_to_7_Segment_decoder bcd_to_7_segment_decoder_3: pin names not known
  O_REG o_reg_1 (
    .DATA_IN(i_reg_1_data_out), .STORE(OUTPUT_REG_IN), .CLOCK(clk_1_clk_out), .RESET(FLUSH),
    .DATA_OUT(binary_to_bcd_converter_1_p1));
  LED led_83 (.in(HALT));
  LED led_84 (.in(controlled_buffer_4_out));
  LED led_85 (.in(controlled_buffer_5_out));
  assign HALT = dcd_1_o2 ? dcd_1_o2 : 1'bz;  // Controlled_Buffer controlled_buffer_3
  assign controlled_buffer_4_out = dcd_1_o3 ? dcd_1_o3 : 1'bz;  // Controlled_Buffer controlled_buffer_4
  assign controlled_buffer_5_out = dcd_1_o4 ? dcd_1_o4 : 1'bz;  // Controlled_Buffer controlled_buffer_5
  assign controlled_buffer_6_out = dcd_1_o5 ? dcd_1_o5 : 1'bz;  // Controlled_Buffer controlled_buffer_6
  assign controlled_buffer_7_out = dcd_1_o6 ? dcd_1_o6 : 1'bz;  // Controlled_Buffer controlled_buffer_7
  assign controlled_buffer_8_out = dcd_1_o7 ? dcd_1_o7 : 1'bz;  // Controlled_Buffer controlled_buffer_8
  assign controlled_buffer_9_out = dcd_1_o8 ? dcd_1_o8 : 1'bz;  // Controlled_Buffer controlled_buffer_9
  assign controlled_buffer_10_out = dcd_1_o9 ? dcd_1_o9 : 1'bz;  // Controlled_Buffer controlled_buffer_10
  assign controlled_buffer_11_out = dcd_1_o10 ? dcd_1_o10 : 1'bz;  // Controlled_Buffer controlled_buffer_11
  assign controlled_buffer_12_out = dcd_1_o11 ? dcd_1_o11 : 1'bz;  // Controlled_Buffer controlled_buffer_12
  assign controlled_buffer_13_out = dcd_1_o12 ? dcd_1_o12 : 1'bz;  // Controlled_Buffer controlled_buffer_13
  assign controlled_buffer_14_out = dcd_1_o13 ? dcd_1_o13 : 1'bz;  // Controlled_Buffer controlled_buffer_14
  assign controlled_buffer_15_out = dcd_1_o14 ? dcd_1_o14 : 1'bz;  // Controlled_Buffer controlled_buffer_15
  assign controlled_buffer_16_out = dcd_1_o15 ? dcd_1_o15 : 1'bz;  // Controlled_Buffer controlled_buffer_16
  Pull_Resistor pull_resistor_17 (.node(HALT));
  Pull_Resistor pull_resistor_18 (.node(controlled_buffer_4_out));
  Pull_Resistor pull_resistor_19 (.node(controlled_buffer_5_out));
  JMP_DCD jmp_dcd_1 (.JUMP(JUMP), .JZ(JZ), .ZERO(ZERO), .J_OUT(jmp_dcd_1_j_out));
  ZF_REG zf_reg_1 (.in_1(alu_1_always_out), .ZERO(zf_reg_1_zero));
  LED led_86 (.in(controlled_buffer_6_out));
  LED led_87 (.in(controlled_buffer_7_out));
  LED led_88 (.in(controlled_buffer_8_out));
  LED led_89 (.in(controlled_buffer_9_out));
  Pull_Resistor pull_resistor_20 (.node(controlled_buffer_6_out));
  Pull_Resistor pull_resistor_21 (.node(controlled_buffer_7_out));
  Pull_Resistor pull_resistor_22 (.node(controlled_buffer_8_out));
  Pull_Resistor pull_resistor_23 (.node(controlled_buffer_9_out));
  F_REG f_reg_1 (
    .CARRY(alu_1_cout), .ZERO(zf_reg_1_zero), .STORE(FLAGS_IN), .CLOCK(clk_1_clk_out), .RESET(FLUSH),
    .CARRY_OUT(COUT), .ZERO_OUT(ZERO));
  LED led_90 (.in(controlled_buffer_10_out));
  LED led_91 (.in(controlled_buffer_11_out));
  LED led_92 (.in(controlled_buffer_12_out));
  LED led_93 (.in(controlled_buffer_13_out));
  Pull_Resistor pull_resistor_24 (.node(controlled_buffer_10_out));
  Pull_Resistor pull_resistor_25 (.node(controlled_buffer_11_out));
  Pull_Resistor pull_resistor_26 (.node(controlled_buffer_12_out));
  Pull_Resistor pull_resistor_27 (.node(controlled_buffer_13_out));
  LED led_94 (.in(COUT));
  LED led_95 (.in(ZERO));
  LED led_96 (.in(controlled_buffer_14_out));
  LED led_97 (.in(controlled_buffer_15_out));
  LED led_98 (.in(controlled_buffer_16_out));
  Pull_Resistor pull_resistor_28 (.node(controlled_buffer_14_out));
  Pull_Resistor pull_resistor_29 (.node(controlled_buffer_15_out));
  Pull_Resistor pull_resistor_30 (.node(controlled_buffer_16_out));
  DCD_CTRL dcd_ctrl_1 (
    .I5(controlled_buffer_4_out), .I4(controlled_buffer_5_out), .l3(controlled_buffer_6_out), .O0(RAM_OUT));  // open: I2, I1, I0
  DCD_CTRL dcd_ctrl_2 (.I5(controlled_buffer_4_out), .I4(controlled_buffer_9_out), .O0(R0_IN));  // open: l3, I2, I1, I0
  DCD_CTRL dcd_ctrl_3 (
    .I5(controlled_buffer_5_out), .I4(controlled_buffer_10_out), .O0(R1_IN));  // open: l3, I2, I1, I0
  DCD_CTRL dcd_ctrl_4 (.I5(controlled_buffer_6_out), .O0(OUTPUT_REG_IN));  // open: I4, l3, I2, I1, I0
  DCD_CTRL dcd_ctrl_5 (
    .I5(controlled_buffer_7_out), .I4(controlled_buffer_8_out), .l3(controlled_buffer_14_out), .O0(RAM_IN));  // open: I2, I1, I0
  DCD_CTRL dcd_ctrl_6 (.I5(controlled_buffer_7_out), .O0(R0_OUT));  // open: I4, l3, I2, I1, I0
  DCD_CTRL dcd_ctrl_7 (.I5(controlled_buffer_8_out), .O0(R1_OUT));  // open: I4, l3, I2, I1, I0
  DCD_CTRL dcd_ctrl_8 (
    .I5(controlled_buffer_9_out), .I4(controlled_buffer_10_out), .l3(controlled_buffer_11_out),
    .I2(controlled_buffer_16_out), .O0(OPR_OUT));  // open: I1, I0
  DCD_CTRL dcd_ctrl_9 (.I5(controlled_buffer_11_out), .O0(JUMP));  // open: I4, l3, I2, I1, I0
  DCD_CTRL dcd_ctrl_10 (
    .I5(controlled_buffer_15_out), .I4(controlled_buffer_12_out), .l3(controlled_buffer_13_out),
    .I2(controlled_buffer_16_out), .O0(FLAGS_IN));  // open: I1, I0
  DCD_CTRL dcd_ctrl_11 (
    .I5(controlled_buffer_12_out), .I4(controlled_buffer_13_out), .O0(RR_IN));  // open: l3, I2, I1, I0
  DCD_CTRL dcd_ctrl_12 (.I5(controlled_buffer_14_out), .O0(RR_OUT));  // open: I4, l3, I2, I1, I0
  DCD_CTRL dcd_ctrl_13 (
    .I5(controlled_buffer_12_out), .I4(controlled_buffer_13_out), .O0(ALU_OUT));  // open: l3, I2, I1, I0
  DCD_CTRL dcd_ctrl_14 (
    .I5(controlled_buffer_13_out), .I4(controlled_buffer_15_out), .O0(SUB));  // open: l3, I2, I1, I0
  DCD_CTRL dcd_ctrl_15 (.I5(controlled_buffer_16_out), .O0(JZ));  // open: I4, l3, I2, I1, I0

  // Other names for the same wires on the sheet: IRN_RESET = FLUSH; MAR_RESET = FLUSH; OPR_RESET = FLUSH;
  //   PROG_MODE = PROGRAM_MODE

  // Notes on the sheet:
  //   T0
  //   T1
  //   T2
  //   T3
  //   contents of rom_1 (hex, n*v repeats v):
  //   81 91 e0 f7 90 71 51 91 71 51 20
  //   contents of rom_2 (hex, n*v repeats v):
  //   229 16 80 900
  //   PROGRAM CODE
  //   MICROCODE
  //   7
  //   6
  //   5
  //   4
  //   data
  //   3
  //   2
  //   1
  //   0
  //   3
  //   2
  //   address
  //   1
  //   0
  //   counter++
endmodule
