// Logisim project main16.circ as structural Verilog: 22 circuits, main circuit CLK
module V1 (
  input  [7:0] in_1,
  input  in_2,
  input  in_3,
  input  input_to_bus,
  input  bus_to_reg,
  input  reg_to_bus,
  input  reset_all__regs,
  input  bus_to_ram,
  input  ram_to_bus,
  input  [1:0] in_10,
  input  [1:0] in_11,
  input  instruction_mode,
  input  reset_pc,
  input  in_14,
  output [7:0] DATA_BUS
);

  wire clk_1_p4, clk_1_p5, clock_1_out, controlled_buffer_3_out, demultiplexer_1_out1, demultiplexer_1_out2,
       demultiplexer_1_out3;
  wire [7:0] A_q, B_q, C_q, controlled_buffer_1_out, controlled_buffer_6_out, D_q, demultiplexer_1_out0,
       demultiplexer_2_out0, demultiplexer_2_out2, multiplexer_1_out, PC_q, ram_1_dout, undriven;

  Clock clock_1 (.out(clock_1_out));
  // CLK clk_1: pin names not known; wires that end beside it: clock_1_out, in_2, in_3, clk_1_p4, clk_1_p5
  Register PC (.D(undriven), .clk(in_14), .Q(PC_q), .clr(reset_pc));  // open: en
  Register A (.D(demultiplexer_2_out0), .en(demultiplexer_1_out0[0]), .clk(clk_1_p5), .Q(A_q), .clr(reset_all__regs));
  Register B (.D(demultiplexer_1_out0), .en(demultiplexer_1_out1), .clk(clk_1_p5), .Q(B_q), .clr(reset_all__regs));
  Register C (.D(demultiplexer_2_out2), .en(demultiplexer_1_out2), .clk(clk_1_p5), .Q(C_q), .clr(reset_all__regs));
  Register D (.D(demultiplexer_1_out0), .en(demultiplexer_1_out3), .clk(clk_1_p5), .Q(D_q), .clr(reset_all__regs));
  Demultiplexer #(.select(2)) demultiplexer_1 (
    .out0(demultiplexer_1_out0[0]), .out1(demultiplexer_1_out1), .out2(demultiplexer_1_out2),
    .out3(demultiplexer_1_out3), .in(bus_to_reg), .sel(in_11));
  assign controlled_buffer_1_out = bus_to_reg ? DATA_BUS : 8'bz;  // Controlled_Buffer controlled_buffer_1
  Demultiplexer #(.select(2), .width(8)) demultiplexer_2 (
    .out0(demultiplexer_2_out0), .out1(demultiplexer_1_out0), .out2(demultiplexer_2_out2),
    .out3(demultiplexer_1_out0), .in(controlled_buffer_1_out), .sel(in_11));
  assign DATA_BUS = reg_to_bus ? multiplexer_1_out : 8'bz;  // Controlled_Buffer controlled_buffer_2
  Multiplexer #(.select(2), .width(8)) multiplexer_1 (
    .in0(A_q), .in1(B_q), .in2(C_q), .in3(D_q), .out(multiplexer_1_out), .sel(in_10));
  RAM ram_1 (
    .addr(PC_q), .we(bus_to_ram), .oe(ram_to_bus), .clk(controlled_buffer_3_out),
    .din(controlled_buffer_6_out), .dout(ram_1_dout));
  assign controlled_buffer_3_out = bus_to_ram ? clk_1_p5 : 1'bz;  // Controlled_Buffer controlled_buffer_3
  assign controlled_buffer_3_out = ram_to_bus ? clk_1_p5 : 1'bz;  // Controlled_Buffer controlled_buffer_4
  assign DATA_BUS = ram_to_bus ? ram_1_dout : 8'bz;  // Controlled_Buffer controlled_buffer_5
  assign controlled_buffer_6_out = bus_to_ram ? DATA_BUS : 8'bz;  // Controlled_Buffer controlled_buffer_6
  assign clk_1_p4 = ram_to_bus ? instruction_mode : 1'bz;  // Controlled_Buffer controlled_buffer_7
  assign DATA_BUS = input_to_bus ? in_1 : 8'bz;  // Controlled_Buffer controlled_buffer_8
  // Pins of 1 and 8 bits meet at demultiplexer_1_out0

  // Notes on the sheet:
  //   GPR REGISTERS
  //   alterna o WE pra input
  //   alterna o reg do input
  //   alterna o reg do output
  //   TODO: STORE mem, R1/R2/R3/R4
  //   instruction mode is on only if ram to bus is on
  //   input
  //   reg output selector
  //   reg input selector
endmodule

module V2 (
  input  [1:0] in_1,
  input  [1:0] in_2,
  input  reset_pc,
  input  halt,
  input  input_to_dbus,
  input  [7:0] in_6,
  input  pc_to_pbus,
  input  in_8,
  input  pbus_to_ram,
  input  dbus_to_ram,
  input  ram_to_ibus,
  input  dbus_to_reg,
  input  reg_to_dbus,
  input  reset_GPR,
  output [2:0] instruction_bus,
  output [7:0] data_bus,
  output [7:0] pc_bus
);

  wire clk_1_clk_out, demultiplexer_1_out0, demultiplexer_1_out1, demultiplexer_1_out2, demultiplexer_1_out3;
  wire [7:0] controlled_buffer_1_out, controlled_buffer_2_out, controlled_buffer_7_out, demultiplexer_2_out1,
       demultiplexer_2_out2, multiplexer_1_out, R0_q, R1_q, R3_q, ram_1_dout;
  wire [7:1] demultiplexer_2_out0, pc_1_p6;

  Clock clock_1 ();  // open: out
  CLK clk_1 (.CLK_ENB(reset_GPR), .MANUAL_CLK(reset_GPR), .CLK_IN(reset_GPR), .CLK_OUT(clk_1_clk_out));  // open: HALT
  Demultiplexer #(.select(2)) demultiplexer_1 (
    .out0(demultiplexer_1_out0), .out1(demultiplexer_1_out1), .out2(demultiplexer_1_out2),
    .out3(demultiplexer_1_out3), .in(dbus_to_ram), .sel(in_2));
  Demultiplexer #(.select(2), .width(8)) demultiplexer_2 (
    .out0({demultiplexer_2_out0, reset_pc}), .out1(demultiplexer_2_out1), .out2(demultiplexer_2_out2),
    .out3({demultiplexer_2_out0, reset_pc}), .in(controlled_buffer_1_out), .sel(in_2));
  // PC pc_1: pin names not known; wires that end beside it: halt, reset_GPR, reset_GPR, clk_1_clk_out, {demultiplexer_2_out0, reset_pc}, {pc_1_p6, dbus_to_ram}
  Register R0 (
    .D({demultiplexer_2_out0, reset_pc}), .en(demultiplexer_1_out0), .clk(clk_1_clk_out), .Q(R0_q),
    .clr(reset_GPR));
  Register R1 (.D(demultiplexer_2_out1), .en(demultiplexer_1_out1), .clk(clk_1_clk_out), .Q(R1_q), .clr(reset_GPR));
  Register R2 (
    .D(demultiplexer_2_out2), .en(demultiplexer_1_out2), .clk(clk_1_clk_out), .Q({pc_1_p6, dbus_to_ram}),
    .clr(reset_GPR));
  Register R3 (
    .D({demultiplexer_2_out0, reset_pc}), .en(demultiplexer_1_out3), .clk(clk_1_clk_out), .Q(R3_q),
    .clr(reset_GPR));
  assign controlled_buffer_1_out = dbus_to_ram ? data_bus : 8'bz;  // Controlled_Buffer controlled_buffer_1
  assign controlled_buffer_2_out = dbus_to_ram ? {pc_1_p6, dbus_to_ram} : 8'bz;  // Controlled_Buffer controlled_buffer_2
  RAM ram_1 (
    .addr(controlled_buffer_2_out), .we(dbus_to_ram), .oe(ram_to_ibus), .clk(clk_1_clk_out),
    .din({pc_1_p6, dbus_to_ram}), .dout(ram_1_dout));
  assign data_bus = reg_to_dbus ? multiplexer_1_out : 8'bz;  // Controlled_Buffer controlled_buffer_3
  assign {pc_1_p6, dbus_to_ram} = dbus_to_ram ? data_bus : 8'bz;  // Controlled_Buffer controlled_buffer_4
  assign data_bus = input_to_dbus ? in_6 : 8'bz;  // Controlled_Buffer controlled_buffer_5
  Bit_Extender #(.out_width(3)) bit_extender_1 (.in(controlled_buffer_7_out), .out(instruction_bus));
  assign {pc_1_p6, dbus_to_ram} = pc_bus;  // Buffer buffer_1, 8 bits wide
  Multiplexer #(.select(2), .width(8)) multiplexer_1 (
    .in0(R0_q), .in1(R1_q), .in2(R3_q), .in3({pc_1_p6, dbus_to_ram}), .out(multiplexer_1_out), .sel(in_1));
  assign pc_bus = pc_to_pbus ? {pc_1_p6, dbus_to_ram} : 8'bz;  // Controlled_Buffer controlled_buffer_6
  assign controlled_buffer_7_out = ram_to_ibus ? ram_1_dout : 8'bz;  // Controlled_Buffer controlled_buffer_7
  ALU alu_1 ();  // open: A_IN, B_IN, OUTPUT_ENB, SUB, ALWAYS_OUT, A_OUT, COUT
  DCD dcd_1 ();  // open: EXEC, DCD_FLUSH, in_4, SELECTOR, ENB, O10, O11, O12, O13, O14, O1, O15, O16, O17, O18, O19, O20, O21, O22, O23, O24, O2, O25, O26, O27, O28, O29, O30, O31, O3, O4, O0, O5, O6, O7, O8, O9, DCD_OUT
  // Pins of 1 and 8 bits meet at {demultiplexer_2_out0, reset_pc}
  // Pins of 1 and 8 bits meet at {pc_1_p6, dbus_to_ram}

  assign dbus_to_reg = dbus_to_ram;
  assign pbus_to_ram = dbus_to_ram;

  // Notes on the sheet:
  //   output register selector
  //   input register selector
  //   input
endmodule

module V3 (
  input  in_1,
  input  in_2,
  input  in_3,
  input  [7:0] in_4,
  input  input_to_bus,
  input  [1:0] in_6,
  input  [7:0] in_7,
  input  input_to_bus_2,
  input  bus_to_reg,
  input  bus_to_ram,
  input  ram_to_bus,
  input  reg_to_bus,
  input  pc_to_pbus,
  input  in_14,
  input  reset_all_GPR,
  output [7:0] pc_bus,
  output [7:0] data_bus
);

  wire clock_1_out, dcd_1_p3, demultiplexer_1_out0, demultiplexer_1_out1, demultiplexer_1_out2,
       demultiplexer_1_out3, undriven;
  wire [1:0] buffer_1_out;
  wire [2:0] bit_extender_1_out;
  wire [7:0] buffer_3_out, buffer_5_out, controlled_buffer_4_out, controlled_buffer_6_out,
       controlled_buffer_7_out, demultiplexer_2_out0, demultiplexer_2_out1, demultiplexer_2_out2,
       demultiplexer_2_out3, multiplexer_1_out, pc_1_p1, R0_q, R1_q, R2_q, R3_q, ram_1_dout;

  Clock clock_1 (.out(clock_1_out));
  CLK clk_1 (.HALT(in_3), .CLK_ENB(in_1), .CLK_IN(clock_1_out));  // open: MANUAL_CLK, CLK_OUT
  // PC pc_1: pin names not known; wires that end beside it: pc_1_p1
  assign buffer_1_out = in_6;  // Buffer buffer_1, 2 bits wide
  Demultiplexer #(.select(2)) demultiplexer_1 (
    .out0(demultiplexer_1_out0), .out1(demultiplexer_1_out1), .out2(demultiplexer_1_out2),
    .out3(demultiplexer_1_out3), .in(bus_to_reg), .sel(buffer_1_out));
  Demultiplexer #(.select(2), .width(8)) demultiplexer_2 (
    .out0(demultiplexer_2_out0), .out1(demultiplexer_2_out1), .out2(demultiplexer_2_out2),
    .out3(demultiplexer_2_out3), .in(pc_bus), .sel(buffer_1_out));
  Register R0 (.D(demultiplexer_2_out0), .en(demultiplexer_1_out0), .clk(undriven), .Q(R0_q), .clr(reset_all_GPR));
  Register R1 (.D(demultiplexer_2_out1), .en(demultiplexer_1_out1), .clk(undriven), .Q(R1_q), .clr(reset_all_GPR));
  Register R2 (.D(demultiplexer_2_out2), .en(demultiplexer_1_out2), .clk(undriven), .Q(R2_q), .clr(reset_all_GPR));
  Register R3 (.D(demultiplexer_2_out3), .en(demultiplexer_1_out3), .clk(undriven), .Q(R3_q), .clr(reset_all_GPR));
  assign pc_bus = pc_to_pbus ? pc_1_p1 : 8'bz;  // Controlled_Buffer controlled_buffer_1
  assign pc_bus = controlled_buffer_7_out;  // Buffer buffer_2, 8 bits wide
  assign buffer_3_out = pc_bus;  // Buffer buffer_3, 8 bits wide
  // ALU alu_1: pin names not known; wires that end beside it: pc_bus, pc_bus, buffer_3_out
  assign data_bus = ram_to_bus ? ram_1_dout : 8'bz;  // Controlled_Buffer controlled_buffer_2
  assign data_bus = controlled_buffer_4_out;  // Buffer buffer_4, 8 bits wide
  assign pc_bus = bus_to_reg ? controlled_buffer_4_out : 8'bz;  // Controlled_Buffer controlled_buffer_3
  assign controlled_buffer_4_out = reg_to_bus ? multiplexer_1_out : 8'bz;  // Controlled_Buffer controlled_buffer_4
  Multiplexer #(.select(2), .width(8)) multiplexer_1 (
    .in0(R0_q), .in1(R1_q), .in2(R2_q), .in3(R3_q), .out(multiplexer_1_out), .sel(in_6));
  RAM ram_1 (
    .addr(buffer_3_out), .we(bus_to_ram), .oe(ram_to_bus), .clk(reset_all_GPR),
    .din(controlled_buffer_6_out), .dout(ram_1_dout));
  assign controlled_buffer_4_out = input_to_bus ? in_4 : 8'bz;  // Controlled_Buffer controlled_buffer_5
  assign controlled_buffer_6_out = bus_to_ram ? data_bus : 8'bz;  // Controlled_Buffer controlled_buffer_6
  assign buffer_5_out = data_bus;  // Buffer buffer_5, 8 bits wide
  assign controlled_buffer_7_out = input_to_bus_2 ? in_7 : 8'bz;  // Controlled_Buffer controlled_buffer_7
  Bit_Extender #(.out_width(3)) bit_extender_1 (.in(buffer_5_out), .out(bit_extender_1_out));
  // DCD dcd_1: pin names not known; wires that end beside it: bit_extender_1_out, in_14, dcd_1_p3, ram_1_dout, ram_1_dout, ram_1_dout, ram_1_dout, ram_1_dout

  // Notes on the sheet:
  //   input reg selector
  //   A = reg ; B = value?
  //   address
endmodule

module DCD (
  input  DCD_FLUSH,
  input  [4:0] SELECTOR,
  input  ENB,
  input  [7:0] in_4,
  input  EXEC,
  output O0,
  output O1,
  output O2,
  output O3,
  output [4:0] DCD_OUT,
  output O4,
  output O5,
  output O6,
  output O7,
  output O8,
  output O9,
  output O10,
  output O11,
  output O12,
  output O13,
  output O14,
  output O15,
  output O16,
  output O17,
  output O18,
  output O19,
  output O20,
  output O21,
  output O22,
  output O23,
  output O24,
  output O25,
  output O26,
  output O27,
  output O28,
  output O29,
  output O30,
  output O31
);

  wire decoder_1_out0, decoder_1_out1, decoder_1_out2, decoder_1_out3, decoder_1_out4, decoder_1_out5,
       decoder_1_out6, decoder_1_out7, decoder_1_out8, decoder_1_out9, decoder_1_out10, decoder_1_out11,
       decoder_1_out12, decoder_1_out13, decoder_1_out14, decoder_1_out15, decoder_1_out16, decoder_1_out17,
       decoder_1_out18, decoder_1_out19, decoder_1_out20, decoder_1_out21, decoder_1_out22, decoder_1_out23,
       decoder_1_out24, decoder_1_out25, decoder_1_out26, decoder_1_out27, decoder_1_out28, decoder_1_out29,
       decoder_1_out30, decoder_1_out31, decoder_2_out0, decoder_2_out1, decoder_2_out2, decoder_2_out3,
       decoder_2_out4, decoder_2_out5, decoder_2_out6, decoder_2_out7, decoder_2_out8, decoder_2_out9,
       decoder_2_out10, decoder_2_out11, decoder_2_out12, decoder_2_out13, decoder_2_out14, decoder_2_out15,
       register_2_q, register_3_q, register_4_q, register_5_q, register_6_q, register_7_q, register_8_q,
       register_9_q, register_10_q, register_11_q, register_12_q, register_13_q, register_14_q,
       register_15_q, register_16_q, register_17_q, register_18_q, register_19_q, register_20_q,
       register_21_q, register_22_q, register_23_q, register_24_q, register_25_q, register_26_q,
       register_27_q, register_28_q, register_29_q, register_30_q, register_31_q, register_32_q,
       register_33_q;

  Decoder #(.select(5)) decoder_1 (
    .out0(decoder_1_out0), .out1(decoder_1_out1), .out2(decoder_1_out2), .out3(decoder_1_out3),
    .out4(decoder_1_out4), .out5(decoder_1_out5), .out6(decoder_1_out6), .out7(decoder_1_out7),
    .out8(decoder_1_out8), .out9(decoder_1_out9), .out10(decoder_1_out10), .out11(decoder_1_out11),
    .out12(decoder_1_out12), .out13(decoder_1_out13), .out14(decoder_1_out14), .out15(decoder_1_out15),
    .out16(decoder_1_out16), .out17(decoder_1_out17), .out18(decoder_1_out18), .out19(decoder_1_out19),
    .out20(decoder_1_out20), .out21(decoder_1_out21), .out22(decoder_1_out22), .out23(decoder_1_out23),
    .out24(decoder_1_out24), .out25(decoder_1_out25), .out26(decoder_1_out26), .out27(decoder_1_out27),
    .out28(decoder_1_out28), .out29(decoder_1_out29), .out30(decoder_1_out30), .out31(decoder_1_out31),
    .sel(SELECTOR), .en(ENB));
  Register #(.width(5)) register_1 (.D(SELECTOR), .en(ENB), .clk(ENB), .Q(DCD_OUT), .clr(DCD_FLUSH));
  Register #(.width(1)) register_2 (
    .D(decoder_1_out0), .en(decoder_1_out0), .clk(decoder_1_out0), .Q(register_2_q), .clr(DCD_FLUSH));
  Register #(.width(1)) register_3 (
    .D(decoder_1_out1), .en(decoder_1_out1), .clk(decoder_1_out1), .Q(register_3_q), .clr(DCD_FLUSH));
  Register #(.width(1)) register_4 (
    .D(decoder_1_out2), .en(decoder_1_out2), .clk(decoder_1_out2), .Q(register_4_q), .clr(DCD_FLUSH));
  Register #(.width(1)) register_5 (
    .D(decoder_1_out3), .en(decoder_1_out3), .clk(decoder_1_out3), .Q(register_5_q), .clr(DCD_FLUSH));
  Register #(.width(1)) register_6 (
    .D(decoder_1_out4), .en(decoder_1_out4), .clk(decoder_1_out4), .Q(register_6_q), .clr(DCD_FLUSH));
  Register #(.width(1)) register_7 (
    .D(decoder_1_out5), .en(decoder_1_out5), .clk(decoder_1_out5), .Q(register_7_q), .clr(DCD_FLUSH));
  Register #(.width(1)) register_8 (
    .D(decoder_1_out6), .en(decoder_1_out6), .clk(decoder_1_out6), .Q(register_8_q), .clr(DCD_FLUSH));
  Register #(.width(1)) register_9 (
    .D(decoder_1_out7), .en(decoder_1_out7), .clk(decoder_1_out7), .Q(register_9_q), .clr(DCD_FLUSH));
  Register #(.width(1)) register_10 (
    .D(decoder_1_out8), .en(decoder_1_out8), .clk(decoder_1_out8), .Q(register_10_q), .clr(DCD_FLUSH));
  Register #(.width(1)) register_11 (
    .D(decoder_1_out9), .en(decoder_1_out9), .clk(decoder_1_out9), .Q(register_11_q), .clr(DCD_FLUSH));
  Register #(.width(1)) register_12 (
    .D(decoder_1_out10), .en(decoder_1_out10), .clk(decoder_1_out10), .Q(register_12_q), .clr(DCD_FLUSH));
  Register #(.width(1)) register_13 (
    .D(decoder_1_out11), .en(decoder_1_out11), .clk(decoder_1_out11), .Q(register_13_q), .clr(DCD_FLUSH));
  Register #(.width(1)) register_14 (
    .D(decoder_1_out12), .en(decoder_1_out12), .clk(decoder_1_out12), .Q(register_14_q), .clr(DCD_FLUSH));
  Register #(.width(1)) register_15 (
    .D(decoder_1_out13), .en(decoder_1_out13), .clk(decoder_1_out13), .Q(register_15_q), .clr(DCD_FLUSH));
  Register #(.width(1)) register_16 (
    .D(decoder_1_out14), .en(decoder_1_out14), .clk(decoder_1_out14), .Q(register_16_q), .clr(DCD_FLUSH));
  Register #(.width(1)) register_17 (
    .D(decoder_1_out15), .en(decoder_1_out15), .clk(decoder_1_out15), .Q(register_17_q), .clr(DCD_FLUSH));
  Register #(.width(1)) register_18 (
    .D(decoder_1_out16), .en(decoder_1_out16), .clk(decoder_1_out16), .Q(register_18_q), .clr(DCD_FLUSH));
  Register #(.width(1)) register_19 (
    .D(decoder_1_out17), .en(decoder_1_out17), .clk(decoder_1_out17), .Q(register_19_q), .clr(DCD_FLUSH));
  Register #(.width(1)) register_20 (
    .D(decoder_1_out18), .en(decoder_1_out18), .clk(decoder_1_out18), .Q(register_20_q), .clr(DCD_FLUSH));
  Register #(.width(1)) register_21 (
    .D(decoder_1_out19), .en(decoder_1_out19), .clk(decoder_1_out19), .Q(register_21_q), .clr(DCD_FLUSH));
  Register #(.width(1)) register_22 (
    .D(decoder_1_out20), .en(decoder_1_out20), .clk(decoder_1_out20), .Q(register_22_q), .clr(DCD_FLUSH));
  Register #(.width(1)) register_23 (
    .D(decoder_1_out21), .en(decoder_1_out21), .clk(decoder_1_out21), .Q(register_23_q), .clr(DCD_FLUSH));
  Register #(.width(1)) register_24 (
    .D(decoder_1_out22), .en(decoder_1_out22), .clk(decoder_1_out22), .Q(register_24_q), .clr(DCD_FLUSH));
  Register #(.width(1)) register_25 (
    .D(decoder_1_out23), .en(decoder_1_out23), .clk(decoder_1_out23), .Q(register_25_q), .clr(DCD_FLUSH));
  Register #(.width(1)) register_26 (
    .D(decoder_1_out24), .en(decoder_1_out24), .clk(decoder_1_out24), .Q(register_26_q), .clr(DCD_FLUSH));
  Register #(.width(1)) register_27 (
    .D(decoder_1_out25), .en(decoder_1_out25), .clk(decoder_1_out25), .Q(register_27_q), .clr(DCD_FLUSH));
  Register #(.width(1)) register_28 (
    .D(decoder_1_out26), .en(decoder_1_out26), .clk(decoder_1_out26), .Q(register_28_q), .clr(DCD_FLUSH));
  Register #(.width(1)) register_29 (
    .D(decoder_1_out27), .en(decoder_1_out27), .clk(decoder_1_out27), .Q(register_29_q), .clr(DCD_FLUSH));
  Register #(.width(1)) register_30 (
    .D(decoder_1_out28), .en(decoder_1_out28), .clk(decoder_1_out28), .Q(register_30_q), .clr(DCD_FLUSH));
  Register #(.width(1)) register_31 (
    .D(decoder_1_out29), .en(decoder_1_out29), .clk(decoder_1_out29), .Q(register_31_q), .clr(DCD_FLUSH));
  Register #(.width(1)) register_32 (
    .D(decoder_1_out30), .en(decoder_1_out30), .clk(decoder_1_out30), .Q(register_32_q), .clr(DCD_FLUSH));
  Register #(.width(1)) register_33 (
    .D(decoder_1_out31), .en(decoder_1_out31), .clk(decoder_1_out31), .Q(register_33_q), .clr(DCD_FLUSH));
  assign O0 = EXEC ? register_2_q : 1'bz;  // Controlled_Buffer controlled_buffer_1
  assign O1 = EXEC ? register_3_q : 1'bz;  // Controlled_Buffer controlled_buffer_2
  assign O2 = EXEC ? register_4_q : 1'bz;  // Controlled_Buffer controlled_buffer_3
  assign O3 = EXEC ? register_5_q : 1'bz;  // Controlled_Buffer controlled_buffer_4
  assign O4 = EXEC ? register_6_q : 1'bz;  // Controlled_Buffer controlled_buffer_5
  assign O5 = EXEC ? register_7_q : 1'bz;  // Controlled_Buffer controlled_buffer_6
  assign O6 = EXEC ? register_8_q : 1'bz;  // Controlled_Buffer controlled_buffer_7
  assign O7 = EXEC ? register_9_q : 1'bz;  // Controlled_Buffer controlled_buffer_8
  assign O8 = EXEC ? register_10_q : 1'bz;  // Controlled_Buffer controlled_buffer_9
  assign O9 = EXEC ? register_11_q : 1'bz;  // Controlled_Buffer controlled_buffer_10
  assign O10 = EXEC ? register_12_q : 1'bz;  // Controlled_Buffer controlled_buffer_11
  assign O11 = EXEC ? register_13_q : 1'bz;  // Controlled_Buffer controlled_buffer_12
  assign O12 = EXEC ? register_14_q : 1'bz;  // Controlled_Buffer controlled_buffer_13
  assign O13 = EXEC ? register_15_q : 1'bz;  // Controlled_Buffer controlled_buffer_14
  assign O14 = EXEC ? register_16_q : 1'bz;  // Controlled_Buffer controlled_buffer_15
  assign O15 = EXEC ? register_17_q : 1'bz;  // Controlled_Buffer controlled_buffer_16
  assign O16 = EXEC ? register_18_q : 1'bz;  // Controlled_Buffer controlled_buffer_17
  assign O17 = EXEC ? register_19_q : 1'bz;  // Controlled_Buffer controlled_buffer_18
  assign O18 = EXEC ? register_20_q : 1'bz;  // Controlled_Buffer controlled_buffer_19
  assign O19 = EXEC ? register_21_q : 1'bz;  // Controlled_Buffer controlled_buffer_20
  assign O20 = EXEC ? register_22_q : 1'bz;  // Controlled_Buffer controlled_buffer_21
  assign O21 = EXEC ? register_23_q : 1'bz;  // Controlled_Buffer controlled_buffer_22
  assign O22 = EXEC ? register_24_q : 1'bz;  // Controlled_Buffer controlled_buffer_23
  assign O23 = EXEC ? register_25_q : 1'bz;  // Controlled_Buffer controlled_buffer_24
  assign O24 = EXEC ? register_26_q : 1'bz;  // Controlled_Buffer controlled_buffer_25
  assign O25 = EXEC ? register_27_q : 1'bz;  // Controlled_Buffer controlled_buffer_26
  assign O26 = EXEC ? register_28_q : 1'bz;  // Controlled_Buffer controlled_buffer_27
  assign O27 = EXEC ? register_29_q : 1'bz;  // Controlled_Buffer controlled_buffer_28
  assign O28 = EXEC ? register_30_q : 1'bz;  // Controlled_Buffer controlled_buffer_29
  assign O29 = EXEC ? register_31_q : 1'bz;  // Controlled_Buffer controlled_buffer_30
  assign O30 = EXEC ? register_32_q : 1'bz;  // Controlled_Buffer controlled_buffer_31
  assign O31 = EXEC ? register_33_q : 1'bz;  // Controlled_Buffer controlled_buffer_32
  Decoder #(.select(4)) decoder_2 (
    .out0(decoder_2_out0), .out1(decoder_2_out1), .out2(decoder_2_out2), .out3(decoder_2_out3),
    .out4(decoder_2_out4), .out5(decoder_2_out5), .out6(decoder_2_out6), .out7(decoder_2_out7),
    .out8(decoder_2_out8), .out9(decoder_2_out9), .out10(decoder_2_out10), .out11(decoder_2_out11),
    .out12(decoder_2_out12), .out13(decoder_2_out13), .out14(decoder_2_out14), .out15(decoder_2_out15),
    .sel(in_4[7:4]));  // open: en
  Decoder #(.select(4)) decoder_3 (
    .sel(in_4[3:0]), .en(decoder_2_out0));  // open: out0, out1, out2, out3, out4, out5, out6, out7, out8, out9, out10, out11, out12, out13, out14, out15
  Decoder #(.select(4)) decoder_4 (
    .sel(in_4[3:0]), .en(decoder_2_out1));  // open: out0, out1, out2, out3, out4, out5, out6, out7, out8, out9, out10, out11, out12, out13, out14, out15
  Decoder #(.select(4)) decoder_5 (
    .sel(in_4[3:0]), .en(decoder_2_out2));  // open: out0, out1, out2, out3, out4, out5, out6, out7, out8, out9, out10, out11, out12, out13, out14, out15
  Decoder #(.select(4)) decoder_6 (
    .sel(in_4[3:0]), .en(decoder_2_out3));  // open: out0, out1, out2, out3, out4, out5, out6, out7, out8, out9, out10, out11, out12, out13, out14, out15
  Decoder #(.select(4)) decoder_7 (
    .sel(in_4[3:0]), .en(decoder_2_out4));  // open: out0, out1, out2, out3, out4, out5, out6, out7, out8, out9, out10, out11, out12, out13, out14, out15
  Decoder #(.select(4)) decoder_8 (
    .sel(in_4[3:0]), .en(decoder_2_out5));  // open: out0, out1, out2, out3, out4, out5, out6, out7, out8, out9, out10, out11, out12, out13, out14, out15
  Decoder #(.select(4)) decoder_9 (
    .sel(in_4[3:0]), .en(decoder_2_out6));  // open: out0, out1, out2, out3, out4, out5, out6, out7, out8, out9, out10, out11, out12, out13, out14, out15
  Decoder #(.select(4)) decoder_10 (
    .sel(in_4[3:0]), .en(decoder_2_out7));  // open: out0, out1, out2, out3, out4, out5, out6, out7, out8, out9, out10, out11, out12, out13, out14, out15
  Decoder #(.select(4)) decoder_11 (
    .sel(in_4[3:0]), .en(decoder_2_out8));  // open: out0, out1, out2, out3, out4, out5, out6, out7, out8, out9, out10, out11, out12, out13, out14, out15
  Decoder #(.select(4)) decoder_12 (
    .sel(in_4[3:0]), .en(decoder_2_out9));  // open: out0, out1, out2, out3, out4, out5, out6, out7, out8, out9, out10, out11, out12, out13, out14, out15
  Decoder #(.select(4)) decoder_13 (
    .sel(in_4[3:0]), .en(decoder_2_out10));  // open: out0, out1, out2, out3, out4, out5, out6, out7, out8, out9, out10, out11, out12, out13, out14, out15
  Decoder #(.select(4)) decoder_14 (
    .sel(in_4[3:0]), .en(decoder_2_out11));  // open: out0, out1, out2, out3, out4, out5, out6, out7, out8, out9, out10, out11, out12, out13, out14, out15
  Decoder #(.select(4)) decoder_15 (
    .sel(in_4[3:0]), .en(decoder_2_out12));  // open: out0, out1, out2, out3, out4, out5, out6, out7, out8, out9, out10, out11, out12, out13, out14, out15
  Decoder #(.select(4)) decoder_16 (
    .sel(in_4[3:0]), .en(decoder_2_out13));  // open: out0, out1, out2, out3, out4, out5, out6, out7, out8, out9, out10, out11, out12, out13, out14, out15
  Decoder #(.select(4)) decoder_17 (
    .sel(in_4[3:0]), .en(decoder_2_out14));  // open: out0, out1, out2, out3, out4, out5, out6, out7, out8, out9, out10, out11, out12, out13, out14, out15
  Decoder #(.select(4)) decoder_18 (
    .sel(in_4[3:0]), .en(decoder_2_out15));  // open: out0, out1, out2, out3, out4, out5, out6, out7, out8, out9, out10, out11, out12, out13, out14, out15
endmodule

module PC (
  input  RESET,
  input  JUMP,
  input  COUNTER_ENB,
  input  CLOCK,
  input  [9:0] ADDR_IN,
  input  COUNTER_OUT,
  output [9:0] ALWAYS_OUT,
  output [9:0] ADDR_OUT
);

  Counter #(.max('h3ff), .width(10)) counter_1 (
    .clr(RESET), .load(JUMP), .up(COUNTER_ENB), .count(COUNTER_ENB), .clk(CLOCK), .D(ADDR_IN), .Q(ALWAYS_OUT));  // open: carry
  assign ADDR_OUT = COUNTER_OUT ? ALWAYS_OUT : 10'bz;  // Controlled_Buffer controlled_buffer_1
endmodule

module R0 (
  input  [15:0] DATA_IN,
  input  A_IN,
  input  A_OUT,
  input  CLOCK,
  input  A_RESET,
  output [15:0] ALWAYS_OUT,
  output [15:0] DATA_OUT
);

  Register #(.width(16)) register_1 (.D(DATA_IN), .en(A_IN), .clk(CLOCK), .Q(ALWAYS_OUT), .clr(A_RESET));
  assign DATA_OUT = A_OUT ? ALWAYS_OUT : 16'bz;  // Controlled_Buffer controlled_buffer_1
endmodule

module R1 (
  input  [15:0] DATA_IN,
  input  B_IN,
  input  B_OUT,
  input  CLOCK,
  input  B_RESET,
  output [15:0] ALWAYS_OUT,
  output [15:0] DATA_OUT
);

  Register #(.width(16)) register_1 (.D(DATA_IN), .en(B_IN), .clk(CLOCK), .Q(ALWAYS_OUT), .clr(B_RESET));
  assign DATA_OUT = B_OUT ? ALWAYS_OUT : 16'bz;  // Controlled_Buffer controlled_buffer_1
endmodule

module I_REG (
  input  [5:0] DATA_IN,
  input  STORE,
  input  CLOCK,
  input  RESET,
  input  DATA_OUT_ENB,
  output [5:0] ALWAYS_OUT,
  output [5:0] DATA_OUT
);

  Register #(.width(6)) register_1 (.D(DATA_IN), .en(STORE), .clk(CLOCK), .Q(ALWAYS_OUT), .clr(RESET));
  assign DATA_OUT = DATA_OUT_ENB ? ALWAYS_OUT : 6'bz;  // Controlled_Buffer controlled_buffer_1
endmodule

module S_CTN (
  input  RESET,
  input  CLOCK,
  output [3:0] BINARY_OUT
);

  Counter #(.max('hf), .width(4)) counter_1 (
    .clr(RESET), .up(1'b1), .count(1'b1), .clk(CLOCK), .Q(BINARY_OUT));  // open: load, D, carry
endmodule

module O_REG (
  input  [12:0] DATA_IN,
  input  STORE,
  input  CLOCK,
  input  RESET,
  output [12:0] DATA_OUT
);

  Register #(.width(13)) register_1 (.D(DATA_IN), .en(STORE), .clk(CLOCK), .Q(DATA_OUT), .clr(RESET));
endmodule

module F_REG (
  input  CARRY,
  input  ZERO,
  input  STORE,
  input  CLOCK,
  input  RESET,
  output CARRY_OUT,
  output ZERO_OUT
);

  Register #(.width(1)) register_1 (.D(CARRY), .en(STORE), .clk(CLOCK), .Q(CARRY_OUT), .clr(RESET));
  Register #(.width(1)) register_2 (.D(ZERO), .en(STORE), .clk(CLOCK), .Q(ZERO_OUT), .clr(RESET));
endmodule

module ZF_REG (
  input  [15:0] in_1,
  output ZERO
);

  wire or_1_out, or_2_out, or_3_out, or_4_out, or_5_out, or_6_out, or_7_out, or_8_out, or_9_out, or_10_out,
       or_11_out, or_12_out, or_13_out, or_14_out, or_15_out;

  or or_1 (or_1_out, in_1[0], in_1[1]);
  or or_2 (or_2_out, in_1[2], in_1[3]);
  or or_3 (or_3_out, in_1[4], in_1[5]);
  or or_4 (or_4_out, in_1[6], in_1[7]);
  or or_5 (or_5_out, in_1[8], in_1[9]);
  or or_6 (or_6_out, in_1[10], in_1[11]);
  or or_7 (or_7_out, in_1[12], in_1[13]);
  or or_8 (or_8_out, in_1[14], in_1[15]);
  or or_9 (or_9_out, or_1_out, or_2_out);
  or or_10 (or_10_out, or_3_out, or_4_out);
  or or_11 (or_11_out, or_5_out, or_6_out);
  or or_12 (or_12_out, or_7_out, or_8_out);
  or or_13 (or_13_out, or_9_out, or_10_out);
  or or_14 (or_14_out, or_11_out, or_12_out);
  or or_15 (or_15_out, or_13_out, or_14_out);
  not not_1 (ZERO, or_15_out);
endmodule

module MAR_REG (
  input  [9:0] DATA_IN,
  input  MAR_IN,
  input  CLOCK,
  input  MAR_RESET,
  input  MAR_OUT,
  output [9:0] ALWAYS_OUT,
  output [9:0] DATA_OUT
);

  Register #(.width(10)) register_1 (.D(DATA_IN), .en(MAR_IN), .clk(CLOCK), .Q(ALWAYS_OUT), .clr(MAR_RESET));
  assign DATA_OUT = MAR_OUT ? ALWAYS_OUT : 10'bz;  // Controlled_Buffer controlled_buffer_1
endmodule

module RESULT_REG (
  input  [15:0] DATA_IN,
  input  R_IN,
  input  R_OUT,
  input  CLOCK,
  input  R_RESET,
  output [15:0] ALWAYS_OUT,
  output [15:0] DATA_OUT
);

  Register #(.width(16)) register_1 (.D(DATA_IN), .en(R_IN), .clk(CLOCK), .Q(ALWAYS_OUT), .clr(R_RESET));
  assign DATA_OUT = R_OUT ? ALWAYS_OUT : 16'bz;  // Controlled_Buffer controlled_buffer_1
endmodule

module OPR_REG (
  input  [9:0] DATA_IN,
  input  STORE,
  input  CLOCK,
  input  RESET,
  input  DATA_OUT_ENB,
  output [9:0] ALWAYS_OUT,
  output [9:0] DATA_OUT
);

  Register #(.width(10)) register_1 (.D(DATA_IN), .en(STORE), .clk(CLOCK), .Q(ALWAYS_OUT), .clr(RESET));
  assign DATA_OUT = DATA_OUT_ENB ? ALWAYS_OUT : 10'bz;  // Controlled_Buffer controlled_buffer_1
endmodule

module MEM (
  input  [9:0] ADDRESS,
  input  [15:0] DATA,
  input  STORE,
  input  CLOCK,
  input  RAM_OUT_ENB,
  output [15:0] ALWAYS_OUT,
  output [15:0] RAM_OUT
);

  RAM #(.addrWidth(10), .dataWidth(16)) ram_1 (
    .addr(ADDRESS), .we(STORE), .oe(RAM_OUT_ENB), .clk(CLOCK), .din(DATA), .dout(ALWAYS_OUT));
  assign RAM_OUT = RAM_OUT_ENB ? ALWAYS_OUT : 16'bz;  // Controlled_Buffer controlled_buffer_1
endmodule

module DCD_CTRL (
  input  I5,
  input  I4,
  input  l3,
  input  I2,
  input  I1,
  input  I0,
  output O0
);

  wire and_1_out, and_2_out, and_3_out, and_4_out, and_5_out, and_6_out, or_1_out, or_2_out, or_3_out,
       or_4_out;

  LED led_1 (.in(I5));
  LED led_2 (.in(I4));
  Pull_Resistor pull_resistor_1 (.node(I5));
  Pull_Resistor pull_resistor_2 (.node(I4));
  LED led_3 (.in(l3));
  LED led_4 (.in(I2));
  LED led_5 (.in(I1));
  LED led_6 (.in(I0));
  Pull_Resistor pull_resistor_3 (.node(l3));
  Pull_Resistor pull_resistor_4 (.node(I2));
  Pull_Resistor pull_resistor_5 (.node(I1));
  Pull_Resistor pull_resistor_6 (.node(I0));
  and and_1 (and_1_out, I0, 1'b1);
  and and_2 (and_2_out, I1, 1'b1);
  and and_3 (and_3_out, I2, 1'b1);
  and and_4 (and_4_out, l3, 1'b1);
  and and_5 (and_5_out, I4, 1'b1);
  and and_6 (and_6_out, I5, 1'b1);
  or or_1 (or_1_out, and_1_out, and_2_out);
  or or_2 (or_2_out, and_3_out, and_4_out);
  or or_3 (or_3_out, and_5_out, and_6_out);
  or or_4 (or_4_out, or_1_out, or_2_out);
  or or_5 (O0, or_4_out, or_3_out);
endmodule

module JMP_DCD (
  input  JZ,
  input  ZERO,
  input  JUMP,
  output J_OUT
);

  wire and_1_out;

  or or_1 (J_OUT, and_1_out, JUMP);
  and and_1 (and_1_out, JZ, ZERO);
endmodule

module CLK (
  input  CLK_IN,
  input  CLK_ENB,
  input  MANUAL_CLK,
  input  HALT,
  output CLK_OUT
);

  wire and_1_out, and_2_out, not_1_out, not_2_out, or_1_out;

  not not_1 (not_1_out, HALT);
  not not_2 (not_2_out, CLK_ENB);
  and and_1 (and_1_out, CLK_IN, CLK_ENB);
  and and_2 (and_2_out, not_2_out, MANUAL_CLK);
  or or_1 (or_1_out, and_1_out, and_2_out);
  and and_3 (CLK_OUT, or_1_out, not_1_out);
endmodule

module ALU (
  input  [15:0] A_IN,
  input  [15:0] B_IN,
  input  OUTPUT_ENB,
  input  SUB,
  output [15:0] ALWAYS_OUT,
  output [15:0] A_OUT,
  output COUT
);

  wire not_1_out;
  wire [15:0] controlled_buffer_1_out, xor_1_out;

  assign controlled_buffer_1_out = SUB ? {16{1'b1}} : 16'bz;  // Controlled_Buffer controlled_buffer_1
  not not_1 (not_1_out, SUB);
  assign controlled_buffer_1_out = not_1_out ? {16{1'b0}} : 16'bz;  // Controlled_Buffer controlled_buffer_2
  assign xor_1_out = B_IN ^ controlled_buffer_1_out;  // XOR_Gate xor_1, 16 bits wide
  Adder #(.width(16)) adder_1 (.a(A_IN), .b(xor_1_out), .out(ALWAYS_OUT), .cin(SUB), .cout(COUT));
  assign A_OUT = OUTPUT_ENB ? ALWAYS_OUT : 16'bz;  // Controlled_Buffer controlled_buffer_3
endmodule

module DCD_2 (
  input  DCD_RESET,
  input  [5:0] SELECTOR,
  input  ENB,
  input  EXEC,
  output O0,
  output O1,
  output O2,
  output O3,
  output O4,
  output O5,
  output O6,
  output O7,
  output [5:0] DCD_OUT,
  output O8,
  output O9,
  output O10,
  output O11,
  output O12,
  output O13,
  output O14,
  output O15,
  output O16,
  output O17,
  output O18,
  output O19,
  output O20,
  output O21,
  output O22,
  output O23,
  output O24,
  output O25,
  output O26,
  output O27,
  output O28,
  output O29,
  output O30,
  output O31,
  output O32,
  output O33,
  output O34,
  output O35,
  output O36,
  output O37,
  output O38,
  output O39,
  output O40,
  output O41,
  output O42,
  output O43,
  output O44,
  output O45,
  output O46,
  output O47,
  output O48,
  output O49,
  output O50,
  output O51,
  output O52,
  output O53,
  output O54,
  output O55,
  output O56,
  output O57,
  output O58,
  output O59,
  output O60,
  output O61,
  output O62,
  output O63,
  output O64
);

  wire decoder_1_out0, decoder_1_out1, decoder_1_out2, decoder_1_out3, decoder_2_out0, decoder_2_out1,
       decoder_2_out2, decoder_2_out3, decoder_2_out4, decoder_2_out5, decoder_2_out6, decoder_2_out7,
       decoder_2_out8, decoder_2_out9, decoder_2_out10, decoder_2_out11, decoder_2_out12, decoder_2_out13,
       decoder_2_out14, decoder_2_out15, decoder_3_out0, decoder_3_out1, decoder_3_out2, decoder_3_out3,
       decoder_3_out4, decoder_3_out5, decoder_3_out6, decoder_3_out7, decoder_3_out8, decoder_3_out9,
       decoder_3_out10, decoder_3_out11, decoder_3_out12, decoder_3_out13, decoder_3_out14, decoder_3_out15,
       decoder_4_out0, decoder_4_out1, decoder_4_out2, decoder_4_out3, decoder_4_out4, decoder_4_out5,
       decoder_4_out6, decoder_4_out7, decoder_4_out8, decoder_4_out9, decoder_4_out10, decoder_4_out11,
       decoder_4_out12, decoder_4_out13, decoder_4_out14, decoder_4_out15, decoder_5_out0, decoder_5_out1,
       decoder_5_out2, decoder_5_out3, decoder_5_out4, decoder_5_out5, decoder_5_out6, decoder_5_out7,
       decoder_5_out8, decoder_5_out9, decoder_5_out10, decoder_5_out11, decoder_5_out12, decoder_5_out13,
       decoder_5_out14, decoder_5_out15, register_2_q, register_3_q, register_4_q, register_5_q,
       register_6_q, register_7_q, register_8_q, register_9_q, register_10_q, register_11_q, register_12_q,
       register_13_q, register_14_q, register_15_q, register_16_q, register_17_q, register_18_q,
       register_19_q, register_20_q, register_21_q, register_22_q, register_23_q, register_24_q,
       register_25_q, register_26_q, register_27_q, register_28_q, register_29_q, register_30_q,
       register_31_q, register_32_q, register_33_q, register_34_q, register_35_q, register_36_q,
       register_37_q, register_38_q, register_39_q, register_40_q, register_41_q, register_42_q,
       register_43_q, register_44_q, register_45_q, register_46_q, register_47_q, register_48_q,
       register_49_q, register_50_q, register_51_q, register_52_q, register_53_q, register_54_q,
       register_55_q, register_56_q, register_57_q, register_58_q, register_59_q, register_60_q,
       register_61_q, register_62_q, register_63_q, register_64_q, register_65_q, register_66_q;

  Decoder #(.select(2)) decoder_1 (
    .out0(decoder_1_out0), .out1(decoder_1_out1), .out2(decoder_1_out2), .out3(decoder_1_out3),
    .sel(SELECTOR[5:4]), .en(ENB));
  Register #(.width(6)) register_1 (.D(SELECTOR), .en(ENB), .clk(ENB), .Q(DCD_OUT), .clr(DCD_RESET));
  Decoder #(.select(4)) decoder_2 (
    .out0(decoder_2_out0), .out1(decoder_2_out1), .out2(decoder_2_out2), .out3(decoder_2_out3),
    .out4(decoder_2_out4), .out5(decoder_2_out5), .out6(decoder_2_out6), .out7(decoder_2_out7),
    .out8(decoder_2_out8), .out9(decoder_2_out9), .out10(decoder_2_out10), .out11(decoder_2_out11),
    .out12(decoder_2_out12), .out13(decoder_2_out13), .out14(decoder_2_out14), .out15(decoder_2_out15),
    .sel(SELECTOR[3:0]), .en(decoder_1_out0));
  Decoder #(.select(4)) decoder_3 (
    .out0(decoder_3_out0), .out1(decoder_3_out1), .out2(decoder_3_out2), .out3(decoder_3_out3),
    .out4(decoder_3_out4), .out5(decoder_3_out5), .out6(decoder_3_out6), .out7(decoder_3_out7),
    .out8(decoder_3_out8), .out9(decoder_3_out9), .out10(decoder_3_out10), .out11(decoder_3_out11),
    .out12(decoder_3_out12), .out13(decoder_3_out13), .out14(decoder_3_out14), .out15(decoder_3_out15),
    .sel(SELECTOR[3:0]), .en(decoder_1_out1));
  Decoder #(.select(4)) decoder_4 (
    .out0(decoder_4_out0), .out1(decoder_4_out1), .out2(decoder_4_out2), .out3(decoder_4_out3),
    .out4(decoder_4_out4), .out5(decoder_4_out5), .out6(decoder_4_out6), .out7(decoder_4_out7),
    .out8(decoder_4_out8), .out9(decoder_4_out9), .out10(decoder_4_out10), .out11(decoder_4_out11),
    .out12(decoder_4_out12), .out13(decoder_4_out13), .out14(decoder_4_out14), .out15(decoder_4_out15),
    .sel(SELECTOR[3:0]), .en(decoder_1_out2));
  Decoder #(.select(4)) decoder_5 (
    .out0(decoder_5_out0), .out1(decoder_5_out1), .out2(decoder_5_out2), .out3(decoder_5_out3),
    .out4(decoder_5_out4), .out5(decoder_5_out5), .out6(decoder_5_out6), .out7(decoder_5_out7),
    .out8(decoder_5_out8), .out9(decoder_5_out9), .out10(decoder_5_out10), .out11(decoder_5_out11),
    .out12(decoder_5_out12), .out13(decoder_5_out13), .out14(decoder_5_out14), .out15(decoder_5_out15),
    .en(decoder_1_out3));  // open: sel
  Register #(.width(1)) register_2 (
    .D(decoder_2_out0), .en(decoder_2_out0), .clk(decoder_2_out0), .Q(register_2_q), .clr(DCD_RESET));
  Register #(.width(1)) register_3 (
    .D(decoder_2_out1), .en(decoder_2_out1), .clk(decoder_2_out1), .Q(register_3_q), .clr(DCD_RESET));
  Register #(.width(1)) register_4 (
    .D(decoder_2_out1), .en(decoder_2_out1), .clk(decoder_2_out1), .Q(register_4_q), .clr(DCD_RESET));
  Register #(.width(1)) register_5 (
    .D(decoder_2_out2), .en(decoder_2_out2), .clk(decoder_2_out2), .Q(register_5_q), .clr(DCD_RESET));
  Register #(.width(1)) register_6 (
    .D(decoder_2_out3), .en(decoder_2_out3), .clk(decoder_2_out3), .Q(register_6_q), .clr(DCD_RESET));
  Register #(.width(1)) register_7 (
    .D(decoder_2_out4), .en(decoder_2_out4), .clk(decoder_2_out4), .Q(register_7_q), .clr(DCD_RESET));
  Register #(.width(1)) register_8 (
    .D(decoder_2_out5), .en(decoder_2_out5), .clk(decoder_2_out5), .Q(register_8_q), .clr(DCD_RESET));
  Register #(.width(1)) register_9 (
    .D(decoder_2_out6), .en(decoder_2_out6), .clk(decoder_2_out6), .Q(register_9_q), .clr(DCD_RESET));
  Register #(.width(1)) register_10 (
    .D(decoder_2_out7), .en(decoder_2_out7), .clk(decoder_2_out7), .Q(register_10_q), .clr(DCD_RESET));
  Register #(.width(1)) register_11 (
    .D(decoder_2_out8), .en(decoder_2_out8), .clk(decoder_2_out8), .Q(register_11_q), .clr(DCD_RESET));
  Register #(.width(1)) register_12 (
    .D(decoder_2_out9), .en(decoder_2_out9), .clk(decoder_2_out9), .Q(register_12_q), .clr(DCD_RESET));
  Register #(.width(1)) register_13 (
    .D(decoder_2_out10), .en(decoder_2_out10), .clk(decoder_2_out10), .Q(register_13_q), .clr(DCD_RESET));
  Register #(.width(1)) register_14 (
    .D(decoder_2_out11), .en(decoder_2_out11), .clk(decoder_2_out11), .Q(register_14_q), .clr(DCD_RESET));
  Register #(.width(1)) register_15 (
    .D(decoder_2_out12), .en(decoder_2_out12), .clk(decoder_2_out12), .Q(register_15_q), .clr(DCD_RESET));
  Register #(.width(1)) register_16 (
    .D(decoder_2_out13), .en(decoder_2_out13), .clk(decoder_2_out13), .Q(register_16_q), .clr(DCD_RESET));
  Register #(.width(1)) register_17 (
    .D(decoder_2_out14), .en(decoder_2_out14), .clk(decoder_2_out14), .Q(register_17_q), .clr(DCD_RESET));
  Register #(.width(1)) register_18 (
    .D(decoder_2_out15), .en(decoder_2_out15), .clk(decoder_2_out15), .Q(register_18_q), .clr(DCD_RESET));
  Register #(.width(1)) register_19 (
    .D(decoder_3_out0), .en(decoder_3_out0), .clk(decoder_3_out0), .Q(register_19_q), .clr(DCD_RESET));
  Register #(.width(1)) register_20 (
    .D(decoder_3_out1), .en(decoder_3_out1), .clk(decoder_3_out1), .Q(register_20_q), .clr(DCD_RESET));
  Register #(.width(1)) register_21 (
    .D(decoder_3_out2), .en(decoder_3_out2), .clk(decoder_3_out2), .Q(register_21_q), .clr(DCD_RESET));
  Register #(.width(1)) register_22 (
    .D(decoder_3_out3), .en(decoder_3_out3), .clk(decoder_3_out3), .Q(register_22_q), .clr(DCD_RESET));
  Register #(.width(1)) register_23 (
    .D(decoder_3_out4), .en(decoder_3_out4), .clk(decoder_3_out4), .Q(register_23_q), .clr(DCD_RESET));
  Register #(.width(1)) register_24 (
    .D(decoder_3_out5), .en(decoder_3_out5), .clk(decoder_3_out5), .Q(register_24_q), .clr(DCD_RESET));
  Register #(.width(1)) register_25 (
    .D(decoder_3_out6), .en(decoder_3_out6), .clk(decoder_3_out6), .Q(register_25_q), .clr(DCD_RESET));
  Register #(.width(1)) register_26 (
    .D(decoder_3_out7), .en(decoder_3_out7), .clk(decoder_3_out7), .Q(register_26_q), .clr(DCD_RESET));
  Register #(.width(1)) register_27 (
    .D(decoder_3_out8), .en(decoder_3_out8), .clk(decoder_3_out8), .Q(register_27_q), .clr(DCD_RESET));
  Register #(.width(1)) register_28 (
    .D(decoder_3_out9), .en(decoder_3_out9), .clk(decoder_3_out9), .Q(register_28_q), .clr(DCD_RESET));
  Register #(.width(1)) register_29 (
    .D(decoder_3_out10), .en(decoder_3_out10), .clk(decoder_3_out10), .Q(register_29_q), .clr(DCD_RESET));
  Register #(.width(1)) register_30 (
    .D(decoder_3_out11), .en(decoder_3_out11), .clk(decoder_3_out11), .Q(register_30_q), .clr(DCD_RESET));
  Register #(.width(1)) register_31 (
    .D(decoder_3_out12), .en(decoder_3_out12), .clk(decoder_3_out12), .Q(register_31_q), .clr(DCD_RESET));
  Register #(.width(1)) register_32 (
    .D(decoder_3_out13), .en(decoder_3_out13), .clk(decoder_3_out13), .Q(register_32_q), .clr(DCD_RESET));
  Register #(.width(1)) register_33 (
    .D(decoder_3_out14), .en(decoder_3_out14), .clk(decoder_3_out14), .Q(register_33_q), .clr(DCD_RESET));
  Register #(.width(1)) register_34 (
    .D(decoder_3_out15), .en(decoder_3_out15), .clk(decoder_3_out15), .Q(register_34_q), .clr(DCD_RESET));
  Register #(.width(1)) register_35 (
    .D(decoder_4_out0), .en(decoder_4_out0), .clk(decoder_4_out0), .Q(register_35_q), .clr(DCD_RESET));
  Register #(.width(1)) register_36 (
    .D(decoder_4_out1), .en(decoder_4_out1), .clk(decoder_4_out1), .Q(register_36_q), .clr(DCD_RESET));
  Register #(.width(1)) register_37 (
    .D(decoder_4_out2), .en(decoder_4_out2), .clk(decoder_4_out2), .Q(register_37_q), .clr(DCD_RESET));
  Register #(.width(1)) register_38 (
    .D(decoder_4_out3), .en(decoder_4_out3), .clk(decoder_4_out3), .Q(register_38_q), .clr(DCD_RESET));
  Register #(.width(1)) register_39 (
    .D(decoder_4_out4), .en(decoder_4_out4), .clk(decoder_4_out4), .Q(register_39_q), .clr(DCD_RESET));
  Register #(.width(1)) register_40 (
    .D(decoder_4_out5), .en(decoder_4_out5), .clk(decoder_4_out5), .Q(register_40_q), .clr(DCD_RESET));
  Register #(.width(1)) register_41 (
    .D(decoder_4_out6), .en(decoder_4_out6), .clk(decoder_4_out6), .Q(register_41_q), .clr(DCD_RESET));
  Register #(.width(1)) register_42 (
    .D(decoder_4_out7), .en(decoder_4_out7), .clk(decoder_4_out7), .Q(register_42_q), .clr(DCD_RESET));
  Register #(.width(1)) register_43 (
    .D(decoder_4_out8), .en(decoder_4_out8), .clk(decoder_4_out8), .Q(register_43_q), .clr(DCD_RESET));
  Register #(.width(1)) register_44 (
    .D(decoder_4_out9), .en(decoder_4_out9), .clk(decoder_4_out9), .Q(register_44_q), .clr(DCD_RESET));
  Register #(.width(1)) register_45 (
    .D(decoder_4_out10), .en(decoder_4_out10), .clk(decoder_4_out10), .Q(register_45_q), .clr(DCD_RESET));
  Register #(.width(1)) register_46 (
    .D(decoder_4_out11), .en(decoder_4_out11), .clk(decoder_4_out11), .Q(register_46_q), .clr(DCD_RESET));
  Register #(.width(1)) register_47 (
    .D(decoder_4_out12), .en(decoder_4_out12), .clk(decoder_4_out12), .Q(register_47_q), .clr(DCD_RESET));
  Register #(.width(1)) register_48 (
    .D(decoder_4_out13), .en(decoder_4_out13), .clk(decoder_4_out13), .Q(register_48_q), .clr(DCD_RESET));
  Register #(.width(1)) register_49 (
    .D(decoder_4_out14), .en(decoder_4_out14), .clk(decoder_4_out14), .Q(register_49_q), .clr(DCD_RESET));
  Register #(.width(1)) register_50 (
    .D(decoder_4_out15), .en(decoder_4_out15), .clk(decoder_4_out15), .Q(register_50_q), .clr(DCD_RESET));
  Register #(.width(1)) register_51 (
    .D(decoder_5_out0), .en(decoder_5_out0), .clk(decoder_5_out0), .Q(register_51_q), .clr(DCD_RESET));
  Register #(.width(1)) register_52 (
    .D(decoder_5_out1), .en(decoder_5_out1), .clk(decoder_5_out1), .Q(register_52_q), .clr(DCD_RESET));
  Register #(.width(1)) register_53 (
    .D(decoder_5_out2), .en(decoder_5_out2), .clk(decoder_5_out2), .Q(register_53_q), .clr(DCD_RESET));
  Register #(.width(1)) register_54 (
    .D(decoder_5_out3), .en(decoder_5_out3), .clk(decoder_5_out3), .Q(register_54_q), .clr(DCD_RESET));
  Register #(.width(1)) register_55 (
    .D(decoder_5_out4), .en(decoder_5_out4), .clk(decoder_5_out4), .Q(register_55_q), .clr(DCD_RESET));
  Register #(.width(1)) register_56 (
    .D(decoder_5_out5), .en(decoder_5_out5), .clk(decoder_5_out5), .Q(register_56_q), .clr(DCD_RESET));
  Register #(.width(1)) register_57 (
    .D(decoder_5_out6), .en(decoder_5_out6), .clk(decoder_5_out6), .Q(register_57_q), .clr(DCD_RESET));
  Register #(.width(1)) register_58 (
    .D(decoder_5_out7), .en(decoder_5_out7), .clk(decoder_5_out7), .Q(register_58_q), .clr(DCD_RESET));
  Register #(.width(1)) register_59 (
    .D(decoder_5_out8), .en(decoder_5_out8), .clk(decoder_5_out8), .Q(register_59_q), .clr(DCD_RESET));
  Register #(.width(1)) register_60 (
    .D(decoder_5_out9), .en(decoder_5_out9), .clk(decoder_5_out9), .Q(register_60_q), .clr(DCD_RESET));
  Register #(.width(1)) register_61 (
    .D(decoder_5_out10), .en(decoder_5_out10), .clk(decoder_5_out10), .Q(register_61_q), .clr(DCD_RESET));
  Register #(.width(1)) register_62 (
    .D(decoder_5_out11), .en(decoder_5_out11), .clk(decoder_5_out11), .Q(register_62_q), .clr(DCD_RESET));
  Register #(.width(1)) register_63 (
    .D(decoder_5_out12), .en(decoder_5_out12), .clk(decoder_5_out12), .Q(register_63_q), .clr(DCD_RESET));
  Register #(.width(1)) register_64 (
    .D(decoder_5_out13), .en(decoder_5_out13), .clk(decoder_5_out13), .Q(register_64_q), .clr(DCD_RESET));
  Register #(.width(1)) register_65 (
    .D(decoder_5_out14), .en(decoder_5_out14), .clk(decoder_5_out14), .Q(register_65_q), .clr(DCD_RESET));
  Register #(.width(1)) register_66 (
    .D(decoder_5_out15), .en(decoder_5_out15), .clk(decoder_5_out15), .Q(register_66_q), .clr(DCD_RESET));
  assign O0 = EXEC ? register_2_q : 1'bz;  // Controlled_Buffer controlled_buffer_1
  assign O1 = EXEC ? register_3_q : 1'bz;  // Controlled_Buffer controlled_buffer_2
  assign O2 = EXEC ? register_4_q : 1'bz;  // Controlled_Buffer controlled_buffer_3
  assign O3 = EXEC ? register_5_q : 1'bz;  // Controlled_Buffer controlled_buffer_4
  assign O4 = EXEC ? register_6_q : 1'bz;  // Controlled_Buffer controlled_buffer_5
  assign O5 = EXEC ? register_7_q : 1'bz;  // Controlled_Buffer controlled_buffer_6
  assign O6 = EXEC ? register_8_q : 1'bz;  // Controlled_Buffer controlled_buffer_7
  assign O7 = EXEC ? register_9_q : 1'bz;  // Controlled_Buffer controlled_buffer_8
  assign O8 = EXEC ? register_10_q : 1'bz;  // Controlled_Buffer controlled_buffer_9
  assign O9 = EXEC ? register_11_q : 1'bz;  // Controlled_Buffer controlled_buffer_10
  assign O10 = EXEC ? register_12_q : 1'bz;  // Controlled_Buffer controlled_buffer_11
  assign O11 = EXEC ? register_13_q : 1'bz;  // Controlled_Buffer controlled_buffer_12
  assign O12 = EXEC ? register_14_q : 1'bz;  // Controlled_Buffer controlled_buffer_13
  assign O13 = EXEC ? register_15_q : 1'bz;  // Controlled_Buffer controlled_buffer_14
  assign O14 = EXEC ? register_16_q : 1'bz;  // Controlled_Buffer controlled_buffer_15
  assign O15 = EXEC ? register_17_q : 1'bz;  // Controlled_Buffer controlled_buffer_16
  assign O16 = EXEC ? register_18_q : 1'bz;  // Controlled_Buffer controlled_buffer_17
  assign O17 = EXEC ? register_19_q : 1'bz;  // Controlled_Buffer controlled_buffer_18
  assign O18 = EXEC ? register_20_q : 1'bz;  // Controlled_Buffer controlled_buffer_19
  assign O19 = EXEC ? register_21_q : 1'bz;  // Controlled_Buffer controlled_buffer_20
  assign O20 = EXEC ? register_22_q : 1'bz;  // Controlled_Buffer controlled_buffer_21
  assign O21 = EXEC ? register_23_q : 1'bz;  // Controlled_Buffer controlled_buffer_22
  assign O22 = EXEC ? register_24_q : 1'bz;  // Controlled_Buffer controlled_buffer_23
  assign O23 = EXEC ? register_25_q : 1'bz;  // Controlled_Buffer controlled_buffer_24
  assign O24 = EXEC ? register_26_q : 1'bz;  // Controlled_Buffer controlled_buffer_25
  assign O25 = EXEC ? register_27_q : 1'bz;  // Controlled_Buffer controlled_buffer_26
  assign O26 = EXEC ? register_28_q : 1'bz;  // Controlled_Buffer controlled_buffer_27
  assign O27 = EXEC ? register_29_q : 1'bz;  // Controlled_Buffer controlled_buffer_28
  assign O28 = EXEC ? register_30_q : 1'bz;  // Controlled_Buffer controlled_buffer_29
  assign O29 = EXEC ? register_31_q : 1'bz;  // Controlled_Buffer controlled_buffer_30
  assign O30 = EXEC ? register_32_q : 1'bz;  // Controlled_Buffer controlled_buffer_31
  assign O31 = EXEC ? register_33_q : 1'bz;  // Controlled_Buffer controlled_buffer_32
  assign O32 = EXEC ? register_34_q : 1'bz;  // Controlled_Buffer controlled_buffer_33
  assign O33 = EXEC ? register_35_q : 1'bz;  // Controlled_Buffer controlled_buffer_34
  assign O34 = EXEC ? register_36_q : 1'bz;  // Controlled_Buffer controlled_buffer_35
  assign O35 = EXEC ? register_37_q : 1'bz;  // Controlled_Buffer controlled_buffer_36
  assign O36 = EXEC ? register_38_q : 1'bz;  // Controlled_Buffer controlled_buffer_37
  assign O37 = EXEC ? register_39_q : 1'bz;  // Controlled_Buffer controlled_buffer_38
  assign O38 = EXEC ? register_40_q : 1'bz;  // Controlled_Buffer controlled_buffer_39
  assign O39 = EXEC ? register_41_q : 1'bz;  // Controlled_Buffer controlled_buffer_40
  assign O40 = EXEC ? register_42_q : 1'bz;  // Controlled_Buffer controlled_buffer_41
  assign O41 = EXEC ? register_43_q : 1'bz;  // Controlled_Buffer controlled_buffer_42
  assign O42 = EXEC ? register_44_q : 1'bz;  // Controlled_Buffer controlled_buffer_43
  assign O43 = EXEC ? register_45_q : 1'bz;  // Controlled_Buffer controlled_buffer_44
  assign O44 = EXEC ? register_46_q : 1'bz;  // Controlled_Buffer controlled_buffer_45
  assign O45 = EXEC ? register_47_q : 1'bz;  // Controlled_Buffer controlled_buffer_46
  assign O46 = EXEC ? register_48_q : 1'bz;  // Controlled_Buffer controlled_buffer_47
  assign O47 = EXEC ? register_49_q : 1'bz;  // Controlled_Buffer controlled_buffer_48
  assign O48 = EXEC ? register_50_q : 1'bz;  // Controlled_Buffer controlled_buffer_49
  assign O49 = EXEC ? register_51_q : 1'bz;  // Controlled_Buffer controlled_buffer_50
  assign O50 = EXEC ? register_52_q : 1'bz;  // Controlled_Buffer controlled_buffer_51
  assign O51 = EXEC ? register_53_q : 1'bz;  // Controlled_Buffer controlled_buffer_52
  assign O52 = EXEC ? register_54_q : 1'bz;  // Controlled_Buffer controlled_buffer_53
  assign O53 = EXEC ? register_55_q : 1'bz;  // Controlled_Buffer controlled_buffer_54
  assign O54 = EXEC ? register_56_q : 1'bz;  // Controlled_Buffer controlled_buffer_55
  assign O55 = EXEC ? register_57_q : 1'bz;  // Controlled_Buffer controlled_buffer_56
  assign O56 = EXEC ? register_58_q : 1'bz;  // Controlled_Buffer controlled_buffer_57
  assign O57 = EXEC ? register_59_q : 1'bz;  // Controlled_Buffer controlled_buffer_58
  assign O58 = EXEC ? register_60_q : 1'bz;  // Controlled_Buffer controlled_buffer_59
  assign O59 = EXEC ? register_61_q : 1'bz;  // Controlled_Buffer controlled_buffer_60
  assign O60 = EXEC ? register_62_q : 1'bz;  // Controlled_Buffer controlled_buffer_61
  assign O61 = EXEC ? register_63_q : 1'bz;  // Controlled_Buffer controlled_buffer_62
  assign O62 = EXEC ? register_64_q : 1'bz;  // Controlled_Buffer controlled_buffer_63
  assign O63 = EXEC ? register_65_q : 1'bz;  // Controlled_Buffer controlled_buffer_64
  assign O64 = EXEC ? register_66_q : 1'bz;  // Controlled_Buffer controlled_buffer_65
endmodule

module CPU (
  input  CLK_ENB,
  input  MANUAL_TICK
);

  wire alu_1_cout, ALU_OUT, clk_1_clk_out, clock_1_out, controlled_buffer_3_out, controlled_buffer_4_out,
       controlled_buffer_5_out, controlled_buffer_6_out, controlled_buffer_7_out, controlled_buffer_8_out,
       controlled_buffer_9_out, controlled_buffer_10_out, controlled_buffer_11_out, controlled_buffer_12_out,
       controlled_buffer_13_out, controlled_buffer_14_out, controlled_buffer_15_out,
       controlled_buffer_16_out, controlled_buffer_17_out, controlled_buffer_18_out,
       controlled_buffer_19_out, controlled_buffer_20_out, controlled_buffer_21_out,
       controlled_buffer_22_out, controlled_buffer_23_out, controlled_buffer_24_out,
       controlled_buffer_25_out, controlled_buffer_26_out, controlled_buffer_27_out,
       controlled_buffer_28_out, controlled_buffer_29_out, controlled_buffer_30_out,
       controlled_buffer_31_out, controlled_buffer_32_out, controlled_buffer_33_out,
       controlled_buffer_34_out, controlled_buffer_35_out, controlled_buffer_36_out,
       controlled_buffer_37_out, controlled_buffer_38_out, controlled_buffer_39_out,
       controlled_buffer_40_out, controlled_buffer_41_out, controlled_buffer_42_out,
       controlled_buffer_43_out, controlled_buffer_44_out, controlled_buffer_45_out,
       controlled_buffer_46_out, controlled_buffer_47_out, controlled_buffer_48_out,
       controlled_buffer_49_out, controlled_buffer_50_out, controlled_buffer_51_out,
       controlled_buffer_52_out, controlled_buffer_53_out, controlled_buffer_54_out,
       controlled_buffer_55_out, controlled_buffer_56_out, controlled_buffer_57_out,
       controlled_buffer_58_out, controlled_buffer_59_out, controlled_buffer_60_out,
       controlled_buffer_61_out, controlled_buffer_62_out, controlled_buffer_63_out,
       controlled_buffer_64_out, COUNTER_ENB, COUT, dcd_2_1_o1, dcd_2_1_o2, dcd_2_1_o3, dcd_2_1_o4,
       dcd_2_1_o5, dcd_2_1_o6, dcd_2_1_o7, dcd_2_1_o8, dcd_2_1_o9, dcd_2_1_o10, dcd_2_1_o11, dcd_2_1_o12,
       dcd_2_1_o13, dcd_2_1_o14, dcd_2_1_o15, dcd_2_1_o16, dcd_2_1_o17, dcd_2_1_o18, dcd_2_1_o19,
       dcd_2_1_o20, dcd_2_1_o21, dcd_2_1_o22, dcd_2_1_o23, dcd_2_1_o24, dcd_2_1_o25, dcd_2_1_o26,
       dcd_2_1_o27, dcd_2_1_o28, dcd_2_1_o29, dcd_2_1_o30, dcd_2_1_o31, dcd_2_1_o32, dcd_2_1_o33,
       dcd_2_1_o34, dcd_2_1_o35, dcd_2_1_o36, dcd_2_1_o37, dcd_2_1_o38, dcd_2_1_o39, dcd_2_1_o40,
       dcd_2_1_o41, dcd_2_1_o42, dcd_2_1_o43, dcd_2_1_o44, dcd_2_1_o45, dcd_2_1_o46, dcd_2_1_o47,
       dcd_2_1_o48, dcd_2_1_o49, dcd_2_1_o50, dcd_2_1_o51, dcd_2_1_o52, dcd_2_1_o53, dcd_2_1_o54,
       dcd_2_1_o55, dcd_2_1_o56, dcd_2_1_o57, dcd_2_1_o58, dcd_2_1_o59, dcd_2_1_o60, dcd_2_1_o61,
       dcd_2_1_o62, dcd_2_1_o63, dcd_2_1_o64, DCD_IN, decoder_1_out4, EXEC, FLAGS_IN, FLUSH, HALT, INR_IN,
       INR_OUT, jmp_dcd_1_j_out, JUMP, JZ, MAR_IN, MAR_OUT, MICRO_RESET, not_1_out, OPR_IN, OPR_OUT,
       or_1_out, or_2_out, or_3_out, or_4_out, or_5_out, OUTPUT_REG_IN, pull_resistor_29_node, R0_IN, R0_OUT,
       R1_IN, R1_OUT, RAM_IN, RAM_OUT, ROM_OUT, RR_IN, RR_OUT, SUB, ZERO, zf_reg_1_zero;
  wire [3:0] decoder_1_out3, s_ctn_1_binary_out;
  wire [3:3] pull_resistor_1_node;
  wire [5:0] dcd_2_1_dcd_out, i_reg_1_always_out, i_reg_1_data_out;
  wire [9:0] mar_reg_1_data_out, opr_reg_1_always_out, PC_ADDR, RAM_ADDR;
  wire [12:0] binary_to_bcd_converter_1_p1;
  wire [15:0] alu_1_always_out, r0_1_always_out, r1_1_always_out, result_reg_1_always_out, rom_1_data,
       undriven;
  wire [15:10] rom_2_data;

  not not_1 (not_1_out, clk_1_clk_out);
  or or_1 (or_1_out, FLUSH, decoder_1_out4);
  S_CTN s_ctn_1 (.RESET(or_1_out), .CLOCK(not_1_out), .BINARY_OUT(s_ctn_1_binary_out));
  Clock clock_1 (.out(clock_1_out));
  LED led_1 (.in(decoder_1_out3[3]));
  CLK clk_1 (.HALT(HALT), .CLK_ENB(CLK_ENB), .MANUAL_CLK(MANUAL_TICK), .CLK_IN(clock_1_out), .CLK_OUT(clk_1_clk_out));
  LED led_2 (.in(decoder_1_out3[2]));
  LED led_3 (.in(decoder_1_out3[1]));
  LED led_4 (.in(decoder_1_out3[0]));
  Decoder #(.enable("false"), .select(3)) decoder_1 (
    .out0(decoder_1_out3[3]), .out1(decoder_1_out3[2]), .out2(decoder_1_out3[1]), .out3(decoder_1_out3[0]),
    .out4(decoder_1_out4), .sel(s_ctn_1_binary_out[2:0]));  // open: out5, out6, out7
  LED led_5 (.in(RAM_ADDR[9]));
  LED led_6 (.in(RAM_ADDR[8]));
  LED led_7 (.in(RAM_ADDR[7]));
  ROM #(.addrWidth(10), .dataWidth(16)) rom_1 (.addr(PC_ADDR), .data(rom_1_data));
  Pull_Resistor pull_resistor_1 (.node(pull_resistor_1_node[3]));
  ROM #(.addrWidth(4), .dataWidth(16)) rom_2 (
    .addr({pull_resistor_1_node[3], s_ctn_1_binary_out[3], s_ctn_1_binary_out[1:0]}),
    .data({rom_2_data, OPR_IN, MICRO_RESET, EXEC, MAR_OUT, MAR_IN, INR_OUT, ROM_OUT, COUNTER_ENB, DCD_IN, INR_IN}));
  LED led_8 (.in(rom_2_data[15]));
  LED led_9 (.in(rom_2_data[14]));
  LED led_10 (.in(rom_2_data[13]));
  LED led_11 (.in(RAM_ADDR[4]));
  LED led_12 (.in(RAM_ADDR[3]));
  LED led_13 (.in(RAM_ADDR[6]));
  LED led_14 (.in(RAM_ADDR[5]));
  or or_2 (or_2_out, FLUSH, MICRO_RESET);
  or or_3 (or_3_out, FLUSH, MICRO_RESET);
  LED led_15 (.in(opr_reg_1_always_out[9]));
  LED led_16 (.in(opr_reg_1_always_out[8]));
  LED led_17 (.in(rom_2_data[10]));
  LED led_18 (.in(OPR_IN));
  LED led_19 (.in(rom_2_data[12]));
  LED led_20 (.in(rom_2_data[11]));
  or or_4 (or_4_out, FLUSH, MICRO_RESET);
  MAR_REG mar_reg_1 (
    .DATA_IN(mar_reg_1_data_out), .MAR_IN(MAR_IN), .CLOCK(clk_1_clk_out), .MAR_RESET(or_4_out),
    .MAR_OUT(MAR_OUT), .ALWAYS_OUT(RAM_ADDR), .DATA_OUT(mar_reg_1_data_out));
  LED led_21 (.in(RAM_ADDR[2]));
  LED led_22 (.in(RAM_ADDR[1]));
  LED led_23 (.in(RAM_ADDR[0]));
  I_REG i_reg_1 (
    .DATA_IN(i_reg_1_data_out), .STORE(INR_IN), .CLOCK(clk_1_clk_out), .RESET(or_2_out),
    .DATA_OUT_ENB(INR_OUT), .ALWAYS_OUT(i_reg_1_always_out), .DATA_OUT(i_reg_1_data_out));
  LED led_24 (.in(i_reg_1_always_out[5]));
  LED led_25 (.in(i_reg_1_always_out[4]));
  LED led_26 (.in(i_reg_1_always_out[3]));
  LED led_27 (.in(i_reg_1_always_out[2]));
  OPR_REG opr_reg_1 (
    .DATA_OUT_ENB(OPR_OUT), .DATA_IN(mar_reg_1_data_out), .STORE(OPR_IN), .CLOCK(clk_1_clk_out),
    .RESET(or_3_out), .ALWAYS_OUT(opr_reg_1_always_out), .DATA_OUT(mar_reg_1_data_out));
  LED led_28 (.in(opr_reg_1_always_out[7]));
  LED led_29 (.in(opr_reg_1_always_out[6]));
  LED led_30 (.in(opr_reg_1_always_out[5]));
  LED led_31 (.in(opr_reg_1_always_out[4]));
  LED led_32 (.in(MICRO_RESET));
  LED led_33 (.in(EXEC));
  LED led_34 (.in(MAR_OUT));
  LED led_35 (.in(MAR_IN));
  LED led_36 (.in(i_reg_1_always_out[1]));
  LED led_37 (.in(i_reg_1_always_out[0]));
  LED led_38 (.in(opr_reg_1_always_out[3]));
  LED led_39 (.in(opr_reg_1_always_out[2]));
  LED led_40 (.in(opr_reg_1_always_out[1]));
  LED led_41 (.in(opr_reg_1_always_out[0]));
  LED led_42 (.in(INR_OUT));
  LED led_43 (.in(ROM_OUT));
  LED led_44 (.in(COUNTER_ENB));
  LED led_45 (.in(DCD_IN));
  assign {i_reg_1_data_out, mar_reg_1_data_out} = ROM_OUT ? rom_1_data : 16'bz;  // Controlled_Buffer controlled_buffer_1
  LED led_46 (.in(INR_IN));
  LED led_47 (.in(i_reg_1_data_out[5]));
  LED led_48 (.in(i_reg_1_data_out[4]));
  LED led_49 (.in(i_reg_1_data_out[3]));
  LED led_50 (.in(i_reg_1_data_out[2]));
  Pull_Resistor pull_resistor_2 (.node(i_reg_1_data_out[5]));
  Pull_Resistor pull_resistor_3 (.node(i_reg_1_data_out[4]));
  Pull_Resistor pull_resistor_4 (.node(i_reg_1_data_out[3]));
  Pull_Resistor pull_resistor_5 (.node(i_reg_1_data_out[2]));
  LED led_51 (.in(i_reg_1_data_out[1]));
  LED led_52 (.in(i_reg_1_data_out[0]));
  LED led_53 (.in(mar_reg_1_data_out[9]));
  LED led_54 (.in(mar_reg_1_data_out[8]));
  Pull_Resistor pull_resistor_6 (.node(i_reg_1_data_out[1]));
  Pull_Resistor pull_resistor_7 (.node(i_reg_1_data_out[0]));
  Pull_Resistor pull_resistor_8 (.node(mar_reg_1_data_out[9]));
  Pull_Resistor pull_resistor_9 (.node(mar_reg_1_data_out[8]));
  LED led_55 (.in(mar_reg_1_data_out[7]));
  LED led_56 (.in(mar_reg_1_data_out[6]));
  LED led_57 (.in(mar_reg_1_data_out[5]));
  LED led_58 (.in(mar_reg_1_data_out[4]));
  Pull_Resistor pull_resistor_10 (.node(mar_reg_1_data_out[7]));
  Pull_Resistor pull_resistor_11 (.node(mar_reg_1_data_out[6]));
  Pull_Resistor pull_resistor_12 (.node(mar_reg_1_data_out[5]));
  Pull_Resistor pull_resistor_13 (.node(mar_reg_1_data_out[4]));
  LED led_59 (.in(mar_reg_1_data_out[3]));
  LED led_60 (.in(mar_reg_1_data_out[2]));
  LED led_61 (.in(mar_reg_1_data_out[1]));
  LED led_62 (.in(mar_reg_1_data_out[0]));
  Pull_Resistor pull_resistor_14 (.node(mar_reg_1_data_out[3]));
  Pull_Resistor pull_resistor_15 (.node(mar_reg_1_data_out[2]));
  Pull_Resistor pull_resistor_16 (.node(mar_reg_1_data_out[1]));
  Pull_Resistor pull_resistor_17 (.node(mar_reg_1_data_out[0]));
  LED led_63 (.in(mar_reg_1_data_out[9]));
  LED led_64 (.in(mar_reg_1_data_out[8]));
  LED led_65 (.in(mar_reg_1_data_out[7]));
  Pull_Resistor pull_resistor_18 (.node(mar_reg_1_data_out[9]));
  Pull_Resistor pull_resistor_19 (.node(mar_reg_1_data_out[8]));
  Pull_Resistor pull_resistor_20 (.node(mar_reg_1_data_out[7]));
  LED led_66 (.in(mar_reg_1_data_out[6]));
  LED led_67 (.in(mar_reg_1_data_out[5]));
  LED led_68 (.in(mar_reg_1_data_out[4]));
  LED led_69 (.in(mar_reg_1_data_out[3]));
  Pull_Resistor pull_resistor_21 (.node(mar_reg_1_data_out[6]));
  Pull_Resistor pull_resistor_22 (.node(mar_reg_1_data_out[5]));
  Pull_Resistor pull_resistor_23 (.node(mar_reg_1_data_out[4]));
  Pull_Resistor pull_resistor_24 (.node(mar_reg_1_data_out[3]));
  LED led_70 (.in(mar_reg_1_data_out[2]));
  LED led_71 (.in(mar_reg_1_data_out[1]));
  LED led_72 (.in(mar_reg_1_data_out[0]));
  Pull_Resistor pull_resistor_25 (.node(mar_reg_1_data_out[2]));
  Pull_Resistor pull_resistor_26 (.node(mar_reg_1_data_out[1]));
  Pull_Resistor pull_resistor_27 (.node(mar_reg_1_data_out[0]));
  Pull_Resistor pull_resistor_28 (.node(FLUSH));
  LED led_73 (.in(undriven[15]));
  LED led_74 (.in(undriven[14]));
  LED led_75 (.in(undriven[13]));
  LED led_76 (.in(r0_1_always_out[15]));
  LED led_77 (.in(r0_1_always_out[14]));
  LED led_78 (.in(r0_1_always_out[13]));
  LED led_79 (.in(r1_1_always_out[15]));
  LED led_80 (.in(r1_1_always_out[14]));
  LED led_81 (.in(r1_1_always_out[13]));
  LED led_82 (.in(result_reg_1_always_out[15]));
  LED led_83 (.in(result_reg_1_always_out[14]));
  LED led_84 (.in(result_reg_1_always_out[13]));
  or or_5 (or_5_out, FLUSH, MICRO_RESET);
  LED led_85 (.in(undriven[12]));
  LED led_86 (.in(undriven[11]));
  LED led_87 (.in(undriven[10]));
  LED led_88 (.in(undriven[9]));
  LED led_89 (.in(r0_1_always_out[12]));
  LED led_90 (.in(r0_1_always_out[11]));
  LED led_91 (.in(r0_1_always_out[10]));
  LED led_92 (.in(r0_1_always_out[9]));
  LED led_93 (.in(r1_1_always_out[12]));
  LED led_94 (.in(r1_1_always_out[11]));
  LED led_95 (.in(r1_1_always_out[10]));
  LED led_96 (.in(r1_1_always_out[9]));
  LED led_97 (.in(result_reg_1_always_out[12]));
  LED led_98 (.in(result_reg_1_always_out[11]));
  LED led_99 (.in(result_reg_1_always_out[10]));
  LED led_100 (.in(result_reg_1_always_out[9]));
  Button RESET (.out(FLUSH));
  LED led_101 (.in(undriven[8]));
  LED led_102 (.in(undriven[7]));
  LED led_103 (.in(undriven[6]));
  LED led_104 (.in(undriven[5]));
  LED led_105 (.in(r0_1_always_out[8]));
  LED led_106 (.in(r0_1_always_out[7]));
  LED led_107 (.in(r0_1_always_out[6]));
  LED led_108 (.in(r0_1_always_out[5]));
  LED led_109 (.in(r1_1_always_out[8]));
  LED led_110 (.in(r1_1_always_out[7]));
  LED led_111 (.in(r1_1_always_out[6]));
  LED led_112 (.in(r1_1_always_out[5]));
  LED led_113 (.in(result_reg_1_always_out[8]));
  LED led_114 (.in(result_reg_1_always_out[7]));
  LED led_115 (.in(result_reg_1_always_out[6]));
  LED led_116 (.in(result_reg_1_always_out[5]));
  _7_Segment_Display u_7_segment_display_1 ();  // open: g, f, a, b, e, d, c, dp
  // BCD_to_7_Segment_decoder bcd_to_7_segment_decoder_1: pin names not known
  LED led_117 (.in(dcd_2_1_dcd_out[5]));
  LED led_118 (.in(dcd_2_1_dcd_out[4]));
  LED led_119 (.in(dcd_2_1_dcd_out[3]));
  PC pc_1 (
    .RESET(FLUSH), .JUMP(jmp_dcd_1_j_out), .COUNTER_ENB(COUNTER_ENB), .CLOCK(clk_1_clk_out),
    .ADDR_IN(mar_reg_1_data_out), .ALWAYS_OUT(PC_ADDR), .ADDR_OUT(mar_reg_1_data_out));  // open: COUNTER_OUT
  LED led_120 (.in(undriven[4]));
  LED led_121 (.in(undriven[3]));
  LED led_122 (.in(undriven[2]));
  LED led_123 (.in(undriven[1]));
  LED led_124 (.in(r0_1_always_out[4]));
  LED led_125 (.in(r0_1_always_out[3]));
  LED led_126 (.in(r0_1_always_out[2]));
  LED led_127 (.in(r0_1_always_out[1]));
  LED led_128 (.in(r1_1_always_out[4]));
  LED led_129 (.in(r1_1_always_out[3]));
  LED led_130 (.in(r1_1_always_out[2]));
  LED led_131 (.in(r1_1_always_out[1]));
  LED led_132 (.in(result_reg_1_always_out[4]));
  LED led_133 (.in(result_reg_1_always_out[3]));
  LED led_134 (.in(result_reg_1_always_out[2]));
  LED led_135 (.in(result_reg_1_always_out[1]));
  _7_Segment_Display u_7_segment_display_2 ();  // open: g, f, a, b, e, d, c, dp
  // BCD_to_7_Segment_decoder bcd_to_7_segment_decoder_2: pin names not known
  // Binary_to_BCD_converter #(.binvalue(13)) binary_to_bcd_converter_1: pin names not known; wires that end beside it: binary_to_bcd_converter_1_p1
  LED led_136 (.in(dcd_2_1_dcd_out[2]));
  LED led_137 (.in(dcd_2_1_dcd_out[1]));
  LED led_138 (.in(dcd_2_1_dcd_out[0]));
  Pull_Resistor pull_resistor_29 (.node(pull_resistor_29_node));
  DCD_2 dcd_2_1 (
    .SELECTOR(i_reg_1_data_out), .ENB(DCD_IN), .EXEC(EXEC), .DCD_RESET(or_5_out), .DCD_OUT(dcd_2_1_dcd_out),
    .O7(dcd_2_1_o7), .O8(dcd_2_1_o8), .O9(dcd_2_1_o9), .O10(dcd_2_1_o10), .O11(dcd_2_1_o11),
    .O12(dcd_2_1_o12), .O13(dcd_2_1_o13), .O14(dcd_2_1_o14), .O15(dcd_2_1_o15), .O16(dcd_2_1_o16),
    .O17(dcd_2_1_o17), .O18(dcd_2_1_o18), .O19(dcd_2_1_o19), .O20(dcd_2_1_o20), .O21(dcd_2_1_o21),
    .O22(dcd_2_1_o22), .O23(dcd_2_1_o23), .O24(dcd_2_1_o24), .O25(dcd_2_1_o25), .O26(dcd_2_1_o26),
    .O27(dcd_2_1_o27), .O28(dcd_2_1_o28), .O29(dcd_2_1_o29), .O30(dcd_2_1_o30), .O31(dcd_2_1_o31),
    .O0(pull_resistor_29_node), .O32(dcd_2_1_o32), .O33(dcd_2_1_o33), .O34(dcd_2_1_o34), .O35(dcd_2_1_o35),
    .O36(dcd_2_1_o36), .O37(dcd_2_1_o37), .O38(dcd_2_1_o38), .O39(dcd_2_1_o39), .O40(dcd_2_1_o40),
    .O41(dcd_2_1_o41), .O1(dcd_2_1_o1), .O42(dcd_2_1_o42), .O43(dcd_2_1_o43), .O44(dcd_2_1_o44),
    .O45(dcd_2_1_o45), .O46(dcd_2_1_o46), .O47(dcd_2_1_o47), .O48(dcd_2_1_o48), .O49(dcd_2_1_o49),
    .O50(dcd_2_1_o50), .O51(dcd_2_1_o51), .O2(dcd_2_1_o2), .O52(dcd_2_1_o52), .O53(dcd_2_1_o53),
    .O54(dcd_2_1_o54), .O55(dcd_2_1_o55), .O56(dcd_2_1_o56), .O57(dcd_2_1_o57), .O58(dcd_2_1_o58),
    .O59(dcd_2_1_o59), .O60(dcd_2_1_o60), .O61(dcd_2_1_o61), .O3(dcd_2_1_o3), .O62(dcd_2_1_o62),
    .O63(dcd_2_1_o63), .O64(dcd_2_1_o64), .O4(dcd_2_1_o4), .O5(dcd_2_1_o5), .O6(dcd_2_1_o6));
  Pull_Resistor pull_resistor_30 (.node(dcd_2_1_o1));
  MEM mem_1 (
    .STORE(RAM_IN), .CLOCK(clk_1_clk_out), .RAM_OUT_ENB(RAM_OUT), .ADDRESS(RAM_ADDR),
    .DATA({i_reg_1_data_out, mar_reg_1_data_out}), .RAM_OUT({i_reg_1_data_out, mar_reg_1_data_out}));  // open: ALWAYS_OUT
  LED led_139 (.in(undriven[0]));
  R0 r0_1 (
    .DATA_IN({i_reg_1_data_out, mar_reg_1_data_out}), .A_IN(R0_IN), .CLOCK(clk_1_clk_out), .A_RESET(FLUSH),
    .A_OUT(R0_OUT), .ALWAYS_OUT(r0_1_always_out), .DATA_OUT({i_reg_1_data_out, mar_reg_1_data_out}));
  LED led_140 (.in(r0_1_always_out[0]));
  ALU alu_1 (
    .A_IN(r0_1_always_out), .B_IN(r1_1_always_out), .OUTPUT_ENB(ALU_OUT), .SUB(SUB),
    .ALWAYS_OUT(alu_1_always_out), .A_OUT({i_reg_1_data_out, mar_reg_1_data_out}), .COUT(alu_1_cout));
  LED led_141 (.in(r1_1_always_out[0]));
  R1 r1_1 (
    .DATA_IN({i_reg_1_data_out, mar_reg_1_data_out}), .B_IN(R1_IN), .CLOCK(clk_1_clk_out), .B_RESET(FLUSH),
    .B_OUT(R1_OUT), .ALWAYS_OUT(r1_1_always_out), .DATA_OUT({i_reg_1_data_out, mar_reg_1_data_out}));
  LED led_142 (.in(result_reg_1_always_out[0]));
  RESULT_REG result_reg_1 (
    .DATA_IN({i_reg_1_data_out, mar_reg_1_data_out}), .R_IN(RR_IN), .CLOCK(clk_1_clk_out), .R_RESET(FLUSH),
    .R_OUT(RR_OUT), .ALWAYS_OUT(result_reg_1_always_out), .DATA_OUT({i_reg_1_data_out, mar_reg_1_data_out}));
  _7_Segment_Display u_7_segment_display_3 ();  // open: g, f, a, b, e, d, c, dp
  // BCD_to_7_Segment_decoder bcd_to_7_segment_decoder_3: pin names not known
  O_REG o_reg_1 (
    .DATA_IN({i_reg_1_data_out[2:0], mar_reg_1_data_out}), .STORE(OUTPUT_REG_IN), .CLOCK(clk_1_clk_out),
    .RESET(FLUSH), .DATA_OUT(binary_to_bcd_converter_1_p1));
  LED led_143 (.in(controlled_buffer_64_out));
  LED led_144 (.in(controlled_buffer_63_out));
  assign HALT = dcd_2_1_o2 ? dcd_2_1_o2 : 1'bz;  // Controlled_Buffer controlled_buffer_2
  assign controlled_buffer_3_out = dcd_2_1_o3 ? dcd_2_1_o3 : 1'bz;  // Controlled_Buffer controlled_buffer_3
  assign controlled_buffer_4_out = dcd_2_1_o4 ? dcd_2_1_o4 : 1'bz;  // Controlled_Buffer controlled_buffer_4
  assign controlled_buffer_5_out = dcd_2_1_o5 ? dcd_2_1_o5 : 1'bz;  // Controlled_Buffer controlled_buffer_5
  assign controlled_buffer_6_out = dcd_2_1_o6 ? dcd_2_1_o6 : 1'bz;  // Controlled_Buffer controlled_buffer_6
  assign controlled_buffer_7_out = dcd_2_1_o7 ? dcd_2_1_o7 : 1'bz;  // Controlled_Buffer controlled_buffer_7
  assign controlled_buffer_8_out = dcd_2_1_o8 ? dcd_2_1_o8 : 1'bz;  // Controlled_Buffer controlled_buffer_8
  assign controlled_buffer_9_out = dcd_2_1_o9 ? dcd_2_1_o9 : 1'bz;  // Controlled_Buffer controlled_buffer_9
  assign controlled_buffer_10_out = dcd_2_1_o10 ? dcd_2_1_o10 : 1'bz;  // Controlled_Buffer controlled_buffer_10
  assign controlled_buffer_11_out = dcd_2_1_o11 ? dcd_2_1_o11 : 1'bz;  // Controlled_Buffer controlled_buffer_11
  assign controlled_buffer_12_out = dcd_2_1_o12 ? dcd_2_1_o12 : 1'bz;  // Controlled_Buffer controlled_buffer_12
  assign controlled_buffer_13_out = dcd_2_1_o13 ? dcd_2_1_o13 : 1'bz;  // Controlled_Buffer controlled_buffer_13
  assign controlled_buffer_14_out = dcd_2_1_o14 ? dcd_2_1_o14 : 1'bz;  // Controlled_Buffer controlled_buffer_14
  assign controlled_buffer_15_out = dcd_2_1_o15 ? dcd_2_1_o15 : 1'bz;  // Controlled_Buffer controlled_buffer_15
  assign controlled_buffer_16_out = dcd_2_1_o16 ? dcd_2_1_o16 : 1'bz;  // Controlled_Buffer controlled_buffer_16
  assign controlled_buffer_17_out = dcd_2_1_o17 ? dcd_2_1_o17 : 1'bz;  // Controlled_Buffer controlled_buffer_17
  assign controlled_buffer_18_out = dcd_2_1_o18 ? dcd_2_1_o18 : 1'bz;  // Controlled_Buffer controlled_buffer_18
  assign controlled_buffer_19_out = dcd_2_1_o19 ? dcd_2_1_o19 : 1'bz;  // Controlled_Buffer controlled_buffer_19
  assign controlled_buffer_20_out = dcd_2_1_o20 ? dcd_2_1_o20 : 1'bz;  // Controlled_Buffer controlled_buffer_20
  assign controlled_buffer_21_out = dcd_2_1_o21 ? dcd_2_1_o21 : 1'bz;  // Controlled_Buffer controlled_buffer_21
  assign controlled_buffer_22_out = dcd_2_1_o22 ? dcd_2_1_o22 : 1'bz;  // Controlled_Buffer controlled_buffer_22
  assign controlled_buffer_23_out = dcd_2_1_o23 ? dcd_2_1_o23 : 1'bz;  // Controlled_Buffer controlled_buffer_23
  assign controlled_buffer_24_out = dcd_2_1_o24 ? dcd_2_1_o24 : 1'bz;  // Controlled_Buffer controlled_buffer_24
  assign controlled_buffer_25_out = dcd_2_1_o25 ? dcd_2_1_o25 : 1'bz;  // Controlled_Buffer controlled_buffer_25
  assign controlled_buffer_26_out = dcd_2_1_o26 ? dcd_2_1_o26 : 1'bz;  // Controlled_Buffer controlled_buffer_26
  assign controlled_buffer_27_out = dcd_2_1_o27 ? dcd_2_1_o27 : 1'bz;  // Controlled_Buffer controlled_buffer_27
  assign controlled_buffer_28_out = dcd_2_1_o28 ? dcd_2_1_o28 : 1'bz;  // Controlled_Buffer controlled_buffer_28
  assign controlled_buffer_29_out = dcd_2_1_o29 ? dcd_2_1_o29 : 1'bz;  // Controlled_Buffer controlled_buffer_29
  assign controlled_buffer_30_out = dcd_2_1_o30 ? dcd_2_1_o30 : 1'bz;  // Controlled_Buffer controlled_buffer_30
  assign controlled_buffer_31_out = dcd_2_1_o31 ? dcd_2_1_o31 : 1'bz;  // Controlled_Buffer controlled_buffer_31
  assign controlled_buffer_32_out = dcd_2_1_o32 ? dcd_2_1_o32 : 1'bz;  // Controlled_Buffer controlled_buffer_32
  assign controlled_buffer_33_out = dcd_2_1_o33 ? dcd_2_1_o33 : 1'bz;  // Controlled_Buffer controlled_buffer_33
  assign controlled_buffer_34_out = dcd_2_1_o34 ? dcd_2_1_o34 : 1'bz;  // Controlled_Buffer controlled_buffer_34
  assign controlled_buffer_35_out = dcd_2_1_o35 ? dcd_2_1_o35 : 1'bz;  // Controlled_Buffer controlled_buffer_35
  assign controlled_buffer_36_out = dcd_2_1_o36 ? dcd_2_1_o36 : 1'bz;  // Controlled_Buffer controlled_buffer_36
  assign controlled_buffer_37_out = dcd_2_1_o37 ? dcd_2_1_o37 : 1'bz;  // Controlled_Buffer controlled_buffer_37
  assign controlled_buffer_38_out = dcd_2_1_o38 ? dcd_2_1_o38 : 1'bz;  // Controlled_Buffer controlled_buffer_38
  assign controlled_buffer_39_out = dcd_2_1_o39 ? dcd_2_1_o39 : 1'bz;  // Controlled_Buffer controlled_buffer_39
  assign controlled_buffer_40_out = dcd_2_1_o40 ? dcd_2_1_o40 : 1'bz;  // Controlled_Buffer controlled_buffer_40
  assign controlled_buffer_41_out = dcd_2_1_o41 ? dcd_2_1_o41 : 1'bz;  // Controlled_Buffer controlled_buffer_41
  assign controlled_buffer_42_out = dcd_2_1_o42 ? dcd_2_1_o42 : 1'bz;  // Controlled_Buffer controlled_buffer_42
  assign controlled_buffer_43_out = dcd_2_1_o43 ? dcd_2_1_o43 : 1'bz;  // Controlled_Buffer controlled_buffer_43
  assign controlled_buffer_44_out = dcd_2_1_o44 ? dcd_2_1_o44 : 1'bz;  // Controlled_Buffer controlled_buffer_44
  assign controlled_buffer_45_out = dcd_2_1_o45 ? dcd_2_1_o45 : 1'bz;  // Controlled_Buffer controlled_buffer_45
  assign controlled_buffer_46_out = dcd_2_1_o46 ? dcd_2_1_o46 : 1'bz;  // Controlled_Buffer controlled_buffer_46
  assign controlled_buffer_47_out = dcd_2_1_o47 ? dcd_2_1_o47 : 1'bz;  // Controlled_Buffer controlled_buffer_47
  assign controlled_buffer_48_out = dcd_2_1_o48 ? dcd_2_1_o48 : 1'bz;  // Controlled_Buffer controlled_buffer_48
  assign controlled_buffer_49_out = dcd_2_1_o49 ? dcd_2_1_o49 : 1'bz;  // Controlled_Buffer controlled_buffer_49
  assign controlled_buffer_50_out = dcd_2_1_o50 ? dcd_2_1_o50 : 1'bz;  // Controlled_Buffer controlled_buffer_50
  assign controlled_buffer_51_out = dcd_2_1_o51 ? dcd_2_1_o51 : 1'bz;  // Controlled_Buffer controlled_buffer_51
  assign controlled_buffer_52_out = dcd_2_1_o52 ? dcd_2_1_o52 : 1'bz;  // Controlled_Buffer controlled_buffer_52
  assign controlled_buffer_53_out = dcd_2_1_o53 ? dcd_2_1_o53 : 1'bz;  // Controlled_Buffer controlled_buffer_53
  assign controlled_buffer_54_out = dcd_2_1_o54 ? dcd_2_1_o54 : 1'bz;  // Controlled_Buffer controlled_buffer_54
  assign controlled_buffer_55_out = dcd_2_1_o55 ? dcd_2_1_o55 : 1'bz;  // Controlled_Buffer controlled_buffer_55
  assign controlled_buffer_56_out = dcd_2_1_o56 ? dcd_2_1_o56 : 1'bz;  // Controlled_Buffer controlled_buffer_56
  assign controlled_buffer_57_out = dcd_2_1_o57 ? dcd_2_1_o57 : 1'bz;  // Controlled_Buffer controlled_buffer_57
  assign controlled_buffer_58_out = dcd_2_1_o58 ? dcd_2_1_o58 : 1'bz;  // Controlled_Buffer controlled_buffer_58
  assign controlled_buffer_59_out = dcd_2_1_o59 ? dcd_2_1_o59 : 1'bz;  // Controlled_Buffer controlled_buffer_59
  assign controlled_buffer_60_out = dcd_2_1_o60 ? dcd_2_1_o60 : 1'bz;  // Controlled_Buffer controlled_buffer_60
  assign controlled_buffer_61_out = dcd_2_1_o61 ? dcd_2_1_o61 : 1'bz;  // Controlled_Buffer controlled_buffer_61
  assign controlled_buffer_62_out = dcd_2_1_o62 ? dcd_2_1_o62 : 1'bz;  // Controlled_Buffer controlled_buffer_62
  assign controlled_buffer_63_out = dcd_2_1_o63 ? dcd_2_1_o63 : 1'bz;  // Controlled_Buffer controlled_buffer_63
  assign controlled_buffer_64_out = dcd_2_1_o64 ? dcd_2_1_o64 : 1'bz;  // Controlled_Buffer controlled_buffer_64
  Pull_Resistor pull_resistor_31 (.node(controlled_buffer_64_out));
  Pull_Resistor pull_resistor_32 (.node(controlled_buffer_63_out));
  JMP_DCD jmp_dcd_1 (.JUMP(JUMP), .JZ(JZ), .ZERO(ZERO), .J_OUT(jmp_dcd_1_j_out));
  ZF_REG zf_reg_1 (.in_1(alu_1_always_out), .ZERO(zf_reg_1_zero));
  _7_Segment_Display u_7_segment_display_4 ();  // open: g, f, a, b, e, d, c, dp
  // BCD_to_7_Segment_decoder bcd_to_7_segment_decoder_4: pin names not known
  LED led_145 (.in(controlled_buffer_62_out));
  LED led_146 (.in(controlled_buffer_61_out));
  LED led_147 (.in(controlled_buffer_60_out));
  LED led_148 (.in(controlled_buffer_59_out));
  Pull_Resistor pull_resistor_33 (.node(controlled_buffer_62_out));
  Pull_Resistor pull_resistor_34 (.node(controlled_buffer_61_out));
  Pull_Resistor pull_resistor_35 (.node(controlled_buffer_60_out));
  Pull_Resistor pull_resistor_36 (.node(controlled_buffer_59_out));
  F_REG f_reg_1 (
    .CARRY(alu_1_cout), .ZERO(zf_reg_1_zero), .STORE(FLAGS_IN), .CLOCK(clk_1_clk_out), .RESET(FLUSH),
    .CARRY_OUT(COUT), .ZERO_OUT(ZERO));
  LED led_149 (.in(controlled_buffer_58_out));
  LED led_150 (.in(controlled_buffer_57_out));
  LED led_151 (.in(controlled_buffer_56_out));
  LED led_152 (.in(controlled_buffer_55_out));
  Pull_Resistor pull_resistor_37 (.node(controlled_buffer_58_out));
  Pull_Resistor pull_resistor_38 (.node(controlled_buffer_57_out));
  Pull_Resistor pull_resistor_39 (.node(controlled_buffer_56_out));
  Pull_Resistor pull_resistor_40 (.node(controlled_buffer_55_out));
  LED led_153 (.in(COUT));
  LED led_154 (.in(ZERO));
  LED led_155 (.in(controlled_buffer_54_out));
  LED led_156 (.in(controlled_buffer_53_out));
  LED led_157 (.in(controlled_buffer_52_out));
  LED led_158 (.in(controlled_buffer_51_out));
  Pull_Resistor pull_resistor_41 (.node(controlled_buffer_54_out));
  Pull_Resistor pull_resistor_42 (.node(controlled_buffer_53_out));
  Pull_Resistor pull_resistor_43 (.node(controlled_buffer_52_out));
  Pull_Resistor pull_resistor_44 (.node(controlled_buffer_51_out));
  LED led_159 (.in(controlled_buffer_50_out));
  LED led_160 (.in(controlled_buffer_49_out));
  LED led_161 (.in(controlled_buffer_48_out));
  LED led_162 (.in(controlled_buffer_47_out));
  Pull_Resistor pull_resistor_45 (.node(controlled_buffer_50_out));
  Pull_Resistor pull_resistor_46 (.node(controlled_buffer_49_out));
  Pull_Resistor pull_resistor_47 (.node(controlled_buffer_48_out));
  Pull_Resistor pull_resistor_48 (.node(controlled_buffer_47_out));
  LED led_163 (.in(controlled_buffer_46_out));
  LED led_164 (.in(controlled_buffer_45_out));
  LED led_165 (.in(controlled_buffer_44_out));
  LED led_166 (.in(controlled_buffer_43_out));
  Pull_Resistor pull_resistor_49 (.node(controlled_buffer_46_out));
  Pull_Resistor pull_resistor_50 (.node(controlled_buffer_45_out));
  Pull_Resistor pull_resistor_51 (.node(controlled_buffer_44_out));
  Pull_Resistor pull_resistor_52 (.node(controlled_buffer_43_out));
  LED led_167 (.in(controlled_buffer_42_out));
  LED led_168 (.in(controlled_buffer_41_out));
  LED led_169 (.in(controlled_buffer_40_out));
  LED led_170 (.in(controlled_buffer_39_out));
  Pull_Resistor pull_resistor_53 (.node(controlled_buffer_42_out));
  Pull_Resistor pull_resistor_54 (.node(controlled_buffer_41_out));
  Pull_Resistor pull_resistor_55 (.node(controlled_buffer_40_out));
  Pull_Resistor pull_resistor_56 (.node(controlled_buffer_39_out));
  LED led_171 (.in(controlled_buffer_38_out));
  LED led_172 (.in(controlled_buffer_37_out));
  LED led_173 (.in(controlled_buffer_36_out));
  LED led_174 (.in(controlled_buffer_35_out));
  Pull_Resistor pull_resistor_57 (.node(controlled_buffer_38_out));
  Pull_Resistor pull_resistor_58 (.node(controlled_buffer_37_out));
  Pull_Resistor pull_resistor_59 (.node(controlled_buffer_36_out));
  Pull_Resistor pull_resistor_60 (.node(controlled_buffer_35_out));
  LED led_175 (.in(controlled_buffer_34_out));
  LED led_176 (.in(controlled_buffer_33_out));
  LED led_177 (.in(controlled_buffer_32_out));
  LED led_178 (.in(controlled_buffer_31_out));
  Pull_Resistor pull_resistor_61 (.node(controlled_buffer_34_out));
  Pull_Resistor pull_resistor_62 (.node(controlled_buffer_33_out));
  Pull_Resistor pull_resistor_63 (.node(controlled_buffer_32_out));
  Pull_Resistor pull_resistor_64 (.node(controlled_buffer_31_out));
  LED led_179 (.in(controlled_buffer_30_out));
  LED led_180 (.in(controlled_buffer_29_out));
  LED led_181 (.in(controlled_buffer_28_out));
  LED led_182 (.in(controlled_buffer_27_out));
  Pull_Resistor pull_resistor_65 (.node(controlled_buffer_30_out));
  Pull_Resistor pull_resistor_66 (.node(controlled_buffer_29_out));
  Pull_Resistor pull_resistor_67 (.node(controlled_buffer_28_out));
  Pull_Resistor pull_resistor_68 (.node(controlled_buffer_27_out));
  LED led_183 (.in(controlled_buffer_26_out));
  LED led_184 (.in(controlled_buffer_25_out));
  LED led_185 (.in(controlled_buffer_24_out));
  LED led_186 (.in(controlled_buffer_23_out));
  Pull_Resistor pull_resistor_69 (.node(controlled_buffer_26_out));
  Pull_Resistor pull_resistor_70 (.node(controlled_buffer_25_out));
  Pull_Resistor pull_resistor_71 (.node(controlled_buffer_24_out));
  Pull_Resistor pull_resistor_72 (.node(controlled_buffer_23_out));
  LED led_187 (.in(controlled_buffer_22_out));
  LED led_188 (.in(controlled_buffer_21_out));
  LED led_189 (.in(controlled_buffer_20_out));
  LED led_190 (.in(controlled_buffer_19_out));
  Pull_Resistor pull_resistor_73 (.node(controlled_buffer_22_out));
  Pull_Resistor pull_resistor_74 (.node(controlled_buffer_21_out));
  Pull_Resistor pull_resistor_75 (.node(controlled_buffer_20_out));
  Pull_Resistor pull_resistor_76 (.node(controlled_buffer_19_out));
  LED led_191 (.in(controlled_buffer_18_out));
  LED led_192 (.in(controlled_buffer_17_out));
  LED led_193 (.in(controlled_buffer_16_out));
  LED led_194 (.in(controlled_buffer_15_out));
  Pull_Resistor pull_resistor_77 (.node(controlled_buffer_18_out));
  Pull_Resistor pull_resistor_78 (.node(controlled_buffer_17_out));
  Pull_Resistor pull_resistor_79 (.node(controlled_buffer_16_out));
  Pull_Resistor pull_resistor_80 (.node(controlled_buffer_15_out));
  LED led_195 (.in(controlled_buffer_14_out));
  LED led_196 (.in(controlled_buffer_13_out));
  LED led_197 (.in(controlled_buffer_12_out));
  LED led_198 (.in(controlled_buffer_11_out));
  Pull_Resistor pull_resistor_81 (.node(controlled_buffer_14_out));
  Pull_Resistor pull_resistor_82 (.node(controlled_buffer_13_out));
  Pull_Resistor pull_resistor_83 (.node(controlled_buffer_12_out));
  Pull_Resistor pull_resistor_84 (.node(controlled_buffer_11_out));
  LED led_199 (.in(controlled_buffer_10_out));
  LED led_200 (.in(controlled_buffer_9_out));
  LED led_201 (.in(controlled_buffer_8_out));
  LED led_202 (.in(controlled_buffer_7_out));
  Pull_Resistor pull_resistor_85 (.node(controlled_buffer_10_out));
  Pull_Resistor pull_resistor_86 (.node(controlled_buffer_9_out));
  Pull_Resistor pull_resistor_87 (.node(controlled_buffer_8_out));
  Pull_Resistor pull_resistor_88 (.node(controlled_buffer_7_out));
  LED led_203 (.in(controlled_buffer_6_out));
  LED led_204 (.in(controlled_buffer_5_out));
  LED led_205 (.in(controlled_buffer_4_out));
  LED led_206 (.in(controlled_buffer_3_out));
  Pull_Resistor pull_resistor_89 (.node(controlled_buffer_6_out));
  Pull_Resistor pull_resistor_90 (.node(controlled_buffer_5_out));
  Pull_Resistor pull_resistor_91 (.node(controlled_buffer_4_out));
  Pull_Resistor pull_resistor_92 (.node(controlled_buffer_3_out));
  LED led_207 (.in(HALT));
  DCD_CTRL dcd_ctrl_1 (
    .I5(controlled_buffer_3_out), .I4(controlled_buffer_4_out), .l3(controlled_buffer_5_out), .O0(RAM_OUT));  // open: I2, I1, I0
  DCD_CTRL dcd_ctrl_2 (.I5(controlled_buffer_3_out), .I4(controlled_buffer_8_out), .O0(R0_IN));  // open: l3, I2, I1, I0
  DCD_CTRL dcd_ctrl_3 (.I5(controlled_buffer_4_out), .I4(controlled_buffer_9_out), .O0(R1_IN));  // open: l3, I2, I1, I0
  DCD_CTRL dcd_ctrl_4 (.I5(controlled_buffer_5_out), .O0(OUTPUT_REG_IN));  // open: I4, l3, I2, I1, I0
  DCD_CTRL dcd_ctrl_5 (
    .I5(controlled_buffer_6_out), .I4(controlled_buffer_7_out), .l3(controlled_buffer_13_out), .O0(RAM_IN));  // open: I2, I1, I0
  DCD_CTRL dcd_ctrl_6 (
    .I5(controlled_buffer_6_out), .I4(controlled_buffer_14_out), .O0(R0_OUT));  // open: l3, I2, I1, I0
  DCD_CTRL dcd_ctrl_7 (
    .I5(controlled_buffer_7_out), .l3(controlled_buffer_14_out), .O0(R1_OUT));  // open: I4, I2, I1, I0
  DCD_CTRL dcd_ctrl_8 (
    .I5(controlled_buffer_8_out), .I4(controlled_buffer_9_out), .l3(controlled_buffer_10_out),
    .I2(controlled_buffer_15_out), .O0(OPR_OUT));  // open: I1, I0
  DCD_CTRL dcd_ctrl_9 (.I5(controlled_buffer_10_out), .O0(JUMP));  // open: I4, l3, I2, I1, I0
  DCD_CTRL dcd_ctrl_10 (
    .I5(controlled_buffer_14_out), .I4(controlled_buffer_15_out), .O0(FLAGS_IN));  // open: l3, I2, I1, I0
  DCD_CTRL dcd_ctrl_11 (
    .I5(controlled_buffer_11_out), .I4(controlled_buffer_12_out), .O0(RR_IN));  // open: l3, I2, I1, I0
  DCD_CTRL dcd_ctrl_12 (.I5(controlled_buffer_13_out), .O0(RR_OUT));  // open: I4, l3, I2, I1, I0
  DCD_CTRL dcd_ctrl_13 (
    .I5(controlled_buffer_11_out), .I4(controlled_buffer_12_out), .O0(ALU_OUT));  // open: l3, I2, I1, I0
  DCD_CTRL dcd_ctrl_14 (
    .I5(controlled_buffer_12_out), .I4(controlled_buffer_14_out), .O0(SUB));  // open: l3, I2, I1, I0
  DCD_CTRL dcd_ctrl_15 (.I5(controlled_buffer_15_out), .O0(JZ));  // open: I4, l3, I2, I1, I0
  Pull_Resistor pull_resistor_93 (.node(HALT));

  // Notes on the sheet:
  //   T0
  //   T1
  //   T2
  //   T3
  //   contents of rom_1 (hex, n*v repeats v):
  //   1c01 2001 2800 3000 1000 800 2402 400 400
  //   contents of rom_2 (hex, n*v repeats v):
  //   229 16 80 100
  //   PROGRAM CODE
  //   MICROCODE
  //   counter++
endmodule
